// Logisim project 74hc374.circ as structural Verilog: 1 circuit, main circuit main
module main (
  input  [7:0] D,
  input  clk,
  input  noe,
  output [7:0] Q
);

  wire [7:0] register_1_q;

  assign Q = noe ? register_1_q : 8'bz;  // Controlled_Buffer controlled_buffer_1
  Register register_1 (.D(D), .Q(register_1_q), .clk(clk));  // open: en, clr
endmodule
