// Logisim project alu.circ as structural Verilog: 1 circuit, main circuit main
module main (
  input  in_1,
  input  in_2,
  input  in_3,
  input  in_4,
  input  in_5,
  input  in_6,
  input  in_7,
  input  in_8,
  input  in_9,
  input  in_10,
  input  in_11,
  input  A_bus,
  input  in_13,
  input  in_14,
  input  in_15,
  input  in_16,
  input  in_17,
  input  in_18,
  input  in_19
);

  wire and_1_out, and_2_out, decoder_1_out0, decoder_1_out1, decoder_1_out2, decoder_1_out3, not_1_out,
       not_2_out, not_3_out;
  wire [7:0] adder_1_out, adder_2_out, and_3_out, controlled_buffer_3_out, controlled_inverter_1_out,
       controlled_inverter_3_out, or_1_out, xor_1_out;

  not not_1 (not_1_out, and_1_out);
  Hex_Digit_Display hex_digit_display_1 (.value({in_4, in_3, in_2, in_1}));  // open: dp
  Hex_Digit_Display hex_digit_display_2 (.value({in_8, in_7, in_6, in_5}));  // open: dp
  assign controlled_inverter_1_out = not_1_out ? ~{in_8, in_7, in_6, in_5, in_4, in_3, in_2, in_1} : 8'bz;  // Controlled_Inverter controlled_inverter_1
  assign controlled_inverter_1_out = and_1_out ? ~8'h1 : 8'bz;  // Controlled_Inverter controlled_inverter_2
  assign controlled_buffer_3_out[5] = decoder_1_out3 ? in_18 : 1'bz;  // Controlled_Buffer controlled_buffer_1
  assign controlled_buffer_3_out[7] = decoder_1_out3 ? A_bus : 1'bz;  // Controlled_Buffer controlled_buffer_2
  assign controlled_buffer_3_out[4] = decoder_1_out3 ? in_17 : 1'bz;  // Controlled_Buffer controlled_buffer_3
  assign controlled_buffer_3_out[6] = decoder_1_out3 ? in_19 : 1'bz;  // Controlled_Buffer controlled_buffer_4
  Adder adder_1 (.a(controlled_inverter_1_out), .b({8{1'b0}}), .out(adder_1_out), .cin(1'b1));  // open: cout
  assign controlled_buffer_3_out[3] = decoder_1_out3 ? in_16 : 1'bz;  // Controlled_Buffer controlled_buffer_5
  assign controlled_buffer_3_out[0] = decoder_1_out3 ? in_13 : 1'bz;  // Controlled_Buffer controlled_buffer_6
  assign controlled_buffer_3_out[2] = decoder_1_out3 ? in_15 : 1'bz;  // Controlled_Buffer controlled_buffer_7
  assign controlled_buffer_3_out[1] = decoder_1_out3 ? in_14 : 1'bz;  // Controlled_Buffer controlled_buffer_8
  assign controlled_inverter_3_out = not_2_out ? ~controlled_inverter_1_out : 8'bz;  // Controlled_Inverter controlled_inverter_3
  assign controlled_inverter_3_out = and_2_out ? adder_1_out : 8'bz;  // Controlled_Buffer controlled_buffer_9
  Hex_Digit_Display hex_digit_display_3 (.value(controlled_inverter_3_out[7:4]));  // open: dp
  not not_2 (not_2_out, and_2_out);
  Hex_Digit_Display hex_digit_display_4 (.value(controlled_inverter_3_out[3:0]));  // open: dp
  and and_1 (and_1_out, in_9, in_11);
  and and_2 (and_2_out, in_10, in_11);
  Adder adder_2 (
    .a(controlled_inverter_3_out), .b({in_19, in_18, in_17, in_16, in_15, in_14, in_13, A_bus}),
    .out(adder_2_out));  // open: cin, cout
  assign and_3_out = controlled_inverter_3_out & {in_19, in_18, in_17, in_16, in_15, in_14, in_13, A_bus};  // AND_Gate and_3, 8 bits wide
  assign or_1_out = controlled_inverter_3_out | {in_19, in_18, in_17, in_16, in_15, in_14, in_13, A_bus};  // OR_Gate or_1, 8 bits wide
  assign xor_1_out = controlled_inverter_3_out ^ {in_19, in_18, in_17, in_16, in_15, in_14, in_13, A_bus};  // XOR_Gate xor_1, 8 bits wide
  assign controlled_buffer_3_out = in_11 ? adder_2_out : 8'bz;  // Controlled_Buffer controlled_buffer_10
  assign controlled_buffer_3_out = decoder_1_out0 ? and_3_out : 8'bz;  // Controlled_Buffer controlled_buffer_11
  assign controlled_buffer_3_out = decoder_1_out1 ? or_1_out : 8'bz;  // Controlled_Buffer controlled_buffer_12
  assign controlled_buffer_3_out = decoder_1_out2 ? xor_1_out : 8'bz;  // Controlled_Buffer controlled_buffer_13
  Hex_Digit_Display hex_digit_display_5 (.value(controlled_buffer_3_out[7:4]));  // open: dp
  Decoder #(.select(2), .disabled(0)) decoder_1 (
    .out0(decoder_1_out0), .out1(decoder_1_out1), .out2(decoder_1_out2), .out3(decoder_1_out3),
    .sel({in_10, in_9}), .en(not_3_out));
  Hex_Digit_Display hex_digit_display_6 (.value(controlled_buffer_3_out[3:0]));  // open: dp
  not not_3 (not_3_out, in_11);

  // Notes on the sheet:
  //   B bus
  //   one/~B
  //   minus/~plus
  //   control
  //   0 = a and b
  //   1 = a or b
  //   2 = a xor b
  //   3 = rra
endmodule
