// Logisim project alu2.circ as structural Verilog: 1 circuit, main circuit 8-bit ALU
module _8_bit_ALU (
  input  [2:0] mode,
  input  Cin,
  input  [7:0] A,
  input  [7:0] B,
  output [7:0] out,
  output Cout,
  output zero
);

  wire adder_1_cout, \and , and_2_out, and_3_out, maths, nand_1_out, nand_2_out, nor_1_out, nor_2_out,
       nor_3_out, nor_4_out, not_2_out, not_3_out, \or , or_2_out, shr, \xor ;
  wire [7:0] adder_1_out, and_1_out, multiplexer_1_out, or_1_out, xor_1_out;

  Decoder #(.select(3), .enable("false")) decoder_1 (
    .out4(\and ), .out5(\xor ), .out6(\or ), .out7(shr), .sel(mode));  // open: out0, out1, out2, out3
  not not_1 (maths, mode[2]);
  Multiplexer #(.width(8), .enable("false")) multiplexer_1 (
    .in0(B), .in1({8{1'b0}}), .out(multiplexer_1_out), .sel(mode[1]));
  not not_2 (not_2_out, mode[0]);
  not not_3 (not_3_out, mode[1]);
  assign xor_1_out = {8{mode[0]}} ^ multiplexer_1_out;  // XOR_Gate xor_1, 8 bits wide
  assign and_1_out = A & B;  // AND_Gate and_1, 8 bits wide
  assign or_1_out = A | B;  // OR_Gate or_1, 8 bits wide
  and and_2 (and_2_out, not_2_out, mode[1]);
  and and_3 (and_3_out, not_3_out, Cin);
  or or_2 (or_2_out, and_2_out, and_3_out);
  Adder adder_1 (.a(A), .b(xor_1_out), .out(adder_1_out), .cin(or_2_out), .cout(adder_1_cout));
  assign out = maths ? adder_1_out : 8'bz;  // Controlled_Buffer controlled_buffer_1
  assign out = \xor  ? xor_1_out : 8'bz;  // Controlled_Buffer controlled_buffer_2
  assign out = \and  ? and_1_out : 8'bz;  // Controlled_Buffer controlled_buffer_3
  assign out = \or  ? or_1_out : 8'bz;  // Controlled_Buffer controlled_buffer_4
  assign out = shr ? {Cin, A[7:1]} : 8'bz;  // Controlled_Buffer controlled_buffer_5
  nor nor_1 (nor_1_out, out[0], out[1]);
  nor nor_2 (nor_2_out, out[2], out[3]);
  nor nor_3 (nor_3_out, out[4], out[5]);
  nor nor_4 (nor_4_out, out[6], out[7]);
  Multiplexer #(.enable("false")) multiplexer_2 (.in0(adder_1_cout), .in1(A[0]), .out(Cout), .sel(mode[2]));
  nand nand_1 (nand_1_out, nor_1_out, nor_2_out);
  nand nand_2 (nand_2_out, nor_3_out, nor_4_out);
  nor nor_5 (zero, nand_1_out, nand_2_out);

  // Notes on the sheet:
  //   Add
  //   Subtract
  //   Inc
  //   Dec
  //   And
  //   Xor
  //   Or
  //   Shr
  //   Mode
  //   0 0 0
  //   0 0 0
  //   0 0 1
  //   0 1 0
  //   0 1 1
  //   1 0 0
  //   1 0 1
  //   1 1 0
  //   1 1 1
endmodule
