// Logisim project cisc-8-2-ttl.circ as structural Verilog: 17 circuits, main circuit system
// CISC-8
module main (
  input  Clock,
  input  nreset,
  input  [7:0] Data_in,
  input  interrupt,
  output out_5,
  output out_6,
  output [15:0] Address,
  output [7:0] Data_out,
  output nWrite,
  output Read,
  output [2:0] phases,
  output [7:0] out_12
);

  wire AddSelADDR, AddSelHL, AddSelPC, AddSelSP, carry_out, Condition_test_condition, dest_acc, dest_addrh,
       dest_addrl, dest_b, dest_c, dest_d, dest_e, dest_flag, dest_h, dest_l, dest_mem, dest_pch, dest_pcl,
       dest_sph, dest_spl, dest_t, instruction_decoder_1_inst_latch, or_1_out, passthru, PC_inc, phase0,
       Restart, sp_count, sp_up, src_00, src_08, src_acc, src_addrh, src_addrl, src_b, src_c, src_d, src_e,
       src_flag, src_h, src_l, src_mem, src_pch, src_pcl, src_sph, src_spl, src_t, writereg, zero;
  wire [2:0] mode, Phase_counter_phase;
  wire [7:0] A_BUS, B_BUS, Instruction_reg_output, T_prime_reg_output;
  wire [15:0] prog_counter_monitor, Stack_pointer_out_10;

  not not_1 (nWrite, dest_mem);
  not not_2 (Read, src_mem);
  registers registers_1 (
    .BusB(B_BUS), .DestA(dest_acc), .DestB(dest_b), .DestT(dest_t), .DestC(dest_c), .DestE(dest_e),
    .DestD(dest_d), .DestADDRL(dest_addrl), .DestADDRH(dest_addrh), .DestH(dest_h), .DestL(dest_l),
    .SrcA(src_acc), .SrcB(src_b), .SrcT(src_t), .SrcC(src_c), .SrcE(src_e), .SrcD(src_d),
    .AddSelADDR(AddSelADDR), .SrcADDRL(src_addrl), .SrcADDRH(src_addrh), .AddSelHL(AddSelHL), .SrcH(src_h),
    .SrcL(src_l), .BusA(A_BUS), .A(Address));
  hc541 hc541_1 (.Input(B_BUS), .noe(or_1_out), .Output(Data_out));
  or or_1 (or_1_out, Read, Clock);
  // Probe on phases
  hc541 hc541_2 (.Input(Data_in), .noe(src_mem), .Output(A_BUS));
  Phase_Counter Phase_counter (
    .Reset(nreset), .Restart(Restart), .Clock(Clock), .Monitor(phases), .phase(Phase_counter_phase));
  // Probe on out_12
  hc574 Instruction_reg (
    .Input(A_BUS), .Clk(instruction_decoder_1_inst_latch), .noe(1'b0), .monitor(out_12),
    .Output(Instruction_reg_output));
  hc574 T_prime_reg (.Input(A_BUS), .Clk(dest_t), .noe(1'b0), .Output(T_prime_reg_output));  // open: monitor
  cisc_8_alu ALU (
    .mode(mode), .Cin(out_5), .A(T_prime_reg_output), .B(A_BUS), .out(B_BUS), .Cout(carry_out), .zero(zero),
    .Passthru(passthru));
  // Probe on prog_counter_monitor
  Program_Counter prog_counter (
    .Bus_B(B_BUS), .clock(Clock), .nmr(nreset), .enable(PC_inc), .Monitor(prog_counter_monitor),
    .nwr_low(dest_pcl), .nwr_high(dest_pch), .nAddSelPC(AddSelPC), .rd_low(src_pcl), .rd_high(src_pch),
    .PC(Address), .Bus_A(A_BUS));
  Condition_Tester Condition_test (
    .Zero_Flag(out_6), .Carry_Flag(out_5), .IR_in(Instruction_reg_output),
    .Condition(Condition_test_condition));
  Instruction_Decoder instruction_decoder_1 (
    .cond_true(Condition_test_condition), .inst(Instruction_reg_output), .phase(Phase_counter_phase),
    .phase0(phase0), .inst_latch(instruction_decoder_1_inst_latch), .interrupt(interrupt), .nreset(nreset),
    .writereg(writereg), .clock(Clock), .dest_b(dest_b), .src_b(src_b), .dest_c(dest_c), .src_c(src_c),
    .dest_d(dest_d), .src_d(src_d), .dest_e(dest_e), .src_e(src_e), .dest_h(dest_h), .src_h(src_h),
    .dest_l(dest_l), .src_l(src_l), .dest_mem(dest_mem), .src_mem(src_mem), .dest_acc(dest_acc),
    .src_acc(src_acc), .dest_T(dest_t), .src_sph(src_sph), .src_flag(src_flag), .dest_SPL(dest_spl),
    .src_spl(src_spl), .dest_SPH(dest_sph), .src_T(src_t), .dest_ADDRL(dest_addrl), .src_PCH(src_pch),
    .dest_ADDRH(dest_addrh), .src_PCL(src_pcl), .src_ADDRL(src_addrl), .src_ADDRH(src_addrh),
    .dest_flag(dest_flag), .src_00(src_00), .src_08(src_08), .mode(mode), .AddselHL(AddSelHL),
    .AddselADDR(AddSelADDR), .AddselSP(AddSelSP), .AddselPC(AddSelPC), .Restart(Restart), .PC_inc(PC_inc),
    .wr_pch(dest_pch), .wr_pcl(dest_pcl), .sp_count(sp_count), .sp_up(sp_up));
  // Probe on Stack_pointer_out_10
  flags Flags (
    .Carry_In(carry_out), .BusB(B_BUS), .Zero_in(zero), .Passthru(passthru), .DestFlag(dest_flag),
    .SrcFlag(src_flag), .Carry_Out(out_5), .BusA(A_BUS), .Zero_Out(out_6));
  Stack_Pointer Stack_pointer (
    .nup_down(sp_up), .B_BUS(B_BUS), .out_10(Stack_pointer_out_10), .wr_spl(dest_spl), .wr_sph(dest_sph),
    .control(sp_count), .clock(Clock), .rd_spl(src_spl), .rd_sph(src_sph), .SelAddSP(AddSelSP),
    .SP_address(Address), .A_BUS(A_BUS));
  Interrupt_Vector Interrupt_vector (.src_00(src_00), .src_08(src_08), .BusA(A_BUS));

  // Other names for the same wires on the sheet: carry_flag = out_5; reset = nreset; zero_flag = out_6
endmodule

module cisc_8_alu (
  input  [7:0] A,
  input  [7:0] B,
  input  [2:0] mode,
  input  Cin,
  output [7:0] out,
  output Cout,
  output zero,
  output Passthru
);

  wire \and , decoder_1_out2, decoder_1_out5, decoder_1_out6, decoder_1_out7, not_1_out, \or , or_2_out,
       or_3_out, or_4_out, or_5_out, or_6_out, or_7_out, or_8_out, \xor ;
  wire [7:0] adder_1_out, and_1_out, hc541_output, or_1_out, xor_1_out;

  hc138 hc138_1 (.Input(mode), ._4(\and ), ._5(\xor ), ._6(\or ), ._7(Passthru));  // open: Enable, _0, _1, _2, _3
  assign and_1_out = A & B;  // AND_Gate and_1, 8 bits wide
  assign or_1_out = A | B;  // OR_Gate or_1, 8 bits wide
  Decoder #(.select(3), .disabled(0), .enable("false")) decoder_1 (
    .out2(decoder_1_out2), .out5(decoder_1_out5), .out6(decoder_1_out6), .out7(decoder_1_out7),
    .sel({Cin, mode[1:0]}));  // open: out0, out1, out3, out4
  not not_1 (not_1_out, \xor );
  hc541 hc541 (.Input({8{mode[1]}}), .noe(not_1_out), .Output(hc541_output));
  hc541 hc541_2 (.Input(A), .noe(\xor ), .Output(hc541_output));
  or or_2 (or_2_out, decoder_1_out2, decoder_1_out5, decoder_1_out6, decoder_1_out7);
  assign xor_1_out = hc541_output ^ B;  // XOR_Gate xor_1, 8 bits wide
  Adder adder_1 (.a(A), .b(xor_1_out), .out(adder_1_out), .cin(or_2_out), .cout(Cout));
  hc541 hc541_3 (.Input(B), .noe(Passthru), .Output(out));
  hc541 hc541_4 (.Input(or_1_out), .noe(\or ), .Output(out));
  hc541 hc541_5 (.Input(adder_1_out), .noe(mode[2]), .Output(out));
  hc541 hc541_6 (.Input(xor_1_out), .noe(\xor ), .Output(out));
  hc541 hc541_7 (.Input(and_1_out), .noe(\and ), .Output(out));
  or or_3 (or_3_out, out[0], out[1]);
  or or_4 (or_4_out, out[2], out[3]);
  or or_5 (or_5_out, or_3_out, or_4_out);
  or or_6 (or_6_out, out[4], out[5]);
  or or_7 (or_7_out, or_6_out, or_8_out);
  or or_8 (or_8_out, out[6], out[7]);
  nor nor_1 (zero, or_5_out, or_7_out);

  // Other names for the same wires on the sheet: pass_b = Passthru
endmodule

module hc163 (
  input  D0,
  input  D1,
  input  D2,
  input  D3,
  input  CET,
  input  CEP,
  input  PE,
  input  nMR,
  input  Clock,
  output Q0,
  output Q1,
  output Q2,
  output Q3,
  output TC
);

  wire and_1_out, and_2_out, and_3_out, and_4_out, and_5_out, and_6_out, and_7_out, and_8_out, and_9_out,
       d_ff_1_q, d_ff_1_qn, d_ff_2_q, d_ff_2_qn, d_ff_3_q, d_ff_3_qn, d_ff_4_q, d_ff_4_qn, nand_1_out,
       nand_2_out, nor_1_out, nor_2_out, nor_3_out, nor_4_out, nor_5_out, nor_6_out, not_1_out, not_2_out,
       or_1_out, or_2_out, or_3_out, or_4_out, or_5_out, xnor_1_out, xnor_2_out, xnor_3_out;

  nand nand_1 (nand_1_out, CET, CEP);
  nor nor_1 (nor_1_out, PE, not_1_out);
  not not_1 (not_1_out, nMR);
  nor nor_2 (nor_2_out, nor_1_out, not_1_out);
  not not_2 (not_2_out, nand_1_out);
  xnor xnor_1 (xnor_1_out, not_2_out, d_ff_1_qn);
  and and_1 (and_1_out, D0, nor_1_out);
  or or_1 (or_1_out, and_1_out, and_2_out);
  and and_2 (and_2_out, xnor_1_out, nor_2_out);
  D_Flip_Flop d_ff_1 (.clk(Clock), .D(or_1_out), .Q(d_ff_1_q), .Qn(d_ff_1_qn));  // open: preset, en, reset
  not not_3 (Q0, d_ff_1_qn);
  nor nor_3 (nor_3_out, nand_1_out, d_ff_1_qn);
  and and_3 (and_3_out, D1, nor_1_out);
  or or_2 (or_2_out, and_3_out, and_4_out);
  xnor xnor_2 (xnor_2_out, nor_3_out, d_ff_2_qn);
  and and_4 (and_4_out, xnor_2_out, nor_2_out);
  D_Flip_Flop d_ff_2 (.clk(Clock), .D(or_2_out), .Q(d_ff_2_q), .Qn(d_ff_2_qn));  // open: preset, en, reset
  not not_4 (Q1, d_ff_2_qn);
  nor nor_4 (nor_4_out, nand_1_out, d_ff_1_qn, d_ff_2_qn);
  xnor xnor_3 (xnor_3_out, nor_4_out, d_ff_3_qn);
  and and_5 (and_5_out, D2, nor_1_out);
  or or_3 (or_3_out, and_5_out, and_6_out);
  and and_6 (and_6_out, xnor_3_out, nor_2_out);
  D_Flip_Flop d_ff_3 (.clk(Clock), .D(or_3_out), .Q(d_ff_3_q), .Qn(d_ff_3_qn));  // open: preset, en, reset
  not not_5 (Q2, d_ff_3_qn);
  nor nor_5 (nor_5_out, nand_1_out, d_ff_1_qn, d_ff_2_qn, d_ff_3_qn);
  and and_7 (and_7_out, D3, nor_1_out);
  or or_4 (or_4_out, and_7_out, and_9_out);
  and and_8 (and_8_out, nor_5_out, d_ff_4_qn);
  nor nor_6 (nor_6_out, nor_5_out, d_ff_4_qn);
  or or_5 (or_5_out, and_8_out, nor_6_out);
  and and_9 (and_9_out, nor_2_out, or_5_out);
  D_Flip_Flop d_ff_4 (.clk(Clock), .D(or_4_out), .Q(d_ff_4_q), .Qn(d_ff_4_qn));  // open: preset, en, reset
  not not_6 (Q3, d_ff_4_qn);
  nand nand_2 (nand_2_out, d_ff_4_q, d_ff_3_q, d_ff_2_q, d_ff_1_q, CET);
  not not_7 (TC, nand_2_out);
endmodule

module Instruction_Decoder (
  input  cond_true,
  input  [7:0] inst,
  input  [2:0] phase,
  input  interrupt,
  input  clock,
  input  nreset,
  output dest_b,
  output src_b,
  output dest_c,
  output src_c,
  output dest_d,
  output src_d,
  output dest_e,
  output src_e,
  output dest_h,
  output phase0,
  output src_h,
  output dest_l,
  output src_l,
  output dest_mem,
  output src_mem,
  output dest_acc,
  output src_acc,
  output dest_T,
  output src_sph,
  output inst_latch,
  output src_flag,
  output dest_SPL,
  output src_spl,
  output dest_SPH,
  output src_T,
  output dest_ADDRL,
  output src_PCH,
  output dest_ADDRH,
  output src_PCL,
  output src_ADDRL,
  output src_ADDRH,
  output dest_flag,
  output src_00,
  output src_08,
  output [2:0] mode,
  output AddselHL,
  output AddselADDR,
  output AddselSP,
  output AddselPC,
  output writereg,
  output Restart,
  output PC_inc,
  output wr_pch,
  output wr_pcl,
  output sp_count,
  output sp_up
);

  wire and_2_out, and_3_out, and_4_out, and_5_out, and_6_out, and_7_out, and_8_out, and_9_out, and_10_out,
       and_11_out, and_12_out, and_13_out, and_14_out, and_15_out, and_16_out, and_17_out, and_18_out,
       and_19_out, and_20_out, and_21_out, and_22_out, and_23_out, and_24_out, and_25_out, and_26_out,
       and_27_out, and_28_out, and_29_out, and_31_out, and_32_out, and_33_out, and_34_out, and_35_out,
       and_36_out, and_37_out, and_39_out, and_40_out, and_41_out, and_42_out, and_43_out, and_44_out,
       and_47_out, and_57_out, and_58_out, and_59_out, and_60_out, and_61_out, and_62_out, and_63_out,
       and_64_out, and_65_out, and_66_out, and_67_out, and_68_out, and_69_out, and_70_out, and_71_out,
       and_73_out, and_74_out, and_75_out, and_76_out, and_77_out, and_78_out, and_79_out, and_80_out,
       and_81_out, and_82_out, and_83_out, and_84_out, and_85_out, and_86_out, and_87_out, and_88_out,
       and_89_out, and_91_out, and_92_out, and_93_out, and_94_out, call, dad, decoder_1_out0, decoder_1_out1,
       decoder_1_out2, decoder_1_out3, decoder_2_out0, decoder_2_out1, decoder_2_out2, decoder_2_out3,
       hc238_1__1, hc238_1__2, hc238_1__3, hc238_1__5, hc238_1__6, hc238_2__1, hc238_2__6, hc238_2__7,
       hc238_3__0, hc238_3__3, hc238_5__0, hc238_5__1, hc238_5__2, hc238_5__3, hc238_5__4, hc238_5__5,
       hc238_5__6, hc238_5__7, hc238_6__0, hc238_6__1, hc238_6__2, hc238_6__3, hc238_7__0, hc238_7__1,
       hc238_7__2, hc238_7__3, hc238_8__0, hc238_8__1, hc238_8__2, hc238_8__3, hc238_8__4, hc238_8__5,
       hc238_8__6, hc238_8__7, \int , jc, jmp, jnc, lda, lri, lxi, maths, mlimm, mov, mov16, nor_5_out,
       not_1_out, not_2_out, not_3_out, not_11_out, or_1_out, or_2_out, or_3_out, or_4_out, or_5_out,
       or_6_out, or_7_out, or_8_out, or_9_out, or_10_out, or_11_out, or_12_out, or_13_out, or_14_out,
       or_15_out, or_16_out, or_17_out, or_18_out, or_19_out, or_20_out, or_21_out, or_22_out, or_23_out,
       or_24_out, or_25_out, or_27_out, or_28_out, or_29_out, or_30_out, or_31_out, or_32_out, or_33_out,
       or_34_out, or_35_out, or_36_out, or_37_out, or_38_out, or_39_out, or_40_out, or_41_out, or_42_out,
       or_43_out, or_44_out, or_45_out, or_46_out, or_47_out, or_48_out, or_51_out, or_52_out, or_53_out,
       or_54_out, or_55_out, or_56_out, or_57_out, or_58_out, or_59_out, phase1, phase2, phase3, phase4,
       phase5, phase6, pop, push, ret, sta;
  wire [2:0] multiplexer_1_out, multiplexer_2_out;

  hc238 hc238_1 (
    .nen(\int ), .nen_2(\int ), .en(1'b1), .Input(inst[2:0]), ._1(hc238_1__1), ._2(hc238_1__2),
    ._3(hc238_1__3), ._5(hc238_1__5), ._6(hc238_1__6));  // open: _0, _4, _7
  hc238 hc238_2 (
    .nen(\int ), .nen_2(\int ), .en(1'b1), .Input(inst[5:3]), ._1(hc238_2__1), ._6(hc238_2__6),
    ._7(hc238_2__7));  // open: _0, _2, _3, _4, _5
  not not_1 (not_1_out, inst[3]);
  interrupt interrupt_control (
    .interrupt(interrupt), .phase0(phase0), .reset(nreset), .\return (ret), .\int (\int ));  // open: int_run
  and and_1 (inst_latch, phase0, clock);
  hc238 hc238_3 (
    .nen(\int ), .nen_2(\int ), .en(1'b1), .Input({1'b0, inst[7:6]}), ._0(hc238_3__0), ._1(mov), ._2(maths),
    ._3(hc238_3__3));  // open: _4, _5, _6, _7
  hc238 hc238_4 (
    .nen(1'b0), .nen_2(1'b0), .en(1'b1), .Input(phase), ._0(phase0), ._1(phase1), ._2(phase2), ._3(phase3),
    ._4(phase4), ._5(phase5), ._6(phase6));  // open: _7
  not not_2 (not_2_out, cond_true);
  and and_2 (and_2_out, phase1, mov);
  and and_3 (and_3_out, phase2, maths);
  or or_1 (or_1_out, maths, mlimm);
  and and_4 (and_4_out, phase3, sta);
  and and_5 (and_5_out, phase1, dad);
  and and_6 (and_6_out, phase1, mov16);
  and and_7 (and_7_out, phase3, dad);
  and and_8 (and_8_out, phase2, mov16);
  and and_9 (and_9_out, phase1, push);
  and and_10 (and_10_out, phase4, dad);
  and and_11 (and_11_out, phase2, push);
  and and_12 (and_12_out, phase2, dad);
  or or_2 (or_2_out, jmp, jc);
  and and_13 (and_13_out, phase3, call);
  and and_14 (and_14_out, phase0, \int );
  and and_15 (and_15_out, phase4, call);
  and and_16 (and_16_out, phase1, \int );
  and and_17 (and_17_out, phase5, call);
  and and_18 (and_18_out, phase6, call);
  and and_19 (and_19_out, phase2, \int );
  and and_20 (and_20_out, phase3, \int );
  and and_21 (and_21_out, phase2, dad);
  and and_22 (and_22_out, phase4, dad);
  or or_3 (or_3_out, maths, mlimm);
  and and_23 (and_23_out, phase1, mov);
  and and_24 (and_24_out, phase2, maths);
  or or_4 (or_4_out, lda, sta);
  or or_5 (or_5_out, phase0, phase1);
  or or_6 (or_6_out, push, pop, ret);
  or or_7 (or_7_out, pop, call, ret);
  and and_25 (and_25_out, phase4, call);
  or or_8 (or_8_out, phase1, phase2);
  or or_9 (or_9_out, lxi, lda, sta, jnc, call);
  and and_26 (and_26_out, mlimm, phase2);
  or or_10 (or_10_out, lri, jmp, jc, call);
  or or_11 (or_11_out, \int , jmp, jc);
  and and_27 (and_27_out, phase6, call);
  and and_28 (and_28_out, phase3, ret);
  or or_12 (or_12_out, \int , jmp, jc);
  and and_29 (and_29_out, phase5, call);
  and and_30 (mlimm, hc238_3__3, hc238_1__6);
  or or_13 (or_13_out, and_2_out, and_3_out);
  and and_31 (and_31_out, phase1, or_1_out);
  or or_14 (or_14_out, and_5_out, and_6_out);
  or or_15 (or_15_out, and_7_out, and_8_out);
  or or_16 (or_16_out, and_9_out, and_10_out);
  or or_17 (or_17_out, and_11_out, and_12_out);
  and and_32 (and_32_out, phase3, or_2_out);
  or or_18 (or_18_out, and_13_out, and_14_out);
  or or_19 (or_19_out, and_15_out, and_16_out);
  Multiplexer #(.width(3), .disabled(0), .enable("false")) multiplexer_1 (
    .in0(3'b001), .in1(3'b000), .out(multiplexer_1_out), .sel(and_21_out));
  or or_20 (or_20_out, and_21_out, and_22_out);
  and and_33 (and_33_out, phase2, or_3_out);
  nor nor_1 (AddselHL, and_23_out, and_24_out);
  and and_34 (and_34_out, or_5_out, \int );
  and and_35 (and_35_out, phase1, or_6_out);
  and and_36 (and_36_out, or_6_out, phase2);
  and and_37 (and_37_out, phase3, or_7_out);
  not not_3 (not_3_out, \int );
  and and_38 (mov16, hc238_3__3, hc238_2__7, hc238_1__1);
  or or_21 (or_21_out, and_31_out, and_4_out);
  Multiplexer #(.width(3), .disabled(0), .enable("false")) multiplexer_2 (
    .in0(3'b111), .in1(multiplexer_1_out), .out(multiplexer_2_out), .sel(or_20_out));
  nand nand_1 (AddselADDR, phase3, or_4_out);
  and and_39 (and_39_out, phase0, not_3_out);
  and and_40 (and_40_out, or_8_out, or_9_out);
  and and_41 (and_41_out, phase1, or_10_out);
  and and_42 (and_42_out, phase2, or_11_out);
  and and_43 (and_43_out, phase3, or_12_out);
  and and_44 (and_44_out, phase2, ret);
  and and_45 (dad, hc238_3__0, inst[3], hc238_1__1);
  hc238 hc238_5 (
    .nen(1'b0), .nen_2(1'b0), .en(or_13_out), .Input(inst[2:0]), ._0(hc238_5__0), ._1(hc238_5__1),
    ._2(hc238_5__2), ._3(hc238_5__3), ._4(hc238_5__4), ._5(hc238_5__5), ._6(hc238_5__6), ._7(hc238_5__7));
  hc238 hc238_6 (
    .nen(1'b0), .nen_2(1'b0), .en(or_16_out), .Input({1'b0, inst[5:4]}), ._0(hc238_6__0), ._1(hc238_6__1),
    ._2(hc238_6__2), ._3(hc238_6__3));  // open: _4, _5, _6, _7
  or or_22 (or_22_out, or_13_out, or_21_out, or_14_out);
  or or_23 (or_23_out, or_15_out, or_16_out, or_17_out);
  or or_24 (or_24_out, and_32_out, or_18_out, or_19_out);
  or or_25 (or_25_out, and_17_out, and_18_out, and_19_out);
  Multiplexer #(.width(3), .disabled(0), .enable("false")) multiplexer_3 (
    .in0(multiplexer_2_out), .in1(inst[5:3]), .out(mode), .sel(and_33_out));
  nor nor_2 (AddselSP, and_34_out, and_35_out, and_36_out, and_37_out, and_25_out);
  or or_26 (PC_inc, and_39_out, and_40_out, and_26_out, and_41_out);
  nor nor_3 (wr_pch, and_42_out, and_27_out, and_28_out);
  nor nor_4 (wr_pcl, and_43_out, and_29_out, and_44_out);
  and and_46 (lxi, hc238_3__0, not_1_out, hc238_1__1);
  and and_47 (and_47_out, hc238_6__3, and_9_out);
  nand nand_2 (src_sph, hc238_6__3, and_10_out);
  hc238 hc238_7 (
    .nen(1'b0), .nen_2(1'b0), .en(or_17_out), .Input({1'b0, inst[5:4]}), ._0(hc238_7__0), ._1(hc238_7__1),
    ._2(hc238_7__2), ._3(hc238_7__3));  // open: _4, _5, _6, _7
  or or_27 (or_27_out, or_22_out, or_23_out, or_24_out);
  nand nand_3 (AddselPC, AddselHL, AddselADDR, AddselSP);
  and and_48 (lda, hc238_3__0, hc238_2__7, hc238_1__2);
  nand nand_4 (src_flag, hc238_7__3, and_11_out);
  nand nand_5 (src_spl, hc238_7__3, and_12_out);
  nor nor_5 (nor_5_out, or_27_out, or_25_out, and_20_out);
  and and_49 (sta, hc238_3__0, hc238_2__6, hc238_1__2);
  nor nor_6 (src_b, hc238_5__0, hc238_6__0);
  nor nor_7 (src_c, hc238_5__1, hc238_7__0);
  nor nor_8 (src_d, hc238_5__2, hc238_6__1);
  nor nor_9 (src_e, hc238_5__3, hc238_7__1);
  nor nor_10 (src_h, hc238_5__4, hc238_6__2, or_15_out);
  nor nor_11 (src_l, hc238_5__5, hc238_7__2, or_14_out);
  nor nor_12 (src_mem, hc238_5__6, nor_5_out);
  nor nor_13 (src_acc, hc238_5__7, or_21_out, and_47_out);
  not not_4 (src_T, and_32_out);
  not not_5 (src_PCH, or_18_out);
  not not_6 (src_PCL, or_19_out);
  not not_7 (src_ADDRL, and_17_out);
  not not_8 (src_ADDRH, and_18_out);
  not not_9 (src_00, and_19_out);
  not not_10 (src_08, and_20_out);
  and and_50 (lri, hc238_3__0, hc238_1__6);
  and and_51 (push, hc238_3__3, not_1_out, hc238_1__5);
  and and_52 (pop, hc238_3__3, not_1_out, hc238_1__1);
  and and_53 (jmp, hc238_3__3, not_1_out, hc238_1__3);
  and and_54 (jc, hc238_3__3, hc238_1__2, cond_true);
  and and_55 (jnc, hc238_3__3, hc238_1__2, not_2_out);
  and and_56 (call, hc238_3__3, hc238_2__1, hc238_1__5);
  or or_28 (or_28_out, lri, mov);
  or or_29 (or_29_out, maths, mlimm, dad, pop, jmp, jc, jnc);
  and and_57 (and_57_out, phase2, jnc);
  and and_58 (and_58_out, phase3, dad);
  or or_30 (or_30_out, maths, mlimm);
  and and_59 (and_59_out, phase3, lda);
  and and_60 (and_60_out, phase1, mov16);
  and and_61 (and_61_out, phase2, mov16);
  or or_31 (or_31_out, lda, sta, call);
  or or_32 (or_32_out, lda, sta, call);
  and and_62 (and_62_out, phase1, push);
  and and_63 (and_63_out, phase2, push);
  or or_33 (or_33_out, sta, call);
  and and_64 (and_64_out, phase4, call);
  or or_34 (or_34_out, phase0, phase1);
  and and_65 (and_65_out, phase1, lxi);
  and and_66 (and_66_out, phase2, pop);
  and and_67 (and_67_out, phase2, lxi);
  and and_68 (and_68_out, phase3, pop);
  or or_35 (or_35_out, maths, mlimm, dad);
  and and_69 (and_69_out, phase4, dad);
  and and_70 (and_70_out, phase2, dad);
  not not_11 (not_11_out, phase0);
  or or_36 (or_36_out, mov, lri);
  or or_37 (or_37_out, maths, mlimm, mov16, push, jnc, lxi);
  or or_38 (or_38_out, lda, sta, pop, jmp, jc, ret, \int );
  and and_71 (and_71_out, phase6, call);
  or or_39 (or_39_out, phase1, phase2);
  or or_40 (or_40_out, phase3, phase4);
  or or_41 (or_41_out, phase0, phase1);
  or or_42 (or_42_out, pop, ret);
  and and_72 (ret, hc238_3__3, hc238_2__1, hc238_1__1);
  and and_73 (and_73_out, phase1, or_28_out);
  and and_74 (and_74_out, phase1, or_29_out);
  and and_75 (and_75_out, phase2, or_30_out);
  and and_76 (and_76_out, phase1, or_31_out);
  and and_77 (and_77_out, phase2, or_32_out);
  and and_78 (and_78_out, phase3, or_33_out);
  and and_79 (and_79_out, or_34_out, \int );
  or or_43 (or_43_out, and_65_out, and_66_out);
  or or_44 (or_44_out, and_67_out, and_68_out);
  and and_80 (and_80_out, phase2, or_35_out);
  and and_81 (and_81_out, dad, phase4);
  or or_45 (or_45_out, \int , not_11_out);
  and and_82 (and_82_out, phase1, or_36_out);
  and and_83 (and_83_out, phase2, or_37_out);
  and and_84 (and_84_out, phase3, or_38_out);
  and and_85 (and_85_out, phase4, dad);
  and and_86 (and_86_out, push, or_39_out);
  and and_87 (and_87_out, call, or_40_out);
  and and_88 (and_88_out, \int , or_41_out);
  and and_89 (and_89_out, or_39_out, or_42_out);
  or or_46 (or_46_out, and_74_out, and_57_out, and_58_out);
  or or_47 (or_47_out, and_75_out, and_59_out);
  or or_48 (or_48_out, and_62_out, and_63_out, and_78_out, and_64_out, and_79_out);
  and and_90 (writereg, or_45_out, clock);
  Decoder #(.select(2), .disabled(0)) decoder_1 (
    .out0(decoder_1_out0), .out1(decoder_1_out1), .out2(decoder_1_out2), .out3(decoder_1_out3),
    .sel(inst[5:4]), .en(or_44_out));
  nor nor_14 (Restart, and_82_out, and_83_out, and_84_out, and_85_out, and_71_out);
  or or_49 (sp_up, and_86_out, and_87_out, and_88_out);
  hc238 hc238_8 (
    .nen(1'b0), .nen_2(1'b0), .en(and_73_out), .Input(inst[5:3]), ._0(hc238_8__0), ._1(hc238_8__1),
    ._2(hc238_8__2), ._3(hc238_8__3), ._4(hc238_8__4), ._5(hc238_8__5), ._6(hc238_8__6), ._7(hc238_8__7));
  Decoder #(.select(2), .disabled(0)) decoder_2 (
    .out0(decoder_2_out0), .out1(decoder_2_out1), .out2(decoder_2_out2), .out3(decoder_2_out3),
    .sel(inst[5:4]), .en(or_43_out));
  or or_50 (sp_count, sp_up, and_89_out);
  and and_91 (and_91_out, decoder_1_out3, and_68_out);
  and and_92 (and_92_out, decoder_1_out3, and_67_out);
  and and_93 (and_93_out, decoder_2_out3, and_66_out);
  and and_94 (and_94_out, decoder_2_out3, and_65_out);
  or or_51 (or_51_out, hc238_8__0, decoder_1_out0);
  or or_52 (or_52_out, hc238_8__1, decoder_2_out0);
  or or_53 (or_53_out, hc238_8__2, decoder_1_out1);
  or or_54 (or_54_out, hc238_8__3, decoder_2_out1);
  or or_55 (or_55_out, hc238_8__4, and_69_out, decoder_1_out2);
  or or_56 (or_56_out, hc238_8__5, and_70_out, decoder_2_out2);
  or or_57 (or_57_out, hc238_8__6, or_48_out);
  or or_58 (or_58_out, hc238_8__7, and_91_out, or_47_out);
  nor nor_15 (dest_SPL, and_60_out, and_94_out);
  nor nor_16 (dest_SPH, and_61_out, and_92_out);
  or or_59 (or_59_out, and_93_out, and_80_out, and_81_out);
  and and_95 (dest_b, or_51_out, writereg);
  and and_96 (dest_c, or_52_out, writereg);
  and and_97 (dest_d, or_53_out, writereg);
  and and_98 (dest_e, or_54_out, writereg);
  and and_99 (dest_h, or_55_out, writereg);
  and and_100 (dest_l, or_56_out, writereg);
  and and_101 (dest_mem, or_57_out, writereg);
  and and_102 (dest_acc, or_58_out, writereg);
  and and_103 (dest_T, or_46_out, writereg);
  and and_104 (dest_ADDRL, and_76_out, writereg);
  and and_105 (dest_ADDRH, and_77_out, writereg);
  and and_106 (dest_flag, or_59_out, writereg);

  // Other names for the same wires on the sheet: destlo[2:0] = inst[5:3]; mmm[2:0] = inst[5:3]; rp[1:0] = inst[5:4];
  //   rp3[1:0] = inst[5:4]; srclo[2:0] = inst[2:0]
endmodule

module Stack_Pointer (
  input  nup_down,
  input  [7:0] B_BUS,
  input  wr_spl,
  input  wr_sph,
  input  control,
  input  clock,
  input  rd_spl,
  input  rd_sph,
  input  SelAddSP,
  output [15:0] out_10,
  output [15:0] SP_address,
  output [7:0] A_BUS
);

  wire and_1_out, and_2_out, not_1_out, not_2_out, not_3_out;
  wire [7:0] hc541_1_output, hc541_3_output;
  wire [15:0] adder_1_out;

  not not_1 (not_1_out, wr_spl);
  not not_2 (not_2_out, wr_sph);
  hc541 hc541_1 (.Input(B_BUS), .noe(wr_spl), .Output(hc541_1_output));
  hc541 hc541_2 (.Input(adder_1_out[7:0]), .noe(not_1_out), .Output(hc541_1_output));
  hc541 hc541_3 (.Input(B_BUS), .noe(wr_sph), .Output(hc541_3_output));
  hc541 hc541_4 (.Input(adder_1_out[15:8]), .noe(not_2_out), .Output(hc541_3_output));
  and and_1 (and_1_out, clock, wr_sph);
  and and_2 (and_2_out, clock, wr_spl);
  not not_3 (not_3_out, clock);
  hc574 hc574_1 (.Input(hc541_1_output), .Clk(and_1_out), .noe(1'b0), .Output(out_10[7:0]));  // open: monitor
  hc574 hc574_2 (.Input(hc541_3_output), .Clk(and_2_out), .noe(1'b0), .Output(out_10[15:8]));  // open: monitor
  Adder #(.width(16)) adder_1 (.a({{15{nup_down}}, control}), .b(out_10), .out(adder_1_out));  // open: cin, cout
  hc574 hc574_3 (.Input(out_10[7:0]), .Clk(not_3_out), .noe(SelAddSP), .Output(SP_address[7:0]));  // open: monitor
  hc574 hc574_4 (.Input(out_10[15:8]), .Clk(not_3_out), .noe(SelAddSP), .Output(SP_address[15:8]));  // open: monitor
  hc541 hc541_5 (.Input(out_10[7:0]), .noe(rd_spl), .Output(A_BUS));
  hc541 hc541_6 (.Input(out_10[15:8]), .noe(rd_sph), .Output(A_BUS));
endmodule

module Program_Counter (
  input  [7:0] Bus_B,
  input  clock,
  input  nmr,
  input  enable,
  input  nwr_low,
  input  nwr_high,
  input  nAddSelPC,
  input  rd_low,
  input  rd_high,
  output [15:0] Monitor,
  output [15:0] PC,
  output [7:0] Bus_A
);

  wire hc163_1_tc, hc163_2_tc, hc163_3_tc, not_1_out;

  hc163 hc163_1 (
    .D0(Bus_B[0]), .D1(Bus_B[1]), .D2(Bus_B[2]), .D3(Bus_B[3]), .CET(enable), .CEP(enable), .PE(nwr_low),
    .nMR(nmr), .Clock(clock), .Q0(Monitor[0]), .Q1(Monitor[1]), .Q2(Monitor[2]), .Q3(Monitor[3]),
    .TC(hc163_1_tc));
  hc163 hc163_2 (
    .D0(Bus_B[4]), .D1(Bus_B[5]), .D2(Bus_B[6]), .D3(Bus_B[7]), .CET(hc163_1_tc), .CEP(enable), .PE(nwr_low),
    .nMR(nmr), .Clock(clock), .Q0(Monitor[4]), .Q1(Monitor[5]), .Q2(Monitor[6]), .Q3(Monitor[7]),
    .TC(hc163_2_tc));
  hc163 hc163_3 (
    .D0(Bus_B[0]), .D1(Bus_B[1]), .D2(Bus_B[2]), .D3(Bus_B[3]), .CET(hc163_2_tc), .CEP(enable),
    .PE(nwr_high), .nMR(nmr), .Clock(clock), .Q0(Monitor[8]), .Q1(Monitor[9]), .Q2(Monitor[10]),
    .Q3(Monitor[11]), .TC(hc163_3_tc));
  hc163 hc163_4 (
    .D0(Bus_B[4]), .D1(Bus_B[5]), .D2(Bus_B[6]), .D3(Bus_B[7]), .CET(hc163_3_tc), .CEP(enable),
    .PE(nwr_high), .nMR(nmr), .Clock(clock), .Q0(Monitor[12]), .Q1(Monitor[13]), .Q2(Monitor[14]),
    .Q3(Monitor[15]));  // open: TC
  not not_1 (not_1_out, clock);
  hc574 hc574_1 (.Input(Monitor[7:0]), .Clk(not_1_out), .noe(nAddSelPC), .Output(PC[7:0]));  // open: monitor
  hc574 hc574_2 (.Input(Monitor[15:8]), .Clk(not_1_out), .noe(nAddSelPC), .Output(PC[15:8]));  // open: monitor
  hc541 hc541_1 (.Input(Monitor[7:0]), .noe(rd_low), .Output(Bus_A));
  hc541 hc541_2 (.Input(Monitor[15:8]), .noe(rd_high), .Output(Bus_A));
endmodule

module interrupt (
  input  interrupt,
  input  phase0,
  input  reset,
  input  \return ,
  output \int ,
  output int_run
);

  wire nand_1_out, nor_1_out, not_1_out, or_1_out;

  nor nor_1 (nor_1_out, interrupt, int_run, \int );
  not not_1 (not_1_out, \return );
  nand nand_1 (nand_1_out, reset, not_1_out);
  D_Flip_Flop d_ff_1 (.clk(phase0), .D(nor_1_out), .Q(\int ), .reset(nand_1_out));  // open: Qn, preset, en
  or or_1 (or_1_out, \int , int_run);
  D_Flip_Flop d_ff_2 (.clk(phase0), .D(or_1_out), .Q(int_run), .reset(nand_1_out));  // open: Qn, preset, en
endmodule

// 574
module hc574 (
  input  [7:0] Input,
  input  Clk,
  input  noe,
  output [7:0] monitor,
  output [7:0] Output
);

  wire not_1_out;

  Register register_1 (.D(Input), .Q(monitor), .clk(Clk));  // open: en, clr
  assign Output = not_1_out ? monitor : 8'bz;  // Controlled_Buffer controlled_buffer_1
  not not_1 (not_1_out, noe);
endmodule

// 541
module hc541 (
  input  [7:0] Input,
  input  noe,
  output [7:0] Output
);

  wire not_1_out;

  assign Output = not_1_out ? Input : 8'bz;  // Controlled_Buffer controlled_buffer_1
  not not_1 (not_1_out, noe);
endmodule

// Registers
module registers (
  input  DestB,
  input  DestC,
  input  DestD,
  input  DestA,
  input  DestT,
  input  DestE,
  input  DestADDRL,
  input  DestADDRH,
  input  DestH,
  input  DestL,
  input  [7:0] BusB,
  input  SrcB,
  input  SrcC,
  input  SrcD,
  input  SrcADDRL,
  input  SrcH,
  input  SrcA,
  input  SrcT,
  input  SrcE,
  input  AddSelADDR,
  input  SrcADDRH,
  input  AddSelHL,
  input  SrcL,
  output [7:0] BusA,
  output [15:0] A
);

  wire [3:0] ADDRH_reg_monitor, ADDRH_reg_monitor_2, H_reg_monitor, H_reg_monitor_2, L_reg_monitor,
       L_reg_monitor_2;
  wire [7:0] A_reg_monitor, ADDRL_reg_monitor, B_reg_monitor, C_Reg_monitor, D_reg_monitor, E_reg_monitor,
       T_reg_monitor;

  Hex_Digit_Display hex_digit_display_1 (.value(B_reg_monitor[3:0]));  // open: dp
  Hex_Digit_Display hex_digit_display_2 (.value(B_reg_monitor[7:4]));  // open: dp
  hc574 B_reg (.Input(BusB), .Clk(DestB), .noe(SrcB), .monitor(B_reg_monitor), .Output(BusA));
  Hex_Digit_Display hex_digit_display_3 (.value(A_reg_monitor[3:0]));  // open: dp
  Hex_Digit_Display hex_digit_display_4 (.value(A_reg_monitor[7:4]));  // open: dp
  hc574 A_reg (.Input(BusB), .Clk(DestA), .noe(SrcA), .monitor(A_reg_monitor), .Output(BusA));
  Hex_Digit_Display hex_digit_display_5 (.value(C_Reg_monitor[7:4]));  // open: dp
  Hex_Digit_Display hex_digit_display_6 (.value(C_Reg_monitor[3:0]));  // open: dp
  hc574 C_Reg (.Input(BusB), .Clk(DestC), .noe(SrcC), .monitor(C_Reg_monitor), .Output(BusA));
  Hex_Digit_Display hex_digit_display_7 (.value(T_reg_monitor[7:4]));  // open: dp
  Hex_Digit_Display hex_digit_display_8 (.value(T_reg_monitor[3:0]));  // open: dp
  hc574 T_reg (.Input(BusB), .Clk(DestT), .noe(SrcT), .monitor(T_reg_monitor), .Output(BusA));
  Hex_Digit_Display hex_digit_display_9 (.value(D_reg_monitor[7:4]));  // open: dp
  Hex_Digit_Display hex_digit_display_10 (.value(D_reg_monitor[3:0]));  // open: dp
  hc574 D_reg (.Input(BusB), .Clk(DestD), .noe(SrcD), .monitor(D_reg_monitor), .Output(BusA));
  Hex_Digit_Display hex_digit_display_11 (.value(E_reg_monitor[3:0]));  // open: dp
  Hex_Digit_Display hex_digit_display_12 (.value(E_reg_monitor[7:4]));  // open: dp
  hc574 E_reg (.Input(BusB), .Clk(DestE), .noe(SrcE), .monitor(E_reg_monitor), .Output(BusA));
  Hex_Digit_Display hex_digit_display_13 (.value(ADDRL_reg_monitor[3:0]));  // open: dp
  Hex_Digit_Display hex_digit_display_14 (.value(ADDRL_reg_monitor[7:4]));  // open: dp
  hc574 ADDRL_reg (.Input(BusB), .Clk(DestADDRL), .noe(SrcADDRL), .monitor(ADDRL_reg_monitor), .Output(BusA));
  hc574 ADDRL_prime_reg (.Input(BusB), .Clk(DestADDRL), .noe(AddSelADDR), .Output(A[7:0]));  // open: monitor
  Hex_Digit_Display hex_digit_display_15 (.value(ADDRH_reg_monitor_2));  // open: dp
  Hex_Digit_Display hex_digit_display_16 (.value(ADDRH_reg_monitor));  // open: dp
  hc574 ADDRH_reg (
    .Input(BusB), .Clk(DestADDRH), .noe(SrcADDRH), .monitor({ADDRH_reg_monitor_2, ADDRH_reg_monitor}),
    .Output(BusA));
  hc574 AddrH_prime_reg (.Input(BusB), .Clk(DestADDRH), .noe(AddSelADDR), .Output(A[15:8]));  // open: monitor
  Hex_Digit_Display hex_digit_display_17 (.value(H_reg_monitor_2));  // open: dp
  hc574 H_reg (.Input(BusB), .Clk(DestH), .noe(SrcH), .monitor({H_reg_monitor_2, H_reg_monitor}), .Output(BusA));
  hc574 H_prime_reg (.Input(BusB), .Clk(DestH), .noe(AddSelHL), .Output(A[15:8]));  // open: monitor
  Hex_Digit_Display hex_digit_display_18 (.value(H_reg_monitor));  // open: dp
  Hex_Digit_Display hex_digit_display_19 (.value(L_reg_monitor));  // open: dp
  Hex_Digit_Display hex_digit_display_20 (.value(L_reg_monitor_2));  // open: dp
  hc574 L_reg (.Input(BusB), .Clk(DestL), .noe(SrcL), .monitor({L_reg_monitor_2, L_reg_monitor}), .Output(BusA));
  hc574 hc574_1 (.Input(BusB), .Clk(DestL), .noe(AddSelHL), .Output(A[7:0]));  // open: monitor
endmodule

module hc138 (
  input  Enable,
  input  [2:0] Input,
  output _0,
  output _1,
  output _2,
  output _3,
  output _4,
  output _5,
  output _6,
  output _7
);

  wire decoder_1_out0, decoder_1_out1, decoder_1_out2, decoder_1_out3, decoder_1_out4, decoder_1_out5,
       decoder_1_out6, decoder_1_out7;

  Decoder #(.select(3), .disabled(0)) decoder_1 (
    .out0(decoder_1_out0), .out1(decoder_1_out1), .out2(decoder_1_out2), .out3(decoder_1_out3),
    .out4(decoder_1_out4), .out5(decoder_1_out5), .out6(decoder_1_out6), .out7(decoder_1_out7), .sel(Input),
    .en(Enable));
  not not_1 (_0, decoder_1_out0);
  not not_2 (_1, decoder_1_out1);
  not not_3 (_2, decoder_1_out2);
  not not_4 (_3, decoder_1_out3);
  not not_5 (_4, decoder_1_out4);
  not not_6 (_5, decoder_1_out5);
  not not_7 (_6, decoder_1_out6);
  not not_8 (_7, decoder_1_out7);
endmodule

module flags (
  input  Carry_In,
  input  [7:0] BusB,
  input  Zero_in,
  input  Passthru,
  input  DestFlag,
  input  SrcFlag,
  output Carry_Out,
  output [7:0] BusA,
  output Zero_Out
);

  wire multiplexer_1_out, multiplexer_2_out;

  Multiplexer #(.disabled(0), .enable("false")) multiplexer_1 (
    .in0(BusB[0]), .in1(Carry_In), .out(multiplexer_1_out), .sel(Passthru));
  Multiplexer #(.disabled(0), .enable("false")) multiplexer_2 (
    .in0(BusB[6]), .in1(Zero_in), .out(multiplexer_2_out), .sel(Passthru));
  D_Flip_Flop Carry (.clk(DestFlag), .D(multiplexer_1_out), .Q(Carry_Out));  // open: Qn, preset, en, reset
  D_Flip_Flop Zero (.clk(DestFlag), .D(multiplexer_2_out), .Q(Zero_Out));  // open: Qn, preset, en, reset
  hc541 hc541 (.Input({1'b0, Zero_Out, {5{1'b0}}, Carry_Out}), .noe(SrcFlag), .Output(BusA));
endmodule

module Interrupt_Vector (
  input  src_00,
  input  src_08,
  output [7:0] BusA
);

  hc541 hc541_1 (.Input({8{1'b0}}), .noe(src_00), .Output(BusA));
  hc541 hc541_2 (.Input(8'h8), .noe(src_08), .Output(BusA));
endmodule

module Condition_Tester (
  input  Zero_Flag,
  input  Carry_Flag,
  input  [7:0] IR_in,
  output Condition
);

  wire xnor_1_out, xnor_2_out;

  xnor xnor_1 (xnor_1_out, Zero_Flag, IR_in[3]);
  Multiplexer #(.disabled(0), .enable("false")) multiplexer_1 (
    .in0(xnor_1_out), .in1(xnor_2_out), .out(Condition), .sel(IR_in[4]));
  xnor xnor_2 (xnor_2_out, IR_in[3], Carry_Flag);
endmodule

module Phase_Counter (
  input  Reset,
  input  Restart,
  input  Clock,
  output [2:0] Monitor,
  output [2:0] phase
);

  wire and_1_out, not_1_out;

  and and_1 (and_1_out, Reset, Restart);
  not not_1 (not_1_out, Clock);
  hc163 hc163_1 (
    .CET(1'b1), .CEP(1'b1), .PE(1'b1), .nMR(and_1_out), .Clock(not_1_out), .Q0(Monitor[0]), .Q1(Monitor[1]),
    .Q2(Monitor[2]));  // open: D0, D1, D2, D3, Q3, TC

  assign phase = Monitor;
endmodule

module system (
  input  nReset,
  input  nInterrupt,
  input  in_3
);

  wire _0xf000, _0xf200, _0xf400, _0xf600, _0xf800, _0xfa00, _0xfc00, _0xfe00, a12, a13, a14, a15, clock_out,
       keyboard_1_avail, main_1_nwrite, main_1_out_5, main_1_out_6, main_1_read, nand_1_out, not_1_out,
       not_2_out, not_3_out, not_4_out;
  wire [2:0] main_1_address_2, main_1_phases;
  wire [6:0] keyboard_1_data;
  wire [7:0] main_1_out_12, ram_1_data;
  wire [8:0] main_1_address;
  wire [31:0] counter_1_q;

  Clock clock (.out(clock_out));
  Decoder #(.select(3), .disabled(0)) decoder_1 (
    .out0(_0xf000), .out1(_0xf200), .out2(_0xf400), .out3(_0xf600), .out4(_0xf800), .out5(_0xfa00),
    .out6(_0xfc00), .out7(_0xfe00), .sel(main_1_address_2), .en(not_2_out));
  Counter #(.width(32), .max('hffffffff)) counter_1 (
    .Q(counter_1_q), .clk(clock_out), .clr(not_1_out));  // open: load, D, count, carry
  not not_1 (not_1_out, nReset);
  nand nand_1 (nand_1_out, a12, a13, a14, a15);
  not not_2 (not_2_out, nand_1_out);
  // Probe on counter_1_q
  RAM #(.addrWidth(16)) ram_1 (
    .addr({a15, a14, a13, a12, main_1_address_2, main_1_address}), .data(ram_1_data), .sel(nand_1_out),
    .clk(main_1_nwrite), .ld(main_1_read));  // open: clr
  // Probe on main_1_phases
  // Probe on main_1_out_12
  // Probe on ram_1_data
  not not_3 (not_3_out, keyboard_1_avail);
  // Probe on main_1_out_5
  main main_1 (
    .Clock(clock_out), .nreset(nReset), .Address({a15, a14, a13, a12, main_1_address_2, main_1_address}),
    .Data_in(ram_1_data), .Data_out(ram_1_data), .nWrite(main_1_nwrite), .Read(main_1_read),
    .interrupt(not_3_out), .phases(main_1_phases), .out_12(main_1_out_12), .out_5(main_1_out_5),
    .out_6(main_1_out_6));
  // Probe on main_1_out_6
  TTY #(.rows(16), .cols(40)) tty_1 (.data(ram_1_data[6:0]), .clk(clock_out), .we(_0xf000), .clr(in_3));
  not not_4 (not_4_out, clock_out);
  Keyboard keyboard_1 (.clk(not_4_out), .re(_0xf200), .avail(keyboard_1_avail), .data(keyboard_1_data));  // open: clr
  assign ram_1_data = _0xf200 ? {1'b0, keyboard_1_data} : 8'bz;  // Controlled_Buffer controlled_buffer_1
  // Probe on keyboard_1_avail
  // Probe on keyboard_1_data
endmodule

// hc283
module hc238 (
  input  nen,
  input  nen_2,
  input  en,
  input  [2:0] Input,
  output _0,
  output _1,
  output _2,
  output _3,
  output _4,
  output _5,
  output _6,
  output _7
);

  wire and_1_out, and_2_out;

  and and_1 (and_1_out, ~nen, ~nen_2);  // AND_Gate
  Decoder #(.select(3), .disabled(0)) decoder_1 (
    .out0(_0), .out1(_1), .out2(_2), .out3(_3), .out4(_4), .out5(_5), .out6(_6), .out7(_7), .sel(Input),
    .en(and_2_out));
  and and_2 (and_2_out, and_1_out, en);
endmodule
