// Logisim project cisc-8-2.circ as structural Verilog: 14 circuits, main circuit main
module main (
  input  nreset,
  input  interrupt
);

  wire AddselADDR, AddselHL, AddselSP, and_1_out, and_2_out, carry_flag, carry_out, Clock, dest_acc,
       dest_addrh, dest_addrl, dest_b, dest_c, dest_d, dest_e, dest_flag, dest_h, dest_l, dest_mem, dest_pch,
       dest_pch_t, dest_pcl, dest_pcl_t, dest_sph, dest_spl, dest_t, instruction_decode_3_1_inst_latch,
       multiplexer_1_out, multiplexer_3_out, multiplexer_4_out, nor_1_out, not_1_out, not_2_out, not_3_out,
       not_4_out, not_5_out, not_6_out, not_7_out, or_1_out, passthru, PC_inc, phase0, Restart, sp_count,
       sp_up, src_00, src_08, src_acc, src_addrh, src_addrl, src_b, src_c, src_d, src_e, src_flag, src_h,
       src_l, src_mem, src_pch, src_pcl, src_sph, src_spl, src_t, writereg, xnor_1_out, xnor_2_out, zero,
       zero_flag;
  wire [1:0] sel_addr;
  wire [2:0] hc163_1_q0, mode;
  wire [7:0] A_BUS, ACC_q, B_BUS, instruction_reg_q, ram_1_data, REG_B_q, REG_C_q, REG_D_q, REG_E_q, temp_q;
  wire [15:0] address, addrl_q, pc, REG_L_q, sp;

  // Probe on B_BUS
  Clock clock_1 (.out(Clock));
  not not_1 (not_1_out, dest_mem);
  assign A_BUS = src_b ? REG_B_q : 8'bz;  // Controlled_Buffer controlled_buffer_1
  Register REG_B (.D(B_BUS), .Q(REG_B_q), .clk(dest_b));  // open: en, clr
  RAM #(.addrWidth(16)) ram_1 (.addr(address), .data(ram_1_data), .clk(not_1_out), .ld(src_mem));  // open: sel, clr
  and and_1 (and_1_out, nreset, Restart);
  not not_2 (not_2_out, Clock);
  assign A_BUS = src_c ? REG_C_q : 8'bz;  // Controlled_Buffer controlled_buffer_2
  Register REG_C (.D(B_BUS), .Q(REG_C_q), .clk(dest_c));  // open: en, clr
  assign A_BUS = src_mem ? ram_1_data : 8'bz;  // Controlled_Buffer controlled_buffer_3
  assign ram_1_data = nor_1_out ? B_BUS : 8'bz;  // Controlled_Buffer controlled_buffer_4
  nor nor_1 (nor_1_out, src_mem, Clock);
  hc163 hc163_1 (
    .CET(1'b1), .CEP(1'b1), .PE(1'b1), .nMR(and_1_out), .Clock(not_2_out), .Q0(hc163_1_q0[0]),
    .Q1(hc163_1_q0[1]), .Q2(hc163_1_q0[2]));  // open: D0, D1, D2, D3, Q3, TC
  assign A_BUS = src_d ? REG_D_q : 8'bz;  // Controlled_Buffer controlled_buffer_5
  Register REG_D (.D(B_BUS), .Q(REG_D_q), .clk(dest_d));  // open: en, clr
  // Probe on hc163_1_q0
  assign A_BUS = src_e ? REG_E_q : 8'bz;  // Controlled_Buffer controlled_buffer_6
  Register REG_E (.D(B_BUS), .Q(REG_E_q), .clk(dest_e));  // open: en, clr
  assign A_BUS = src_h ? REG_L_q[15:8] : 8'bz;  // Controlled_Buffer controlled_buffer_7
  Register REG_L (.D(B_BUS), .Q(REG_L_q[7:0]), .clk(dest_l));  // open: en, clr
  Register REG_H (.D(B_BUS), .Q(REG_L_q[15:8]), .clk(dest_h));  // open: en, clr
  Register instruction_reg (
    .D(A_BUS), .Q(instruction_reg_q), .clk(instruction_decode_3_1_inst_latch));  // open: en, clr
  assign A_BUS = src_l ? REG_L_q[7:0] : 8'bz;  // Controlled_Buffer controlled_buffer_8
  assign A_BUS = src_acc ? ACC_q : 8'bz;  // Controlled_Buffer controlled_buffer_9
  Register ACC (.D(B_BUS), .Q(ACC_q), .clk(dest_acc));  // open: en, clr
  assign A_BUS = src_addrl ? addrl_q[7:0] : 8'bz;  // Controlled_Buffer controlled_buffer_10
  Register addrl (.D(B_BUS), .Q(addrl_q[7:0]), .clk(dest_addrl));  // open: en, clr
  assign A_BUS = src_addrh ? addrl_q[15:8] : 8'bz;  // Controlled_Buffer controlled_buffer_11
  Register addrh (.D(B_BUS), .Q(addrl_q[15:8]), .clk(dest_addrh));  // open: en, clr
  xnor xnor_1 (xnor_1_out, zero_flag, instruction_reg_q[3]);
  Multiplexer #(.disabled(0), .enable("false")) multiplexer_1 (
    .in0(xnor_1_out), .in1(xnor_2_out), .out(multiplexer_1_out), .sel(instruction_reg_q[4]));
  xnor xnor_2 (xnor_2_out, instruction_reg_q[3], carry_flag);
  assign A_BUS = src_t ? temp_q : 8'bz;  // Controlled_Buffer controlled_buffer_12
  Register temp (.D(B_BUS), .Q(temp_q), .clk(dest_t));  // open: en, clr
  instruction_decode_3 instruction_decode_3_1 (
    .cond_true(multiplexer_1_out), .inst(instruction_reg_q), .phase(hc163_1_q0), .phase0(phase0),
    .inst_latch(instruction_decode_3_1_inst_latch), .interrupt(interrupt), .nreset(nreset),
    .writereg(writereg), .clock(Clock), .dest_b(dest_b), .src_b(src_b), .dest_c(dest_c), .src_c(src_c),
    .dest_d(dest_d), .src_d(src_d), .dest_e(dest_e), .src_e(src_e), .dest_h(dest_h), .src_h(src_h),
    .dest_l(dest_l), .src_l(src_l), .dest_mem(dest_mem), .src_mem(src_mem), .dest_acc(dest_acc),
    .src_acc(src_acc), .dest_T(dest_t), .src_sph(src_sph), .src_flag(src_flag), .dest_SPL(dest_spl),
    .src_spl(src_spl), .dest_SPH(dest_sph), .src_T(src_t), .dest_ADDRL(dest_addrl), .src_PCH(src_pch),
    .dest_ADDRH(dest_addrh), .src_PCL(src_pcl), .src_ADDRL(src_addrl), .src_ADDRH(src_addrh),
    .dest_flag(dest_flag), .src_00(src_00), .src_08(src_08), .dest__PCH(dest_pch), .mode(mode),
    .dest__PCL(dest_pcl), .AddselHL(AddselHL), .AddselADDR(AddselADDR), .AddselSP(AddselSP),
    .Restart(Restart), .PC_inc(PC_inc), .wr_pch(dest_pch_t), .wr_pcl(dest_pcl_t), .sp_count(sp_count),
    .sp_up(sp_up));
  Multiplexer #(.select(2), .width(16), .enable("false")) multiplexer_2 (
    .in0(REG_L_q), .in1(addrl_q), .in2(sp), .in3(pc), .out(address), .sel(sel_addr));
  // Probe on A_BUS
  cisc_8_alu ALU (
    .mode(mode), .Cin(carry_flag), .A(temp_q), .B(A_BUS), .out(B_BUS), .Cout(carry_out), .zero(zero),
    .Passthru(passthru));
  // Probe on address
  // Probe on sel_addr
  assign A_BUS = src_00 ? {8{1'b0}} : 8'bz;  // Controlled_Buffer controlled_buffer_13
  assign A_BUS = src_08 ? 8'h8 : 8'bz;  // Controlled_Buffer controlled_buffer_14
  not not_3 (not_3_out, passthru);
  and and_2 (and_2_out, not_3_out, writereg);
  not not_4 (not_4_out, AddselSP);
  and and_3 (sel_addr[0], not_4_out, not_5_out);
  not not_5 (not_5_out, AddselHL);
  not not_6 (not_6_out, AddselADDR);
  and and_4 (sel_addr[1], not_6_out, not_7_out);
  not not_7 (not_7_out, AddselHL);
  Multiplexer #(.disabled(0), .enable("false")) multiplexer_3 (
    .in0(carry_out), .in1(B_BUS[0]), .out(multiplexer_3_out), .sel(passthru));
  Multiplexer #(.disabled(0), .enable("false")) multiplexer_4 (
    .in0(zero), .in1(B_BUS[6]), .out(multiplexer_4_out), .sel(passthru));
  or or_1 (or_1_out, and_2_out, dest_flag);
  _16_bit_up_count Prog_Counter (
    .Bus_B(B_BUS), .clock(Clock), .nmr(nreset), .enable(PC_inc), .nwr_low(dest_pcl_t), .nwr_high(dest_pch_t),
    .rd_low(src_pcl), .rd_high(src_pch), .PC(pc), .Bus_A(A_BUS));
  D_Flip_Flop Carry (.clk(or_1_out), .D(multiplexer_3_out), .Q(carry_flag));  // open: Qn, preset, en, reset
  D_Flip_Flop u_Zero (.clk(or_1_out), .D(multiplexer_4_out), .Q(zero_flag));  // open: Qn, preset, en, reset
  // Probe on pc
  // Probe on sp
  stack_pointer_2 Stack_Pointer (
    .nreset(1'b1), .nup_down(sp_up), .B_BUS(B_BUS), .wr_spl(dest_spl), .wr_sph(dest_sph), .control(sp_count),
    .clock(Clock), .rd_spl(src_spl), .rd_sph(src_sph), .SP_address(sp), .A_BUS(A_BUS));
  assign A_BUS = src_flag ? {1'b0, zero_flag, {5{1'b0}}, carry_flag} : 8'bz;  // Controlled_Buffer controlled_buffer_15

  // Other names for the same wires on the sheet: reset = nreset
endmodule

module cisc_8_alu (
  input  [7:0] A,
  input  [7:0] B,
  input  [2:0] mode,
  input  Cin,
  output [7:0] out,
  output Cout,
  output zero,
  output Passthru
);

  wire \and , decoder_2_out2, decoder_2_out5, decoder_2_out7, nor_1_out, nor_2_out, not_1_out, \or ,
       or_2_out, \xor ;
  wire [7:0] adder_1_out, and_1_out, multiplexer_1_out, or_1_out, xor_1_out;

  Decoder #(.select(3), .enable("false")) decoder_1 (
    .out4(\and ), .out5(\xor ), .out6(\or ), .out7(Passthru), .sel(mode));  // open: out0, out1, out2, out3
  not not_1 (not_1_out, mode[2]);
  assign and_1_out = A & B;  // AND_Gate and_1, 8 bits wide
  assign or_1_out = A | B;  // OR_Gate or_1, 8 bits wide
  Decoder #(.select(3), .disabled(0), .enable("false")) decoder_2 (
    .out2(decoder_2_out2), .out5(decoder_2_out5), .out7(decoder_2_out7), .sel({Cin, mode[1:0]}));  // open: out0, out1, out3, out4, out6
  Multiplexer #(.width(8), .enable("false")) multiplexer_1 (
    .in0({8{mode[1]}}), .in1(A), .out(multiplexer_1_out), .sel(\xor ));
  assign xor_1_out = multiplexer_1_out ^ B;  // XOR_Gate xor_1, 8 bits wide
  or or_2 (or_2_out, decoder_2_out2, decoder_2_out5, decoder_2_out7);
  assign out = Passthru ? B : 8'bz;  // Controlled_Buffer controlled_buffer_1
  assign out = \or  ? or_1_out : 8'bz;  // Controlled_Buffer controlled_buffer_2
  Adder adder_1 (.a(A), .b(xor_1_out), .out(adder_1_out), .cin(or_2_out), .cout(Cout));
  assign out = not_1_out ? adder_1_out : 8'bz;  // Controlled_Buffer controlled_buffer_3
  assign out = \xor  ? xor_1_out : 8'bz;  // Controlled_Buffer controlled_buffer_4
  assign out = \and  ? and_1_out : 8'bz;  // Controlled_Buffer controlled_buffer_5
  nor nor_1 (nor_1_out, out[0], out[1], out[2], out[3]);
  nor nor_2 (nor_2_out, out[4], out[5], out[6], out[7]);
  and and_2 (zero, nor_1_out, nor_2_out);

  // Other names for the same wires on the sheet: pass_b = Passthru

  // Notes on the sheet:
  //   Add
  //   Adc
  //   Sub
  //   Sbb
  //   And
  //   Xor
  //   Or
  //   passb
  //   Mode
  //   0 0 0
  //   0 0 0
  //   0 0 1
  //   0 1 0
  //   0 1 1
  //   1 0 0
  //   1 0 1
  //   1 1 0
  //   1 1 1
endmodule

module hc163 (
  input  D0,
  input  D1,
  input  D2,
  input  D3,
  input  CET,
  input  CEP,
  input  PE,
  input  nMR,
  input  Clock,
  output Q0,
  output Q1,
  output Q2,
  output Q3,
  output TC
);

  wire and_1_out, and_2_out, and_3_out, and_4_out, and_5_out, and_6_out, and_7_out, and_8_out, and_9_out,
       d_ff_1_q, d_ff_1_qn, d_ff_2_q, d_ff_2_qn, d_ff_3_q, d_ff_3_qn, d_ff_4_q, d_ff_4_qn, nand_1_out,
       nand_2_out, nor_1_out, nor_2_out, nor_3_out, nor_4_out, nor_5_out, nor_6_out, not_1_out, not_2_out,
       or_1_out, or_2_out, or_3_out, or_4_out, or_5_out, xnor_1_out, xnor_2_out, xnor_3_out;

  nand nand_1 (nand_1_out, CET, CEP);
  nor nor_1 (nor_1_out, PE, not_1_out);
  not not_1 (not_1_out, nMR);
  nor nor_2 (nor_2_out, nor_1_out, not_1_out);
  not not_2 (not_2_out, nand_1_out);
  xnor xnor_1 (xnor_1_out, not_2_out, d_ff_1_qn);
  and and_1 (and_1_out, D0, nor_1_out);
  or or_1 (or_1_out, and_1_out, and_2_out);
  and and_2 (and_2_out, xnor_1_out, nor_2_out);
  D_Flip_Flop d_ff_1 (.clk(Clock), .D(or_1_out), .Q(d_ff_1_q), .Qn(d_ff_1_qn));  // open: preset, en, reset
  not not_3 (Q0, d_ff_1_qn);
  nor nor_3 (nor_3_out, nand_1_out, d_ff_1_qn);
  and and_3 (and_3_out, D1, nor_1_out);
  or or_2 (or_2_out, and_3_out, and_4_out);
  xnor xnor_2 (xnor_2_out, nor_3_out, d_ff_2_qn);
  and and_4 (and_4_out, xnor_2_out, nor_2_out);
  D_Flip_Flop d_ff_2 (.clk(Clock), .D(or_2_out), .Q(d_ff_2_q), .Qn(d_ff_2_qn));  // open: preset, en, reset
  not not_4 (Q1, d_ff_2_qn);
  nor nor_4 (nor_4_out, nand_1_out, d_ff_1_qn, d_ff_2_qn);
  xnor xnor_3 (xnor_3_out, nor_4_out, d_ff_3_qn);
  and and_5 (and_5_out, D2, nor_1_out);
  or or_3 (or_3_out, and_5_out, and_6_out);
  and and_6 (and_6_out, xnor_3_out, nor_2_out);
  D_Flip_Flop d_ff_3 (.clk(Clock), .D(or_3_out), .Q(d_ff_3_q), .Qn(d_ff_3_qn));  // open: preset, en, reset
  not not_5 (Q2, d_ff_3_qn);
  nor nor_5 (nor_5_out, nand_1_out, d_ff_1_qn, d_ff_2_qn, d_ff_3_qn);
  and and_7 (and_7_out, D3, nor_1_out);
  or or_4 (or_4_out, and_7_out, and_9_out);
  and and_8 (and_8_out, nor_5_out, d_ff_4_qn);
  nor nor_6 (nor_6_out, nor_5_out, d_ff_4_qn);
  or or_5 (or_5_out, and_8_out, nor_6_out);
  and and_9 (and_9_out, nor_2_out, or_5_out);
  D_Flip_Flop d_ff_4 (.clk(Clock), .D(or_4_out), .Q(d_ff_4_q), .Qn(d_ff_4_qn));  // open: preset, en, reset
  not not_6 (Q3, d_ff_4_qn);
  nand nand_2 (nand_2_out, d_ff_4_q, d_ff_3_q, d_ff_2_q, d_ff_1_q, CET);
  not not_7 (TC, nand_2_out);
endmodule

module instruction_decode_3 (
  input  cond_true,
  input  [7:0] inst,
  input  [2:0] phase,
  input  interrupt,
  input  nreset,
  input  clock,
  output dest_b,
  output src_b,
  output dest_c,
  output src_c,
  output dest_d,
  output src_d,
  output dest_e,
  output src_e,
  output dest_h,
  output phase0,
  output src_h,
  output dest_l,
  output src_l,
  output dest_mem,
  output src_mem,
  output dest_acc,
  output src_acc,
  output dest_T,
  output src_sph,
  output inst_latch,
  output src_flag,
  output dest_SPL,
  output src_spl,
  output dest_SPH,
  output src_T,
  output dest_ADDRL,
  output src_PCH,
  output dest_ADDRH,
  output src_PCL,
  output src_ADDRL,
  output src_ADDRH,
  output dest_flag,
  output src_00,
  output src_08,
  output dest__PCH,
  output [2:0] mode,
  output dest__PCL,
  output AddselHL,
  output AddselADDR,
  output AddselSP,
  output writereg,
  output Restart,
  output PC_inc,
  output wr_pch,
  output wr_pcl,
  output sp_count,
  output sp_up
);

  wire and_2_out, and_3_out, and_4_out, and_5_out, and_6_out, and_7_out, and_8_out, and_9_out, and_10_out,
       and_11_out, and_12_out, and_13_out, and_14_out, and_15_out, and_16_out, and_23_out, and_24_out,
       and_25_out, and_26_out, and_27_out, and_28_out, and_29_out, and_30_out, and_31_out, and_33_out,
       and_35_out, and_37_out, and_38_out, and_39_out, and_40_out, and_42_out, and_43_out, and_44_out,
       and_45_out, and_46_out, and_47_out, and_50_out, and_63_out, and_64_out, and_65_out, and_66_out,
       and_67_out, and_68_out, and_69_out, and_70_out, and_71_out, and_72_out, and_73_out, and_74_out,
       and_75_out, and_76_out, and_77_out, and_78_out, and_79_out, and_80_out, and_82_out, and_83_out,
       and_84_out, and_85_out, and_86_out, and_87_out, and_88_out, and_89_out, and_90_out, and_92_out,
       and_93_out, and_94_out, and_95_out, and_96_out, and_97_out, and_98_out, and_99_out, and_100_out,
       and_101_out, and_102_out, and_103_out, call, dad, decoder_1_out1, decoder_1_out2, decoder_1_out3,
       decoder_1_out5, decoder_1_out6, decoder_2_out1, decoder_2_out6, decoder_2_out7, decoder_3_out0,
       decoder_3_out3, decoder_5_out0, decoder_5_out1, decoder_5_out2, decoder_5_out3, decoder_5_out4,
       decoder_5_out5, decoder_5_out6, decoder_5_out7, decoder_6_out0, decoder_6_out1, decoder_6_out2,
       decoder_6_out3, decoder_7_out0, decoder_7_out1, decoder_7_out2, decoder_7_out3, decoder_8_out0,
       decoder_8_out1, decoder_8_out2, decoder_8_out3, decoder_9_out0, decoder_9_out1, decoder_9_out2,
       decoder_9_out3, decoder_9_out4, decoder_9_out5, decoder_9_out6, decoder_9_out7, decoder_10_out0,
       decoder_10_out1, decoder_10_out2, decoder_10_out3, \int , jc, jmp, jnc, lda, lri, lxi, maths, mlimm,
       mov, mov16, nor_1_out, not_1_out, not_2_out, not_3_out, not_4_out, not_5_out, or_1_out, or_2_out,
       or_3_out, or_4_out, or_5_out, or_6_out, or_7_out, or_8_out, or_9_out, or_10_out, or_11_out, or_12_out,
       or_13_out, or_14_out, or_15_out, or_16_out, or_17_out, or_20_out, or_22_out, or_33_out, or_34_out,
       or_35_out, or_36_out, or_37_out, or_38_out, or_39_out, or_40_out, or_41_out, or_42_out, or_43_out,
       or_44_out, or_45_out, or_46_out, or_47_out, or_49_out, or_50_out, or_51_out, or_52_out, or_53_out,
       or_54_out, or_57_out, or_58_out, or_59_out, or_60_out, or_61_out, or_62_out, or_63_out, or_64_out,
       phase1, phase2, phase3, phase4, phase5, phase6, pop, push, ret, sta;
  wire [2:0] multiplexer_1_out, multiplexer_2_out;

  Decoder #(.select(3), .disabled(0)) decoder_1 (
    .out1(decoder_1_out1), .out2(decoder_1_out2), .out3(decoder_1_out3), .out5(decoder_1_out5),
    .out6(decoder_1_out6), .sel(inst[2:0]), .en(not_2_out));  // open: out0, out4, out7
  Decoder #(.select(3), .disabled(0)) decoder_2 (
    .out1(decoder_2_out1), .out6(decoder_2_out6), .out7(decoder_2_out7), .sel(inst[5:3]), .en(not_2_out));  // open: out0, out2, out3, out4, out5
  not not_1 (not_1_out, inst[3]);
  not not_2 (not_2_out, \int );
  interrupt interrupt_control (
    .interrupt(interrupt), .phase0(phase0), .reset(nreset), .\return (ret), .\int (\int ));  // open: int_run
  and and_1 (inst_latch, phase0, clock);
  D_Flip_Flop d_ff_1 (.preset(inst[3]), .en(inst[3]), .reset(inst[3]));  // open: clk, D, Q, Qn
  Decoder #(.select(2), .disabled(0)) decoder_3 (
    .out0(decoder_3_out0), .out1(mov), .out2(maths), .out3(decoder_3_out3), .sel(inst[7:6]), .en(not_2_out));
  not not_3 (not_3_out, cond_true);
  Decoder #(.select(3), .disabled(0), .enable("false")) decoder_4 (
    .out0(phase0), .out1(phase1), .out2(phase2), .out3(phase3), .out4(phase4), .out5(phase5), .out6(phase6),
    .sel(phase));  // open: out7
  and and_2 (and_2_out, phase1, mov);
  and and_3 (and_3_out, phase2, maths);
  or or_1 (or_1_out, maths, mlimm);
  and and_4 (and_4_out, phase3, sta);
  and and_5 (and_5_out, phase1, dad);
  and and_6 (and_6_out, phase1, mov16);
  and and_7 (and_7_out, phase3, dad);
  and and_8 (and_8_out, phase2, mov16);
  and and_9 (and_9_out, phase1, push);
  and and_10 (and_10_out, phase4, dad);
  and and_11 (and_11_out, phase2, push);
  and and_12 (and_12_out, phase2, dad);
  or or_2 (or_2_out, jmp, jc);
  and and_13 (and_13_out, phase3, call);
  and and_14 (and_14_out, phase0, \int );
  and and_15 (and_15_out, phase4, call);
  and and_16 (and_16_out, phase1, \int );
  // AND_Gate and_17 has open pins: in0=phase1, in1=lxi, out=open
  and and_18 (src_ADDRL, phase5, call);
  and and_19 (src_ADDRH, phase6, call);
  // AND_Gate and_20 has open pins: in0=phase2, in1=lxi, out=open
  and and_21 (src_00, phase2, \int );
  and and_22 (src_08, phase3, \int );
  and and_23 (and_23_out, phase2, dad);
  and and_24 (and_24_out, phase4, dad);
  or or_3 (or_3_out, maths, mlimm);
  and and_25 (and_25_out, phase1, mov);
  and and_26 (and_26_out, phase2, maths);
  or or_4 (or_4_out, lda, sta);
  or or_5 (or_5_out, phase0, phase1);
  or or_6 (or_6_out, push, pop, ret);
  or or_7 (or_7_out, pop, call, ret);
  and and_27 (and_27_out, phase4, call);
  or or_8 (or_8_out, phase1, phase2);
  or or_9 (or_9_out, lxi, lda, sta, jnc);
  and and_28 (and_28_out, mlimm, phase2);
  or or_10 (or_10_out, lri, jmp, jc, call);
  or or_11 (or_11_out, \int , jmp, jc);
  and and_29 (and_29_out, phase6, call);
  and and_30 (and_30_out, phase3, ret);
  or or_12 (or_12_out, \int , jmp, jc);
  and and_31 (and_31_out, phase5, call);
  and and_32 (mlimm, decoder_3_out3, decoder_1_out6);
  or or_13 (or_13_out, and_2_out, and_3_out);
  and and_33 (and_33_out, phase1, or_1_out);
  or or_14 (or_14_out, and_5_out, and_6_out);
  or or_15 (or_15_out, and_7_out, and_8_out);
  or or_16 (or_16_out, and_9_out, and_10_out);
  or or_17 (or_17_out, and_11_out, and_12_out);
  and and_34 (src_T, phase3, or_2_out);
  or or_18 (src_PCH, and_13_out, and_14_out);
  or or_19 (src_PCL, and_15_out, and_16_out);
  Multiplexer #(.width(3), .disabled(0), .enable("false")) multiplexer_1 (
    .in0(3'b001), .in1(3'b000), .out(multiplexer_1_out), .sel(and_23_out));
  or or_20 (or_20_out, and_23_out, and_24_out);
  and and_35 (and_35_out, phase2, or_3_out);
  or or_21 (AddselHL, and_25_out, and_26_out);
  and and_36 (AddselADDR, phase3, or_4_out);
  and and_37 (and_37_out, or_5_out, \int );
  and and_38 (and_38_out, phase1, or_6_out);
  and and_39 (and_39_out, or_6_out, phase2);
  and and_40 (and_40_out, phase3, or_7_out);
  not not_4 (not_4_out, \int );
  and and_41 (mov16, decoder_3_out3, decoder_2_out7, decoder_1_out1);
  or or_22 (or_22_out, and_33_out, and_4_out);
  nor nor_1 (nor_1_out, src_00, src_ADDRH, src_ADDRL, src_PCL, src_PCH, src_T, or_17_out, or_16_out, or_15_out, or_14_out, or_22_out, or_13_out, src_08);
  Multiplexer #(.width(3), .disabled(0), .enable("false")) multiplexer_2 (
    .in0(3'b111), .in1(multiplexer_1_out), .out(multiplexer_2_out), .sel(or_20_out));
  and and_42 (and_42_out, phase0, not_4_out);
  and and_43 (and_43_out, or_8_out, or_9_out);
  and and_44 (and_44_out, phase1, or_10_out);
  and and_45 (and_45_out, phase2, or_11_out);
  and and_46 (and_46_out, phase3, or_12_out);
  and and_47 (and_47_out, phase2, ret);
  and and_48 (dad, decoder_3_out0, inst[3], decoder_1_out1);
  Decoder #(.select(3), .disabled(0)) decoder_5 (
    .out0(decoder_5_out0), .out1(decoder_5_out1), .out2(decoder_5_out2), .out3(decoder_5_out3),
    .out4(decoder_5_out4), .out5(decoder_5_out5), .out6(decoder_5_out6), .out7(decoder_5_out7),
    .sel(inst[2:0]), .en(or_13_out));
  Decoder #(.select(2), .disabled(0)) decoder_6 (
    .out0(decoder_6_out0), .out1(decoder_6_out1), .out2(decoder_6_out2), .out3(decoder_6_out3),
    .sel(inst[5:4]), .en(or_16_out));
  Multiplexer #(.width(3), .disabled(0), .enable("false")) multiplexer_3 (
    .in0(multiplexer_2_out), .in1(inst[5:3]), .out(mode), .sel(and_35_out));
  or or_23 (AddselSP, and_37_out, and_38_out, and_39_out, and_40_out, and_27_out);
  or or_24 (PC_inc, and_42_out, and_43_out, and_28_out, and_44_out);
  nor nor_2 (wr_pch, and_45_out, and_29_out, and_30_out);
  nor nor_3 (wr_pcl, and_46_out, and_31_out, and_47_out);
  and and_49 (lxi, decoder_3_out0, not_1_out, decoder_1_out1);
  and and_50 (and_50_out, decoder_6_out3, and_9_out);
  and and_51 (src_sph, decoder_6_out3, and_10_out);
  Decoder #(.select(2), .disabled(0)) decoder_7 (
    .out0(decoder_7_out0), .out1(decoder_7_out1), .out2(decoder_7_out2), .out3(decoder_7_out3),
    .sel(inst[5:4]), .en(or_17_out));
  and and_52 (lda, decoder_3_out0, decoder_2_out7, decoder_1_out2);
  and and_53 (src_flag, decoder_7_out3, and_11_out);
  and and_54 (src_spl, decoder_7_out3, and_12_out);
  and and_55 (sta, decoder_3_out0, decoder_2_out6, decoder_1_out2);
  or or_25 (src_b, decoder_5_out0, decoder_6_out0);
  or or_26 (src_c, decoder_5_out1, decoder_7_out0);
  or or_27 (src_d, decoder_5_out2, decoder_6_out1);
  or or_28 (src_e, decoder_5_out3, decoder_7_out1);
  or or_29 (src_h, decoder_5_out4, decoder_6_out2, or_15_out);
  or or_30 (src_l, decoder_5_out5, decoder_7_out2, or_14_out);
  or or_31 (src_mem, decoder_5_out6, nor_1_out);
  or or_32 (src_acc, decoder_5_out7, and_50_out, or_22_out);
  and and_56 (lri, decoder_3_out0, decoder_1_out6);
  and and_57 (push, decoder_3_out3, not_1_out, decoder_1_out5);
  and and_58 (pop, decoder_3_out3, not_1_out, decoder_1_out1);
  and and_59 (jmp, decoder_3_out3, not_1_out, decoder_1_out3);
  and and_60 (jc, decoder_3_out3, decoder_1_out2, cond_true);
  and and_61 (jnc, decoder_3_out3, decoder_1_out2, not_3_out);
  and and_62 (call, decoder_3_out3, decoder_2_out1, decoder_1_out5);
  or or_33 (or_33_out, lri, mov);
  or or_34 (or_34_out, maths, mlimm, dad, pop, jmp, jc, jnc);
  and and_63 (and_63_out, phase2, jnc);
  and and_64 (and_64_out, phase3, dad);
  or or_35 (or_35_out, maths, mlimm);
  and and_65 (and_65_out, phase3, lda);
  and and_66 (and_66_out, phase1, mov16);
  and and_67 (and_67_out, phase2, mov16);
  or or_36 (or_36_out, lda, sta, call);
  or or_37 (or_37_out, lda, sta, call);
  and and_68 (and_68_out, phase1, push);
  and and_69 (and_69_out, phase2, push);
  or or_38 (or_38_out, sta, call);
  and and_70 (and_70_out, phase4, call);
  or or_39 (or_39_out, phase0, phase1);
  and and_71 (and_71_out, phase1, lxi);
  and and_72 (and_72_out, phase2, pop);
  and and_73 (and_73_out, phase2, lxi);
  and and_74 (and_74_out, phase3, pop);
  and and_75 (and_75_out, phase1, ret);
  or or_40 (or_40_out, jmp, jc, ret, \int );
  and and_76 (and_76_out, phase6, call);
  or or_41 (or_41_out, jmp, jc, ret, \int );
  and and_77 (and_77_out, phase5, call);
  and and_78 (and_78_out, phase4, dad);
  and and_79 (and_79_out, phase2, dad);
  not not_5 (not_5_out, phase0);
  or or_42 (or_42_out, mov, lri);
  or or_43 (or_43_out, maths, mlimm, mov16, push, jnc, lxi);
  or or_44 (or_44_out, lda, sta, pop, jmp, jc, ret, \int );
  and and_80 (and_80_out, phase6, call);
  or or_45 (or_45_out, phase1, phase2);
  or or_46 (or_46_out, phase3, phase4);
  or or_47 (or_47_out, phase0, phase1);
  // OR_Gate or_48 has open pins: in0=phase1, in1=phase2, out=open
  or or_49 (or_49_out, pop, ret);
  and and_81 (ret, decoder_3_out3, decoder_2_out1, decoder_1_out1);
  and and_82 (and_82_out, phase1, or_33_out);
  and and_83 (and_83_out, phase1, or_34_out);
  and and_84 (and_84_out, phase2, or_35_out);
  and and_85 (and_85_out, phase1, or_36_out);
  and and_86 (and_86_out, phase2, or_37_out);
  and and_87 (and_87_out, phase3, or_38_out);
  and and_88 (and_88_out, or_39_out, \int );
  or or_50 (or_50_out, and_71_out, and_72_out);
  or or_51 (or_51_out, and_73_out, and_74_out);
  and and_89 (and_89_out, phase2, or_40_out);
  and and_90 (and_90_out, phase3, or_41_out);
  and and_91 (writereg, not_5_out, clock);
  and and_92 (and_92_out, phase1, or_42_out);
  and and_93 (and_93_out, phase2, or_43_out);
  and and_94 (and_94_out, phase3, or_44_out);
  and and_95 (and_95_out, phase4, dad);
  and and_96 (and_96_out, push, or_45_out);
  and and_97 (and_97_out, call, or_46_out);
  and and_98 (and_98_out, \int , or_47_out);
  and and_99 (and_99_out, or_45_out, or_49_out);
  or or_52 (or_52_out, and_83_out, and_63_out, and_64_out);
  or or_53 (or_53_out, and_84_out, and_65_out);
  or or_54 (or_54_out, and_68_out, and_69_out, and_87_out, and_70_out, and_88_out);
  nor nor_4 (dest__PCH, and_75_out, and_89_out, and_76_out);
  nor nor_5 (dest__PCL, and_90_out, and_77_out);
  Decoder #(.select(2), .disabled(0)) decoder_8 (
    .out0(decoder_8_out0), .out1(decoder_8_out1), .out2(decoder_8_out2), .out3(decoder_8_out3),
    .sel(inst[5:4]), .en(or_51_out));
  nor nor_6 (Restart, and_92_out, and_93_out, and_94_out, and_95_out, and_80_out);
  or or_55 (sp_up, and_96_out, and_97_out, and_98_out);
  Decoder #(.select(3), .disabled(0)) decoder_9 (
    .out0(decoder_9_out0), .out1(decoder_9_out1), .out2(decoder_9_out2), .out3(decoder_9_out3),
    .out4(decoder_9_out4), .out5(decoder_9_out5), .out6(decoder_9_out6), .out7(decoder_9_out7),
    .sel(inst[5:3]), .en(and_82_out));
  Decoder #(.select(2), .disabled(0)) decoder_10 (
    .out0(decoder_10_out0), .out1(decoder_10_out1), .out2(decoder_10_out2), .out3(decoder_10_out3),
    .sel(inst[5:4]), .en(or_50_out));
  or or_56 (sp_count, sp_up, and_99_out);
  and and_100 (and_100_out, decoder_8_out3, and_74_out);
  and and_101 (and_101_out, decoder_8_out3, and_73_out);
  and and_102 (and_102_out, decoder_10_out3, and_72_out);
  and and_103 (and_103_out, decoder_10_out3, and_71_out);
  or or_57 (or_57_out, decoder_9_out0, decoder_8_out0);
  or or_58 (or_58_out, decoder_9_out1, decoder_10_out0);
  or or_59 (or_59_out, decoder_9_out2, decoder_8_out1);
  or or_60 (or_60_out, decoder_9_out3, decoder_10_out1);
  or or_61 (or_61_out, decoder_9_out4, and_78_out, decoder_8_out2);
  or or_62 (or_62_out, decoder_9_out5, and_79_out, decoder_10_out2);
  or or_63 (or_63_out, decoder_9_out6, or_54_out);
  or or_64 (or_64_out, decoder_9_out7, and_100_out, or_53_out);
  nor nor_7 (dest_SPL, and_66_out, and_103_out);
  nor nor_8 (dest_SPH, and_67_out, and_101_out);
  and and_104 (dest_b, or_57_out, writereg);
  and and_105 (dest_c, or_58_out, writereg);
  and and_106 (dest_d, or_59_out, writereg);
  and and_107 (dest_e, or_60_out, writereg);
  and and_108 (dest_h, or_61_out, writereg);
  and and_109 (dest_l, or_62_out, writereg);
  and and_110 (dest_mem, or_63_out, writereg);
  and and_111 (dest_acc, or_64_out, writereg);
  and and_112 (dest_T, or_52_out, writereg);
  and and_113 (dest_ADDRL, and_85_out, writereg);
  and and_114 (dest_ADDRH, and_86_out, writereg);
  and and_115 (dest_flag, and_102_out, writereg);

  // Other names for the same wires on the sheet: destlo[2:0] = inst[5:3]; mmm[2:0] = inst[5:3]; rp[1:0] = inst[5:4];
  //   srclo[2:0] = inst[2:0]
endmodule

module stack_pointer_2 (
  input  nreset,
  input  nup_down,
  input  [7:0] B_BUS,
  input  wr_spl,
  input  wr_sph,
  input  control,
  input  clock,
  input  rd_spl,
  input  rd_sph,
  output [15:0] SP_address,
  output [7:0] A_BUS
);

  wire and_1_out, and_2_out, not_1_out;
  wire [7:0] multiplexer_1_out, multiplexer_2_out, multiplexer_3_out, multiplexer_4_out, register_1_q,
       register_2_q;
  wire [15:0] adder_1_out;

  Multiplexer #(.width(8), .disabled(0), .enable("false")) multiplexer_1 (
    .in0(B_BUS), .in1(adder_1_out[7:0]), .out(multiplexer_1_out), .sel(wr_spl));
  Multiplexer #(.width(8), .disabled(0), .enable("false")) multiplexer_2 (
    .in0(B_BUS), .in1(adder_1_out[15:8]), .out(multiplexer_2_out), .sel(wr_sph));
  Multiplexer #(.width(8), .disabled(0), .enable("false")) multiplexer_3 (
    .in0({8{1'b0}}), .in1(multiplexer_1_out), .out(multiplexer_3_out), .sel(nreset));
  Multiplexer #(.width(8), .disabled(0), .enable("false")) multiplexer_4 (
    .in0({8{1'b0}}), .in1(multiplexer_2_out), .out(multiplexer_4_out), .sel(nreset));
  and and_1 (and_1_out, clock, wr_sph);
  and and_2 (and_2_out, clock, wr_spl);
  not not_1 (not_1_out, clock);
  Register register_1 (.D(multiplexer_3_out), .Q(register_1_q), .clk(and_1_out));  // open: en, clr
  Register register_2 (.D(multiplexer_4_out), .Q(register_2_q), .clk(and_2_out));  // open: en, clr
  assign A_BUS = rd_spl ? register_1_q : 8'bz;  // Controlled_Buffer controlled_buffer_1
  assign A_BUS = rd_sph ? register_2_q : 8'bz;  // Controlled_Buffer controlled_buffer_2
  Adder #(.width(16)) adder_1 (
    .a({{15{nup_down}}, control}), .b({register_2_q, register_1_q}), .out(adder_1_out));  // open: cin, cout
  Register #(.width(16)) register_3 (
    .D({register_2_q, register_1_q}), .Q(SP_address), .clk(not_1_out));  // open: en, clr
endmodule

module graphics (
  input  in_1,
  input  in_2
);
endmodule

module test (
  output sp_count,
  output sp_up
);

  wire and_1_out, and_2_out, and_3_out, call, \int , or_1_out, or_2_out, or_3_out, or_4_out, or_5_out,
       or_6_out, phase0, phase1, phase2, phase3, phase4, pop, push, ret;

  or or_1 (or_1_out, phase1, phase2);
  or or_2 (or_2_out, phase3, phase4);
  or or_3 (or_3_out, phase0, phase1);
  or or_4 (or_4_out, phase1, phase2);
  or or_5 (or_5_out, pop, ret);
  and and_1 (and_1_out, push, or_1_out);
  and and_2 (and_2_out, call, or_2_out);
  and and_3 (and_3_out, \int , or_3_out);
  and and_4 (sp_up, or_4_out, or_5_out);
  or or_6 (or_6_out, and_1_out, and_2_out, and_3_out);
  or or_7 (sp_count, or_6_out, sp_up);
endmodule

module hc193 (
  input  CLR,
  input  UP,
  input  DOWN,
  input  nLOAD,
  input  A,
  input  B,
  input  C,
  input  D,
  output nCO,
  output nBO,
  output QA,
  output QB,
  output QC,
  output QD
);

  wire and_1_out, and_2_out, and_3_out, and_4_out, and_5_out, and_6_out, and_7_out, and_8_out, and_9_out,
       d_ff_1_qn, d_ff_2_qn, d_ff_3_qn, d_ff_4_qn, nand_1_out, nand_2_out, nand_3_out, nand_4_out,
       nand_5_out, nand_6_out, nand_7_out, nand_8_out, nand_9_out, nand_10_out, nand_11_out, nand_12_out,
       nand_13_out, nand_14_out, not_1_out, not_2_out, not_3_out, not_4_out, not_5_out, not_6_out, not_7_out,
       not_8_out, not_9_out, not_10_out, not_11_out, not_12_out, not_13_out, not_14_out, or_1_out, or_2_out,
       or_3_out, s_r_ff_1_q, s_r_ff_1_qn, xor_1_out, xor_2_out, xor_3_out, xor_4_out, xor_5_out, xor_6_out;

  not not_1 (not_1_out, CLR);
  not not_2 (not_2_out, nLOAD);
  not not_3 (not_3_out, A);
  nand nand_1 (nand_1_out, not_3_out, not_2_out);
  not not_4 (not_4_out, B);
  nand nand_2 (nand_2_out, not_4_out, not_2_out);
  not not_5 (not_5_out, C);
  nand nand_3 (nand_3_out, not_5_out, not_2_out);
  not not_6 (not_6_out, D);
  nand nand_4 (nand_4_out, not_6_out, not_2_out);
  not not_7 (not_7_out, UP);
  and and_1 (and_1_out, A, not_1_out, not_2_out);
  nand nand_5 (nand_5_out, not_1_out, nand_1_out);
  and and_2 (and_2_out, B, not_1_out, not_2_out);
  nand nand_6 (nand_6_out, not_1_out, nand_2_out);
  and and_3 (and_3_out, C, not_1_out, not_2_out);
  nand nand_7 (nand_7_out, not_1_out, nand_3_out);
  and and_4 (and_4_out, D, not_1_out, not_2_out);
  nand nand_8 (nand_8_out, not_1_out, nand_4_out);
  not not_8 (not_8_out, DOWN);
  and and_5 (and_5_out, not_11_out, not_12_out);
  and and_6 (and_6_out, d_ff_1_qn, d_ff_2_qn);
  and and_7 (and_7_out, not_11_out, not_12_out, not_13_out);
  and and_8 (and_8_out, d_ff_1_qn, d_ff_2_qn, d_ff_3_qn);
  not not_9 (not_9_out, DOWN);
  not not_10 (not_10_out, UP);
  S_R_Flip_Flop s_r_ff_1 (
    .Q(s_r_ff_1_q), .Qn(s_r_ff_1_qn), .preset(not_10_out), .reset(not_8_out));  // open: S, clk, R, en
  xor xor_1 (xor_1_out, not_11_out, not_12_out);
  xor xor_2 (xor_2_out, not_12_out, d_ff_1_qn);
  xor xor_3 (xor_3_out, and_5_out, not_13_out);
  xor xor_4 (xor_4_out, not_13_out, and_6_out);
  xor xor_5 (xor_5_out, and_7_out, not_14_out);
  xor xor_6 (xor_6_out, not_14_out, and_8_out);
  and and_9 (and_9_out, DOWN, UP);
  not not_11 (not_11_out, d_ff_1_qn);
  nand nand_9 (nand_9_out, s_r_ff_1_q, xor_1_out);
  nand nand_10 (nand_10_out, xor_2_out, s_r_ff_1_qn);
  not not_12 (not_12_out, d_ff_2_qn);
  nand nand_11 (nand_11_out, s_r_ff_1_q, xor_3_out);
  nand nand_12 (nand_12_out, xor_4_out, s_r_ff_1_qn);
  not not_13 (not_13_out, d_ff_3_qn);
  nand nand_13 (nand_13_out, s_r_ff_1_q, xor_5_out);
  nand nand_14 (nand_14_out, xor_6_out, s_r_ff_1_qn);
  not not_14 (not_14_out, d_ff_4_qn);
  or or_1 (or_1_out, ~nand_9_out, ~nand_10_out);  // OR_Gate
  or or_2 (or_2_out, ~nand_11_out, ~nand_12_out);  // OR_Gate
  or or_3 (or_3_out, ~nand_13_out, ~nand_14_out);  // OR_Gate
  D_Flip_Flop d_ff_1 (
    .clk(and_9_out), .D(d_ff_1_qn), .Q(QA), .Qn(d_ff_1_qn), .preset(and_1_out), .reset(nand_5_out));  // open: en
  D_Flip_Flop d_ff_2 (
    .clk(and_9_out), .D(or_1_out), .Q(QB), .Qn(d_ff_2_qn), .preset(and_2_out), .reset(nand_6_out));  // open: en
  D_Flip_Flop d_ff_3 (
    .clk(and_9_out), .D(or_2_out), .Q(QC), .Qn(d_ff_3_qn), .preset(and_3_out), .reset(nand_7_out));  // open: en
  D_Flip_Flop d_ff_4 (
    .clk(and_9_out), .D(or_3_out), .Q(QD), .Qn(d_ff_4_qn), .preset(and_4_out), .reset(nand_8_out));  // open: en
  nand nand_15 (nCO, not_11_out, not_12_out, not_13_out, not_14_out, not_7_out);
  nand nand_16 (nBO, d_ff_1_qn, d_ff_2_qn, d_ff_3_qn, d_ff_4_qn, not_9_out);
endmodule

module prog_counter_2 (
  input  CLR,
  input  UP,
  input  DOWN,
  input  [7:0] B_BUS,
  input  nWR_LO,
  input  nWR_HI,
  input  RD_LO,
  input  RD_HI,
  output [7:0] A_BUS,
  output [15:0] PROG_COUNTER
);

  wire hc193_1_nbo, hc193_1_nco, hc193_2_nbo, hc193_2_nco, hc193_3_nbo, hc193_3_nco;

  hc193 hc193_1 (
    .CLR(CLR), .UP(UP), .DOWN(DOWN), .nLOAD(nWR_LO), .A(B_BUS[0]), .B(B_BUS[1]), .C(B_BUS[2]), .D(B_BUS[3]),
    .nCO(hc193_1_nco), .nBO(hc193_1_nbo), .QA(PROG_COUNTER[0]), .QB(PROG_COUNTER[1]), .QC(PROG_COUNTER[2]),
    .QD(PROG_COUNTER[3]));
  hc193 hc193_2 (
    .CLR(CLR), .UP(hc193_1_nco), .DOWN(hc193_1_nbo), .nLOAD(nWR_LO), .A(B_BUS[4]), .B(B_BUS[5]),
    .C(B_BUS[6]), .D(B_BUS[7]), .nCO(hc193_2_nco), .nBO(hc193_2_nbo), .QA(PROG_COUNTER[4]),
    .QB(PROG_COUNTER[5]), .QC(PROG_COUNTER[6]), .QD(PROG_COUNTER[7]));
  hc193 hc193_3 (
    .CLR(CLR), .UP(hc193_2_nco), .DOWN(hc193_2_nbo), .nLOAD(nWR_HI), .A(B_BUS[0]), .B(B_BUS[1]),
    .C(B_BUS[2]), .D(B_BUS[3]), .nCO(hc193_3_nco), .nBO(hc193_3_nbo), .QA(PROG_COUNTER[8]),
    .QB(PROG_COUNTER[9]), .QC(PROG_COUNTER[10]), .QD(PROG_COUNTER[11]));
  assign A_BUS = RD_LO ? PROG_COUNTER[7:0] : 8'bz;  // Controlled_Buffer controlled_buffer_1
  assign A_BUS = RD_HI ? PROG_COUNTER[15:8] : 8'bz;  // Controlled_Buffer controlled_buffer_2
  hc193 hc193_4 (
    .CLR(CLR), .UP(hc193_3_nco), .DOWN(hc193_3_nbo), .nLOAD(nWR_HI), .A(B_BUS[4]), .B(B_BUS[5]),
    .C(B_BUS[6]), .D(B_BUS[7]), .QA(PROG_COUNTER[12]), .QB(PROG_COUNTER[13]), .QC(PROG_COUNTER[14]),
    .QD(PROG_COUNTER[15]));  // open: nCO, nBO
endmodule

module _16_bit_up_count (
  input  [7:0] Bus_B,
  input  clock,
  input  nmr,
  input  enable,
  input  nwr_low,
  input  nwr_high,
  input  rd_low,
  input  rd_high,
  output [15:0] PC,
  output [7:0] Bus_A
);

  wire hc163_1_tc, hc163_2_tc, hc163_3_tc, not_1_out;
  wire [3:0] hc163_1_q0, hc163_2_q0, hc163_3_q0, hc163_4_q0;

  hc163 hc163_1 (
    .D0(Bus_B[0]), .D1(Bus_B[1]), .D2(Bus_B[2]), .D3(Bus_B[3]), .CET(enable), .CEP(enable), .PE(nwr_low),
    .nMR(nmr), .Clock(clock), .Q0(hc163_1_q0[0]), .Q1(hc163_1_q0[1]), .Q2(hc163_1_q0[2]), .Q3(hc163_1_q0[3]),
    .TC(hc163_1_tc));
  hc163 hc163_2 (
    .D0(Bus_B[4]), .D1(Bus_B[5]), .D2(Bus_B[6]), .D3(Bus_B[7]), .CET(hc163_1_tc), .CEP(enable), .PE(nwr_low),
    .nMR(nmr), .Clock(clock), .Q0(hc163_2_q0[0]), .Q1(hc163_2_q0[1]), .Q2(hc163_2_q0[2]), .Q3(hc163_2_q0[3]),
    .TC(hc163_2_tc));
  hc163 hc163_3 (
    .D0(Bus_B[0]), .D1(Bus_B[1]), .D2(Bus_B[2]), .D3(Bus_B[3]), .CET(hc163_2_tc), .CEP(enable),
    .PE(nwr_high), .nMR(nmr), .Clock(clock), .Q0(hc163_3_q0[0]), .Q1(hc163_3_q0[1]), .Q2(hc163_3_q0[2]),
    .Q3(hc163_3_q0[3]), .TC(hc163_3_tc));
  hc163 hc163_4 (
    .D0(Bus_B[4]), .D1(Bus_B[5]), .D2(Bus_B[6]), .D3(Bus_B[7]), .CET(hc163_3_tc), .CEP(enable),
    .PE(nwr_high), .nMR(nmr), .Clock(clock), .Q0(hc163_4_q0[0]), .Q1(hc163_4_q0[1]), .Q2(hc163_4_q0[2]),
    .Q3(hc163_4_q0[3]));  // open: TC
  not not_1 (not_1_out, clock);
  Register #(.width(16)) register_1 (
    .D({hc163_4_q0, hc163_3_q0, hc163_2_q0, hc163_1_q0}), .Q(PC), .clk(not_1_out));  // open: en, clr
  assign Bus_A = rd_low ? {hc163_2_q0, hc163_1_q0} : 8'bz;  // Controlled_Buffer controlled_buffer_1
  assign Bus_A = rd_high ? {hc163_4_q0, hc163_3_q0} : 8'bz;  // Controlled_Buffer controlled_buffer_2
endmodule

module _16_bit_stack_pointer (
  input  enable,
  input  up_down,
  input  clock,
  input  [7:0] B_BUS,
  input  nWR_LO,
  input  nWR_HI,
  input  RD_LO,
  input  RD_HI,
  output [15:0] PROG_COUNTER,
  output [7:0] A_BUS
);

  wire and_1_out, and_2_out, hc193_1_nbo, hc193_1_nco, hc193_2_nbo, hc193_2_nco, hc193_3_nbo, hc193_3_nco,
       not_1_out, not_2_out, not_3_out, not_4_out, or_1_out, or_2_out;
  wire [7:0] hc193_1_qa;
  wire [15:8] hc193_3_qa;

  not not_1 (not_1_out, clock);
  not not_2 (not_2_out, enable);
  not not_3 (not_3_out, enable);
  not not_4 (not_4_out, up_down);
  or or_1 (or_1_out, not_2_out, clock, up_down);
  or or_2 (or_2_out, not_3_out, not_4_out, clock);
  and and_1 (and_1_out, nWR_LO, not_1_out);
  and and_2 (and_2_out, not_1_out, nWR_HI);
  hc193 hc193_1 (
    .CLR(1'b0), .UP(or_1_out), .DOWN(or_2_out), .nLOAD(and_1_out), .A(B_BUS[0]), .B(B_BUS[1]), .C(B_BUS[2]),
    .D(B_BUS[3]), .nCO(hc193_1_nco), .nBO(hc193_1_nbo), .QA(hc193_1_qa[0]), .QB(hc193_1_qa[1]),
    .QC(hc193_1_qa[2]), .QD(hc193_1_qa[3]));
  hc193 hc193_2 (
    .CLR(1'b0), .UP(hc193_1_nco), .DOWN(hc193_1_nbo), .nLOAD(and_1_out), .A(B_BUS[4]), .B(B_BUS[5]),
    .C(B_BUS[6]), .D(B_BUS[7]), .nCO(hc193_2_nco), .nBO(hc193_2_nbo), .QA(hc193_1_qa[4]), .QB(hc193_1_qa[5]),
    .QC(hc193_1_qa[6]), .QD(hc193_1_qa[7]));
  assign A_BUS = RD_LO ? hc193_1_qa : 8'bz;  // Controlled_Buffer controlled_buffer_1
  hc193 hc193_3 (
    .CLR(1'b0), .UP(hc193_2_nco), .DOWN(hc193_2_nbo), .nLOAD(and_2_out), .A(B_BUS[0]), .B(B_BUS[1]),
    .C(B_BUS[2]), .D(B_BUS[3]), .nCO(hc193_3_nco), .nBO(hc193_3_nbo), .QA(hc193_3_qa[8]), .QB(hc193_3_qa[9]),
    .QC(hc193_3_qa[10]), .QD(hc193_3_qa[11]));
  assign A_BUS = RD_HI ? hc193_3_qa : 8'bz;  // Controlled_Buffer controlled_buffer_2
  Register #(.width(16)) register_1 (.D({hc193_3_qa, hc193_1_qa}), .Q(PROG_COUNTER), .clk(not_1_out));  // open: en, clr
  hc193 hc193_4 (
    .CLR(1'b0), .UP(hc193_3_nco), .DOWN(hc193_3_nbo), .nLOAD(and_2_out), .A(B_BUS[4]), .B(B_BUS[5]),
    .C(B_BUS[6]), .D(B_BUS[7]), .QA(hc193_3_qa[12]), .QB(hc193_3_qa[13]), .QC(hc193_3_qa[14]),
    .QD(hc193_3_qa[15]));  // open: nCO, nBO
endmodule

module _16_bit_stack_pointer_2 (
  input  [7:0] B_Bus,
  input  nenable,
  input  clock,
  input  nup_down,
  input  wr_low,
  input  wr_high,
  input  rd_low,
  input  rd_high,
  output [15:0] Count,
  output [7:0] A_bus
);

  wire hc191_1_nrc, hc191_2_nrc, hc191_3_nrc;
  wire [15:0] hc191_1_q0;

  hc191 hc191_1 (
    .D0(B_Bus[0]), .D1(B_Bus[1]), .D2(B_Bus[2]), .D3(B_Bus[3]), .nPL(wr_low), .nU_D(nup_down), .nCE(nenable),
    .CLK(clock), .Q0(hc191_1_q0[0]), .Q1(hc191_1_q0[1]), .Q2(hc191_1_q0[2]), .Q3(hc191_1_q0[3]),
    .nRC(hc191_1_nrc));  // open: TC
  hc191 hc191_2 (
    .D0(B_Bus[4]), .D1(B_Bus[5]), .D2(B_Bus[6]), .D3(B_Bus[7]), .nPL(wr_low), .nU_D(nup_down),
    .nCE(hc191_1_nrc), .CLK(clock), .Q0(hc191_1_q0[4]), .Q1(hc191_1_q0[5]), .Q2(hc191_1_q0[6]),
    .Q3(hc191_1_q0[7]), .nRC(hc191_2_nrc));  // open: TC
  assign A_bus = rd_low ? ~hc191_1_q0[7:0] : 8'bz;  // Controlled_Inverter controlled_inverter_1
  hc191 hc191_3 (
    .D0(B_Bus[0]), .D1(B_Bus[1]), .D2(B_Bus[2]), .D3(B_Bus[3]), .nPL(wr_high), .nU_D(nup_down),
    .nCE(hc191_2_nrc), .CLK(clock), .Q0(hc191_1_q0[8]), .Q1(hc191_1_q0[9]), .Q2(hc191_1_q0[10]),
    .Q3(hc191_1_q0[11]), .nRC(hc191_3_nrc));  // open: TC
  hc191 hc191_4 (
    .D0(B_Bus[4]), .D1(B_Bus[5]), .D2(B_Bus[6]), .D3(B_Bus[7]), .nPL(wr_high), .nU_D(nup_down),
    .nCE(hc191_3_nrc), .CLK(clock), .Q0(hc191_1_q0[12]), .Q1(hc191_1_q0[13]), .Q2(hc191_1_q0[14]),
    .Q3(hc191_1_q0[15]));  // open: TC, nRC
  assign A_bus = rd_high ? ~hc191_1_q0[15:8] : 8'bz;  // Controlled_Inverter controlled_inverter_2
  Register #(.width(16)) register_1 (.D(hc191_1_q0), .Q(Count), .clk(clock));  // open: en, clr
endmodule

module hc191 (
  input  D0,
  input  D1,
  input  D2,
  input  D3,
  input  nPL,
  input  nU_D,
  input  nCE,
  input  CLK,
  output Q0,
  output Q1,
  output Q2,
  output Q3,
  output TC,
  output nRC
);

  wire and_1_out, and_2_out, and_3_out, and_4_out, and_5_out, and_6_out, and_7_out, and_8_out, and_9_out,
       and_10_out, and_11_out, and_12_out, and_13_out, and_14_out, j_k_ff_1_qn, j_k_ff_2_qn, j_k_ff_3_qn,
       j_k_ff_4_qn, nand_2_out, nand_3_out, nand_4_out, nand_5_out, not_1_out, not_2_out, not_3_out,
       not_4_out, not_5_out, not_6_out, not_7_out, not_8_out, or_2_out, or_3_out, or_4_out;

  not not_1 (not_1_out, nPL);
  not not_2 (not_2_out, nU_D);
  not not_3 (not_3_out, nCE);
  not not_4 (not_4_out, CLK);
  and and_1 (and_1_out, not_2_out, not_3_out);
  and and_2 (and_2_out, not_3_out, nU_D);
  and and_3 (and_3_out, not_2_out, Q1, Q0, Q2, Q3);
  nand nand_1 (nRC, not_4_out, not_3_out, TC);
  and and_4 (and_4_out, nU_D, j_k_ff_1_qn, j_k_ff_2_qn, j_k_ff_3_qn, j_k_ff_4_qn);
  or or_1 (TC, and_3_out, and_4_out);
  nand nand_2 (nand_2_out, D0, not_1_out);
  not not_5 (not_5_out, nand_2_out);
  J_K_Flip_Flop #(.trigger("falling")) j_k_ff_1 (
    .J(not_3_out), .clk(not_4_out), .K(not_3_out), .Q(Q0), .Qn(j_k_ff_1_qn), .preset(not_5_out),
    .reset(and_5_out));  // open: en
  nand nand_3 (nand_3_out, D1, not_1_out);
  and and_5 (and_5_out, nand_2_out, not_1_out);
  and and_6 (and_6_out, and_2_out, j_k_ff_1_qn);
  or or_2 (or_2_out, and_6_out, and_7_out);
  not not_6 (not_6_out, nand_3_out);
  and and_7 (and_7_out, Q0, and_1_out);
  and and_8 (and_8_out, nand_3_out, not_1_out);
  J_K_Flip_Flop #(.trigger("falling")) j_k_ff_2 (
    .J(or_2_out), .clk(not_4_out), .K(or_2_out), .Q(Q1), .Qn(j_k_ff_2_qn), .preset(not_6_out),
    .reset(and_8_out));  // open: en
  and and_9 (and_9_out, and_2_out, j_k_ff_1_qn, j_k_ff_2_qn);
  nand nand_4 (nand_4_out, D2, not_1_out);
  not not_7 (not_7_out, nand_4_out);
  and and_10 (and_10_out, Q0, Q1, and_1_out);
  or or_3 (or_3_out, and_9_out, and_10_out);
  and and_11 (and_11_out, nand_4_out, not_1_out);
  J_K_Flip_Flop #(.trigger("falling")) j_k_ff_3 (
    .J(or_3_out), .clk(not_4_out), .K(or_3_out), .Q(Q2), .Qn(j_k_ff_3_qn), .preset(not_7_out),
    .reset(and_11_out));  // open: en
  nand nand_5 (nand_5_out, D3, not_1_out);
  and and_12 (and_12_out, Q0, Q1, Q2, and_1_out);
  and and_13 (and_13_out, and_2_out, j_k_ff_1_qn, j_k_ff_2_qn, j_k_ff_3_qn);
  or or_4 (or_4_out, and_13_out, and_12_out);
  J_K_Flip_Flop #(.trigger("falling")) j_k_ff_4 (
    .J(or_4_out), .clk(not_4_out), .K(or_4_out), .Q(Q3), .Qn(j_k_ff_4_qn), .preset(not_8_out),
    .reset(and_14_out));  // open: en
  not not_8 (not_8_out, nand_5_out);
  and and_14 (and_14_out, nand_5_out, not_1_out);
endmodule

module interrupt (
  input  interrupt,
  input  phase0,
  input  reset,
  input  \return ,
  output \int ,
  output int_run
);

  wire nand_1_out, nor_1_out, not_1_out, or_1_out;

  nor nor_1 (nor_1_out, interrupt, int_run, \int );
  not not_1 (not_1_out, \return );
  nand nand_1 (nand_1_out, reset, not_1_out);
  D_Flip_Flop d_ff_1 (.clk(phase0), .D(nor_1_out), .Q(\int ), .reset(nand_1_out));  // open: Qn, preset, en
  or or_1 (or_1_out, \int , int_run);
  D_Flip_Flop d_ff_2 (.clk(phase0), .D(or_1_out), .Q(int_run), .reset(nand_1_out));  // open: Qn, preset, en
endmodule
