// Logisim project cisc-8-demo.circ as structural Verilog: 8 circuits, main circuit main
module main (
  input  nreset,
  input  interrupt
);

  wire AddselADDR, AddselHL, AddselPC, AddselSP, and_1_out, and_4_out, carry_flag, carry_out, Clock,
       decoder_1_out0, decoder_1_out1, decoder_1_out2, decoder_1_out3, decoder_1_out4, decoder_1_out5,
       decoder_1_out6, decoder_1_out7, decoder_1_out8, decoder_1_out10, decoder_1_out11, decoder_2_out0,
       decoder_2_out1, decoder_2_out2, decoder_2_out3, decoder_2_out4, decoder_2_out5, decoder_2_out6,
       decoder_2_out7, decoder_2_out8, decoder_2_out10, decoder_2_out11, equal,
       instruction_decode_2_1_inst_latch, multiplexer_1_out, multiplexer_3_out, multiplexer_4_out, nor_1_out,
       not_1_out, not_2_out, not_3_out, not_4_out, not_5_out, not_6_out, not_7_out, or_1_out, or_2_out,
       passthru, PCenable, phase0, rdflag, rdpch, rdpcl, rdsph, rdspl, Restart, SPdir, SPenable, wr_pch,
       wr_pcl, wrflag, writereg, wrsph, wrspl, xnor_1_out, xnor_2_out, zero, zero_flag;
  wire [1:0] sel_addr;
  wire [2:0] hc163_1_q0, mode;
  wire [3:0] dest, src;
  wire [7:0] A_BUS, ACC_q, B_BUS, instruction_reg_q, ram_1_data, REG_B_q, REG_C_q, REG_D_q, REG_E_q, temp_q;
  wire [15:0] address, addrl_q, pc, REG_L_q, sp;

  // Probe on B_BUS
  Decoder #(.select(4), .disabled(0)) decoder_1 (
    .out0(decoder_1_out0), .out1(decoder_1_out1), .out2(decoder_1_out2), .out3(decoder_1_out3),
    .out4(decoder_1_out4), .out5(decoder_1_out5), .out6(decoder_1_out6), .out7(decoder_1_out7),
    .out8(decoder_1_out8), .out9(wrflag), .out10(decoder_1_out10), .out11(decoder_1_out11), .out12(wrspl),
    .out13(wrsph), .sel(dest), .en(writereg));  // open: out14, out15
  Decoder #(.select(4), .disabled(0), .enable("false")) decoder_2 (
    .out0(decoder_2_out0), .out1(decoder_2_out1), .out2(decoder_2_out2), .out3(decoder_2_out3),
    .out4(decoder_2_out4), .out5(decoder_2_out5), .out6(decoder_2_out6), .out7(decoder_2_out7),
    .out8(decoder_2_out8), .out9(rdflag), .out10(decoder_2_out10), .out11(decoder_2_out11), .out12(rdspl),
    .out13(rdsph), .out14(rdpcl), .out15(rdpch), .sel(src));
  Clock clock_1 (.out(Clock));
  assign A_BUS = decoder_2_out0 ? REG_B_q : 8'bz;  // Controlled_Buffer controlled_buffer_1
  Register REG_B (.D(B_BUS), .Q(REG_B_q), .clk(decoder_1_out0));  // open: en, clr
  RAM #(.addrWidth(16)) ram_1 (
    .addr(address), .data(ram_1_data), .clk(not_1_out), .ld(decoder_2_out6));  // open: sel, clr
  not not_1 (not_1_out, decoder_1_out6);
  and and_1 (and_1_out, nreset, Restart);
  not not_2 (not_2_out, Clock);
  assign A_BUS = decoder_2_out1 ? REG_C_q : 8'bz;  // Controlled_Buffer controlled_buffer_2
  Register REG_C (.D(B_BUS), .Q(REG_C_q), .clk(decoder_1_out1));  // open: en, clr
  assign A_BUS = decoder_2_out6 ? ram_1_data : 8'bz;  // Controlled_Buffer controlled_buffer_3
  assign ram_1_data = nor_1_out ? B_BUS : 8'bz;  // Controlled_Buffer controlled_buffer_4
  nor nor_1 (nor_1_out, decoder_2_out6, Clock);
  hc163 hc163_1 (
    .CET(1'b1), .CEP(1'b1), .PE(1'b1), .nMR(and_1_out), .Clock(not_2_out), .Q0(hc163_1_q0[0]),
    .Q1(hc163_1_q0[1]), .Q2(hc163_1_q0[2]));  // open: D0, D1, D2, D3, Q3, TC
  assign A_BUS = decoder_2_out2 ? REG_D_q : 8'bz;  // Controlled_Buffer controlled_buffer_5
  Register REG_D (.D(B_BUS), .Q(REG_D_q), .clk(decoder_1_out2));  // open: en, clr
  // Probe on hc163_1_q0
  assign A_BUS = decoder_2_out3 ? REG_E_q : 8'bz;  // Controlled_Buffer controlled_buffer_6
  Register REG_E (.D(B_BUS), .Q(REG_E_q), .clk(decoder_1_out3));  // open: en, clr
  assign A_BUS = decoder_2_out4 ? REG_L_q[15:8] : 8'bz;  // Controlled_Buffer controlled_buffer_7
  Register REG_H (.D(B_BUS), .Q(REG_L_q[15:8]), .clk(decoder_1_out4));  // open: en, clr
  Register REG_L (.D(B_BUS), .Q(REG_L_q[7:0]), .clk(decoder_1_out5));  // open: en, clr
  Register instruction_reg (
    .D(A_BUS), .Q(instruction_reg_q), .clk(instruction_decode_2_1_inst_latch));  // open: en, clr
  assign A_BUS = decoder_2_out5 ? REG_L_q[7:0] : 8'bz;  // Controlled_Buffer controlled_buffer_8
  assign A_BUS = decoder_2_out7 ? ACC_q : 8'bz;  // Controlled_Buffer controlled_buffer_9
  Register ACC (.D(B_BUS), .Q(ACC_q), .clk(decoder_1_out7));  // open: en, clr
  assign A_BUS = decoder_2_out10 ? addrl_q[7:0] : 8'bz;  // Controlled_Buffer controlled_buffer_10
  Register addrl (.D(B_BUS), .Q(addrl_q[7:0]), .clk(decoder_1_out10));  // open: en, clr
  instruction_decode_2 instruction_decode_2_1 (
    .cond_true(multiplexer_1_out), .inst(instruction_reg_q), .phase(hc163_1_q0), .phase0(phase0),
    .inst_latch(instruction_decode_2_1_inst_latch), .interrupt(interrupt), .nreset(nreset), .clock(Clock),
    .src(src), .dest(dest), .mode(mode), .AddselHL(AddselHL), .AddselADDR(AddselADDR), .AddselSP(AddselSP),
    .AddselPC(AddselPC), .writereg(writereg), .Restart(Restart), .PCenable(PCenable), .wr_pch(wr_pch),
    .wr_pcl(wr_pcl), .SPenable(SPenable), .SP_dir(SPdir));
  assign A_BUS = decoder_2_out11 ? addrl_q[15:8] : 8'bz;  // Controlled_Buffer controlled_buffer_11
  Register addrh (.D(B_BUS), .Q(addrl_q[15:8]), .clk(decoder_1_out11));  // open: en, clr
  // Probe on dest
  // Probe on mode
  // Probe on src
  assign A_BUS = decoder_2_out8 ? temp_q : 8'bz;  // Controlled_Buffer controlled_buffer_12
  Register temp (.D(B_BUS), .Q(temp_q), .clk(decoder_1_out8));  // open: en, clr
  xnor xnor_1 (xnor_1_out, zero_flag, instruction_reg_q[3]);
  Multiplexer #(.disabled(0), .enable("false")) multiplexer_1 (
    .in0(xnor_1_out), .in1(xnor_2_out), .out(multiplexer_1_out), .sel(instruction_reg_q[4]));
  xnor xnor_2 (xnor_2_out, instruction_reg_q[3], carry_flag);
  Multiplexer #(.select(2), .width(16), .enable("false")) multiplexer_2 (
    .in0(REG_L_q), .in1(addrl_q), .in2(sp), .in3(pc), .out(address), .sel(sel_addr));
  or or_1 (or_1_out, phase0, PCenable);
  // Probe on A_BUS
  cisc_8_alu ALU (
    .mode(mode), .Cin(carry_flag), .A(temp_q), .B(A_BUS), .Passthru(passthru), .out(B_BUS), .Cout(carry_out),
    .zero(zero), .equal(equal));
  // Probe on address
  not not_3 (not_3_out, AddselSP);
  not not_4 (not_4_out, AddselHL);
  not not_5 (not_5_out, AddselADDR);
  not not_6 (not_6_out, AddselHL);
  prog_counter Program_counter (
    .enable(or_1_out), .reset(nreset), .clock(Clock), .b_bus(B_BUS), .wr_pcl(wr_pcl), .wr_pch(wr_pch),
    .rdpcl(rdpcl), .rdpch(rdpch), .prog_count(pc), .writereg(A_BUS));
  stack_pointer stack_pointer (
    .B_BUS(B_BUS), .nenable(SPenable), .clock(Clock), .nup_down(SPdir), .wr_spl(wrspl), .wr_sph(wrsph),
    .rdspl(rdspl), .rdsph(rdsph), .stack_pointer(sp), .A_BUS(A_BUS));
  and and_2 (sel_addr[0], not_3_out, not_4_out);
  and and_3 (sel_addr[1], not_5_out, not_6_out);
  // Probe on pc
  // Probe on sp
  not not_7 (not_7_out, passthru);
  and and_4 (and_4_out, not_7_out, writereg);
  Multiplexer #(.disabled(0), .enable("false")) multiplexer_3 (
    .in0(carry_out), .in1(B_BUS[0]), .out(multiplexer_3_out), .sel(passthru));
  Multiplexer #(.disabled(0), .enable("false")) multiplexer_4 (
    .in0(zero), .in1(B_BUS[6]), .out(multiplexer_4_out), .sel(passthru));
  or or_2 (or_2_out, and_4_out, wrflag);
  D_Flip_Flop Carry (.clk(or_2_out), .D(multiplexer_3_out), .Q(carry_flag));  // open: Qn, preset, en, reset
  D_Flip_Flop u_Zero (.clk(or_2_out), .D(multiplexer_4_out), .Q(zero_flag));  // open: Qn, preset, en, reset
  assign A_BUS = rdflag ? {1'b0, zero_flag, {5{1'b0}}, carry_flag} : 8'bz;  // Controlled_Buffer controlled_buffer_13

  // Other names for the same wires on the sheet: reset = nreset
endmodule

module cisc_8_alu (
  input  [2:0] mode,
  input  Cin,
  input  [7:0] A,
  input  [7:0] B,
  output [7:0] out,
  output Cout,
  output zero,
  output equal,
  output Passthru
);

  wire \and , decoder_2_out2, decoder_2_out5, decoder_2_out7, nor_1_out, nor_2_out, nor_3_out, nor_4_out,
       not_1_out, \or , or_2_out, \xor ;
  wire [7:0] adder_1_out, and_1_out, multiplexer_1_out, or_1_out, xor_1_out, xor_2_out;

  Decoder #(.select(3), .enable("false")) decoder_1 (
    .out4(\and ), .out5(\xor ), .out6(\or ), .out7(Passthru), .sel(mode));  // open: out0, out1, out2, out3
  not not_1 (not_1_out, mode[2]);
  assign and_1_out = A & B;  // AND_Gate and_1, 8 bits wide
  assign or_1_out = A | B;  // OR_Gate or_1, 8 bits wide
  Decoder #(.select(3), .disabled(0), .enable("false")) decoder_2 (
    .out2(decoder_2_out2), .out5(decoder_2_out5), .out7(decoder_2_out7), .sel({Cin, mode[1:0]}));  // open: out0, out1, out3, out4, out6
  Multiplexer #(.width(8), .enable("false")) multiplexer_1 (
    .in0({8{mode[1]}}), .in1(A), .out(multiplexer_1_out), .sel(\xor ));
  assign xor_1_out = A ^ B;  // XOR_Gate xor_1, 8 bits wide
  assign xor_2_out = multiplexer_1_out ^ B;  // XOR_Gate xor_2, 8 bits wide
  or or_2 (or_2_out, decoder_2_out2, decoder_2_out5, decoder_2_out7);
  assign out = Passthru ? B : 8'bz;  // Controlled_Buffer controlled_buffer_1
  assign out = \or  ? or_1_out : 8'bz;  // Controlled_Buffer controlled_buffer_2
  Adder adder_1 (.a(A), .b(xor_2_out), .out(adder_1_out), .cin(or_2_out), .cout(Cout));
  nor nor_1 (nor_1_out, xor_1_out[0], xor_1_out[1], xor_1_out[2], xor_1_out[3]);
  and and_2 (equal, nor_1_out, nor_2_out);
  nor nor_2 (nor_2_out, xor_1_out[4], xor_1_out[5], xor_1_out[6], xor_1_out[7]);
  assign out = not_1_out ? adder_1_out : 8'bz;  // Controlled_Buffer controlled_buffer_3
  assign out = \xor  ? xor_2_out : 8'bz;  // Controlled_Buffer controlled_buffer_4
  assign out = \and  ? and_1_out : 8'bz;  // Controlled_Buffer controlled_buffer_5
  nor nor_3 (nor_3_out, out[0], out[1], out[2], out[3]);
  nor nor_4 (nor_4_out, out[4], out[5], out[6], out[7]);
  and and_3 (zero, nor_3_out, nor_4_out);

  // Other names for the same wires on the sheet: pass_b = Passthru

  // Notes on the sheet:
  //   Add
  //   Adc
  //   Sub
  //   Sbb
  //   And
  //   Xor
  //   Or
  //   passb
  //   Mode
  //   0 0 0
  //   0 0 0
  //   0 0 1
  //   0 1 0
  //   0 1 1
  //   1 0 0
  //   1 0 1
  //   1 1 0
  //   1 1 1
endmodule

module hc191 (
  input  D0,
  input  D1,
  input  D2,
  input  D3,
  input  nPL,
  input  nU_D,
  input  nCE,
  input  CLK,
  output Q0,
  output Q1,
  output Q2,
  output Q3,
  output TC,
  output nRC
);

  wire and_1_out, and_2_out, and_3_out, and_4_out, and_5_out, and_6_out, and_7_out, and_8_out, and_9_out,
       and_10_out, and_11_out, and_12_out, and_13_out, and_14_out, j_k_ff_1_qn, j_k_ff_2_qn, j_k_ff_3_qn,
       j_k_ff_4_qn, nand_2_out, nand_3_out, nand_4_out, nand_5_out, not_1_out, not_2_out, not_3_out,
       not_4_out, not_5_out, not_6_out, not_7_out, not_8_out, or_2_out, or_3_out, or_4_out;

  not not_1 (not_1_out, nPL);
  not not_2 (not_2_out, nU_D);
  not not_3 (not_3_out, nCE);
  not not_4 (not_4_out, CLK);
  and and_1 (and_1_out, not_2_out, not_3_out);
  and and_2 (and_2_out, not_3_out, nU_D);
  and and_3 (and_3_out, not_2_out, Q1, Q0, Q2, Q3);
  nand nand_1 (nRC, not_4_out, not_3_out, TC);
  and and_4 (and_4_out, nU_D, j_k_ff_1_qn, j_k_ff_2_qn, j_k_ff_3_qn, j_k_ff_4_qn);
  or or_1 (TC, and_3_out, and_4_out);
  nand nand_2 (nand_2_out, D0, not_1_out);
  not not_5 (not_5_out, nand_2_out);
  J_K_Flip_Flop j_k_ff_1 (
    .J(not_3_out), .clk(not_4_out), .K(not_3_out), .Q(Q0), .Qn(j_k_ff_1_qn), .preset(not_5_out),
    .reset(and_5_out));  // open: en
  nand nand_3 (nand_3_out, D1, not_1_out);
  and and_5 (and_5_out, nand_2_out, not_1_out);
  and and_6 (and_6_out, and_2_out, j_k_ff_1_qn);
  or or_2 (or_2_out, and_6_out, and_7_out);
  not not_6 (not_6_out, nand_3_out);
  and and_7 (and_7_out, Q0, and_1_out);
  and and_8 (and_8_out, nand_3_out, not_1_out);
  J_K_Flip_Flop j_k_ff_2 (
    .J(or_2_out), .clk(not_4_out), .K(or_2_out), .Q(Q1), .Qn(j_k_ff_2_qn), .preset(not_6_out),
    .reset(and_8_out));  // open: en
  and and_9 (and_9_out, and_2_out, j_k_ff_1_qn, j_k_ff_2_qn);
  nand nand_4 (nand_4_out, D2, not_1_out);
  not not_7 (not_7_out, nand_4_out);
  and and_10 (and_10_out, Q0, Q1, and_1_out);
  or or_3 (or_3_out, and_9_out, and_10_out);
  and and_11 (and_11_out, nand_4_out, not_1_out);
  J_K_Flip_Flop j_k_ff_3 (
    .J(or_3_out), .clk(not_4_out), .K(or_3_out), .Q(Q2), .Qn(j_k_ff_3_qn), .preset(not_7_out),
    .reset(and_11_out));  // open: en
  nand nand_5 (nand_5_out, D3, not_1_out);
  and and_12 (and_12_out, Q0, Q1, Q2, and_1_out);
  and and_13 (and_13_out, and_2_out, j_k_ff_1_qn, j_k_ff_2_qn, j_k_ff_3_qn);
  or or_4 (or_4_out, and_13_out, and_12_out);
  J_K_Flip_Flop j_k_ff_4 (
    .J(or_4_out), .clk(not_4_out), .K(or_4_out), .Q(Q3), .Qn(j_k_ff_4_qn), .preset(not_8_out),
    .reset(and_14_out));  // open: en
  not not_8 (not_8_out, nand_5_out);
  and and_14 (and_14_out, nand_5_out, not_1_out);
endmodule

module hc163 (
  input  D0,
  input  D1,
  input  D2,
  input  D3,
  input  CET,
  input  CEP,
  input  PE,
  input  nMR,
  input  Clock,
  output Q0,
  output Q1,
  output Q2,
  output Q3,
  output TC
);

  wire and_1_out, and_2_out, and_3_out, and_4_out, and_5_out, and_6_out, and_7_out, and_8_out, and_9_out,
       d_ff_1_q, d_ff_1_qn, d_ff_2_q, d_ff_2_qn, d_ff_3_q, d_ff_3_qn, d_ff_4_q, d_ff_4_qn, nand_1_out,
       nand_2_out, nor_1_out, nor_2_out, nor_3_out, nor_4_out, nor_5_out, nor_6_out, not_1_out, not_2_out,
       or_1_out, or_2_out, or_3_out, or_4_out, or_5_out, xnor_1_out, xnor_2_out, xnor_3_out;

  nand nand_1 (nand_1_out, CET, CEP);
  nor nor_1 (nor_1_out, PE, not_1_out);
  not not_1 (not_1_out, nMR);
  nor nor_2 (nor_2_out, nor_1_out, not_1_out);
  not not_2 (not_2_out, nand_1_out);
  xnor xnor_1 (xnor_1_out, not_2_out, d_ff_1_qn);
  and and_1 (and_1_out, D0, nor_1_out);
  or or_1 (or_1_out, and_1_out, and_2_out);
  and and_2 (and_2_out, xnor_1_out, nor_2_out);
  D_Flip_Flop d_ff_1 (.clk(Clock), .D(or_1_out), .Q(d_ff_1_q), .Qn(d_ff_1_qn));  // open: preset, en, reset
  not not_3 (Q0, d_ff_1_qn);
  nor nor_3 (nor_3_out, nand_1_out, d_ff_1_qn);
  and and_3 (and_3_out, D1, nor_1_out);
  or or_2 (or_2_out, and_3_out, and_4_out);
  xnor xnor_2 (xnor_2_out, nor_3_out, d_ff_2_qn);
  and and_4 (and_4_out, xnor_2_out, nor_2_out);
  D_Flip_Flop d_ff_2 (.clk(Clock), .D(or_2_out), .Q(d_ff_2_q), .Qn(d_ff_2_qn));  // open: preset, en, reset
  not not_4 (Q1, d_ff_2_qn);
  nor nor_4 (nor_4_out, nand_1_out, d_ff_1_qn, d_ff_2_qn);
  xnor xnor_3 (xnor_3_out, nor_4_out, d_ff_3_qn);
  and and_5 (and_5_out, D2, nor_1_out);
  or or_3 (or_3_out, and_5_out, and_6_out);
  and and_6 (and_6_out, xnor_3_out, nor_2_out);
  D_Flip_Flop d_ff_3 (.clk(Clock), .D(or_3_out), .Q(d_ff_3_q), .Qn(d_ff_3_qn));  // open: preset, en, reset
  not not_5 (Q2, d_ff_3_qn);
  nor nor_5 (nor_5_out, nand_1_out, d_ff_1_qn, d_ff_2_qn, d_ff_3_qn);
  and and_7 (and_7_out, D3, nor_1_out);
  or or_4 (or_4_out, and_7_out, and_9_out);
  and and_8 (and_8_out, nor_5_out, d_ff_4_qn);
  nor nor_6 (nor_6_out, nor_5_out, d_ff_4_qn);
  or or_5 (or_5_out, and_8_out, nor_6_out);
  and and_9 (and_9_out, nor_2_out, or_5_out);
  D_Flip_Flop d_ff_4 (.clk(Clock), .D(or_4_out), .Q(d_ff_4_q), .Qn(d_ff_4_qn));  // open: preset, en, reset
  not not_6 (Q3, d_ff_4_qn);
  nand nand_2 (nand_2_out, d_ff_4_q, d_ff_3_q, d_ff_2_q, d_ff_1_q, CET);
  not not_7 (TC, nand_2_out);
endmodule

module _8_bit_up_count_w_preset (
  input  [7:0] D,
  input  CEP_T,
  input  nPE,
  input  nMR,
  input  CP,
  output [7:0] Q,
  output TC
);

  wire hc163_1_tc;

  hc163 hc163_1 (
    .D0(D[0]), .D1(D[1]), .D2(D[2]), .D3(D[3]), .CET(CEP_T), .CEP(CEP_T), .PE(nPE), .nMR(nMR), .Clock(CP),
    .Q0(Q[0]), .Q1(Q[1]), .Q2(Q[2]), .Q3(Q[3]), .TC(hc163_1_tc));
  hc163 hc163_2 (
    .D0(D[4]), .D1(D[5]), .D2(D[6]), .D3(D[7]), .CET(hc163_1_tc), .CEP(hc163_1_tc), .PE(nPE), .nMR(nMR),
    .Clock(CP), .Q0(Q[4]), .Q1(Q[5]), .Q2(Q[6]), .Q3(Q[7]), .TC(TC));
endmodule

module prog_counter (
  input  enable,
  input  reset,
  input  clock,
  input  [7:0] b_bus,
  input  wr_pcl,
  input  wr_pch,
  input  rdpcl,
  input  rdpch,
  output [15:0] prog_count,
  output [7:0] writereg
);

  wire hc163_1_tc, hc163_2_tc, hc163_3_tc, not_1_out, not_2_out;

  hc163 hc163_1 (
    .D0(b_bus[0]), .D1(b_bus[1]), .D2(b_bus[2]), .D3(b_bus[3]), .CET(enable), .CEP(enable), .PE(not_1_out),
    .nMR(reset), .Clock(clock), .Q0(prog_count[0]), .Q1(prog_count[1]), .Q2(prog_count[2]),
    .Q3(prog_count[3]), .TC(hc163_1_tc));
  not not_1 (not_1_out, wr_pcl);
  hc163 hc163_2 (
    .D0(b_bus[4]), .D1(b_bus[5]), .D2(b_bus[6]), .D3(b_bus[7]), .CET(hc163_1_tc), .CEP(hc163_1_tc),
    .PE(not_1_out), .nMR(reset), .Clock(clock), .Q0(prog_count[4]), .Q1(prog_count[5]), .Q2(prog_count[6]),
    .Q3(prog_count[7]), .TC(hc163_2_tc));
  hc163 hc163_3 (
    .D0(b_bus[0]), .D1(b_bus[1]), .D2(b_bus[2]), .D3(b_bus[3]), .CET(hc163_2_tc), .CEP(hc163_2_tc),
    .PE(not_2_out), .nMR(reset), .Clock(clock), .Q0(prog_count[8]), .Q1(prog_count[9]), .Q2(prog_count[10]),
    .Q3(prog_count[11]), .TC(hc163_3_tc));
  not not_2 (not_2_out, wr_pch);
  hc163 hc163_4 (
    .D0(b_bus[4]), .D1(b_bus[5]), .D2(b_bus[6]), .D3(b_bus[7]), .CET(hc163_3_tc), .CEP(hc163_3_tc),
    .PE(not_2_out), .nMR(reset), .Clock(clock), .Q0(prog_count[12]), .Q1(prog_count[13]),
    .Q2(prog_count[14]), .Q3(prog_count[15]));  // open: TC
  assign writereg = rdpch ? prog_count[15:8] : 8'bz;  // Controlled_Buffer controlled_buffer_1
  assign writereg = rdpcl ? prog_count[7:0] : 8'bz;  // Controlled_Buffer controlled_buffer_2
endmodule

module instruction_decode_2 (
  input  cond_true,
  input  [7:0] inst,
  input  [2:0] phase,
  input  interrupt,
  input  nreset,
  input  clock,
  output [3:0] src,
  output phase0,
  output inst_latch,
  output [3:0] dest,
  output [2:0] mode,
  output AddselHL,
  output AddselADDR,
  output AddselSP,
  output AddselPC,
  output writereg,
  output Restart,
  output PCenable,
  output wr_pch,
  output wr_pcl,
  output SPenable,
  output SP_dir
);

  wire and_17_out, and_18_out, and_19_out, and_20_out, and_21_out, and_22_out, and_23_out, and_24_out,
       and_25_out, and_26_out, and_27_out, and_28_out, and_29_out, and_30_out, and_31_out, and_32_out,
       and_33_out, and_34_out, and_35_out, and_36_out, and_37_out, and_38_out, and_39_out, and_40_out,
       and_41_out, and_42_out, and_44_out, and_45_out, and_46_out, and_47_out, and_48_out, and_50_out,
       and_51_out, and_52_out, and_53_out, and_54_out, and_55_out, and_56_out, and_57_out, and_58_out,
       and_59_out, and_60_out, and_62_out, and_63_out, and_64_out, and_65_out, and_66_out, and_67_out,
       and_68_out, and_69_out, and_70_out, and_71_out, and_72_out, and_73_out, and_74_out, and_75_out,
       and_76_out, call, d_ff_1_q, decoder_1_out1, decoder_1_out2, decoder_1_out3, decoder_1_out5,
       decoder_1_out6, decoder_2_out1, decoder_2_out6, decoder_2_out7, decoder_3_out0, decoder_3_out3, jc,
       jmp, jnc, lda, lri, maths, mlimm, mov, mov16, nor_1_out, not_1_out, not_2_out, not_3_out, not_4_out,
       not_5_out, not_6_out, or_1_out, or_2_out, or_3_out, or_4_out, or_5_out, or_6_out, or_7_out, or_8_out,
       or_9_out, or_10_out, or_11_out, or_12_out, or_13_out, or_14_out, or_15_out, or_16_out, or_17_out,
       or_18_out, or_19_out, or_20_out, or_21_out, or_22_out, or_23_out, or_24_out, or_25_out, or_26_out,
       or_27_out, or_28_out, or_30_out, or_31_out, or_32_out, or_33_out, or_34_out, or_35_out, phase1,
       phase2, phase3, phase4, phase5, phase6, pop, push, ret, sta;
  wire [0:0] RPH;
  wire [3:1] RPL;

  Decoder #(.select(3), .disabled(0)) decoder_1 (
    .out1(decoder_1_out1), .out2(decoder_1_out2), .out3(decoder_1_out3), .out5(decoder_1_out5),
    .out6(decoder_1_out6), .sel(inst[2:0]), .en(d_ff_1_q));  // open: out0, out4, out7
  Decoder #(.select(3), .disabled(0)) decoder_2 (
    .out1(decoder_2_out1), .out6(decoder_2_out6), .out7(decoder_2_out7), .sel(inst[5:3]), .en(d_ff_1_q));  // open: out0, out2, out3, out4, out5
  D_Flip_Flop d_ff_1 (.clk(phase0), .D(interrupt), .Q(d_ff_1_q), .preset(not_1_out));  // open: Qn, en, reset
  not not_1 (not_1_out, nreset);
  not not_2 (not_2_out, inst[3]);
  and and_1 (inst_latch, phase0, clock);
  Decoder #(.select(2), .disabled(0)) decoder_3 (
    .out0(decoder_3_out0), .out1(mov), .out2(maths), .out3(decoder_3_out3), .sel(inst[7:6]), .en(d_ff_1_q));
  not not_3 (not_3_out, cond_true);
  Decoder #(.select(3), .disabled(0), .enable("false")) decoder_4 (
    .out0(phase0), .out1(phase1), .out2(phase2), .out3(phase3), .out4(phase4), .out5(phase5), .out6(phase6),
    .sel(phase));  // open: out7
  and and_2 (mlimm, decoder_3_out3, decoder_1_out6);
  and and_3 (mov16, decoder_3_out3, decoder_2_out7, decoder_1_out1);
  and and_4 (lda, decoder_3_out0, decoder_2_out7, decoder_1_out2);
  and and_5 (sta, decoder_3_out0, decoder_2_out6, decoder_1_out2);
  and and_6 (lri, decoder_3_out0, decoder_1_out6);
  and and_7 (push, decoder_3_out3, not_2_out, decoder_1_out5);
  and and_8 (pop, decoder_3_out3, not_2_out, decoder_1_out1);
  and and_9 (jmp, decoder_3_out3, not_2_out, decoder_1_out3);
  and and_10 (jc, decoder_3_out3, decoder_1_out2, cond_true);
  and and_11 (jnc, decoder_3_out3, decoder_1_out2, not_3_out);
  and and_12 (call, decoder_3_out3, decoder_2_out1, decoder_1_out5);
  and and_13 (ret, decoder_3_out3, decoder_2_out1, decoder_1_out1);
  not not_4 (not_4_out, phase0);
  not not_5 (not_5_out, inst[5]);
  and and_14 (RPL[1], not_5_out, inst[4]);
  and and_15 (RPL[2], inst[5], not_6_out);
  not not_6 (not_6_out, inst[4]);
  and and_16 (RPL[3], inst[5], inst[4]);
  and and_17 (and_17_out, phase1, mov);
  and and_18 (and_18_out, phase2, maths);
  or or_1 (or_1_out, maths, mlimm);
  and and_19 (and_19_out, phase3, sta);
  and and_20 (and_20_out, phase1, mov16);
  and and_21 (and_21_out, phase2, mov16);
  and and_22 (and_22_out, phase1, push);
  and and_23 (and_23_out, phase2, push);
  or or_2 (or_2_out, jmp, jc);
  and and_24 (and_24_out, phase3, call);
  and and_25 (and_25_out, phase4, call);
  and and_26 (and_26_out, phase5, call);
  and and_27 (and_27_out, phase6, call);
  or or_3 (or_3_out, lri, mov);
  or or_4 (or_4_out, maths, mlimm, pop, jmp, jc, jnc);
  and and_28 (and_28_out, jnc, phase2);
  or or_5 (or_5_out, maths, mlimm);
  and and_29 (and_29_out, phase3, lda);
  and and_30 (and_30_out, phase1, mov16);
  and and_31 (and_31_out, phase2, mov16);
  or or_6 (or_6_out, lda, sta, call);
  or or_7 (or_7_out, lda, sta, call);
  and and_32 (and_32_out, phase1, push);
  and and_33 (and_33_out, phase2, push);
  or or_8 (or_8_out, sta, call);
  and and_34 (and_34_out, phase4, call);
  and and_35 (and_35_out, phase2, pop);
  and and_36 (and_36_out, phase3, pop);
  and and_37 (and_37_out, phase1, ret);
  or or_9 (or_9_out, jmp, jc, ret);
  and and_38 (and_38_out, phase6, call);
  or or_10 (or_10_out, jmp, jc, ret);
  and and_39 (and_39_out, phase5, call);
  or or_11 (or_11_out, maths, mlimm);
  and and_40 (and_40_out, phase1, mov);
  and and_41 (and_41_out, phase2, maths);
  or or_12 (or_12_out, lda, sta);
  or or_13 (or_13_out, push, pop, ret);
  or or_14 (or_14_out, push, pop, ret);
  or or_15 (or_15_out, pop, call, ret);
  and and_42 (and_42_out, phase4, call);
  and and_43 (writereg, not_4_out, clock);
  or or_16 (or_16_out, mov, lri);
  or or_17 (or_17_out, maths, mlimm, mov16, push, jnc);
  or or_18 (or_18_out, lda, sta, pop, jmp, jc, ret);
  and and_44 (and_44_out, phase6, call);
  or or_19 (or_19_out, lda, sta, lri, jmp, jc, jnc, call);
  or or_20 (or_20_out, mlimm, lda, sta, jnc, call);
  or or_21 (or_21_out, jmp, jc);
  and and_45 (and_45_out, phase6, call);
  and and_46 (and_46_out, phase3, call);
  or or_22 (or_22_out, jmp, jc);
  and and_47 (and_47_out, phase5, call);
  and and_48 (and_48_out, phase2, call);
  or or_23 (or_23_out, push, pop, ret);
  or or_24 (or_24_out, push, pop, ret);
  or or_25 (or_25_out, phase3, phase4);
  or or_26 (or_26_out, phase1, phase2);
  or or_27 (or_27_out, phase3, phase4);
  and and_49 (RPH[0], inst[5], inst[4]);
  or or_28 (or_28_out, and_17_out, and_18_out);
  and and_50 (and_50_out, phase1, or_1_out);
  and and_51 (and_51_out, phase3, or_2_out);
  nor nor_1 (nor_1_out, and_27_out, and_26_out, and_25_out, and_24_out, and_51_out, and_23_out, and_22_out, and_21_out, and_20_out, or_30_out, or_28_out);
  and and_52 (and_52_out, phase1, or_3_out);
  and and_53 (and_53_out, phase1, or_4_out);
  and and_54 (and_54_out, phase2, or_5_out);
  and and_55 (and_55_out, phase1, or_6_out);
  and and_56 (and_56_out, phase2, or_7_out);
  and and_57 (and_57_out, phase3, or_8_out);
  and and_58 (and_58_out, phase2, or_9_out);
  and and_59 (and_59_out, phase3, or_10_out);
  and and_60 (and_60_out, phase2, or_11_out);
  or or_29 (AddselHL, and_40_out, and_41_out);
  and and_61 (AddselADDR, phase3, or_12_out);
  and and_62 (and_62_out, phase1, or_13_out);
  and and_63 (and_63_out, phase2, or_14_out);
  and and_64 (and_64_out, phase3, or_15_out);
  and and_65 (and_65_out, phase1, or_16_out);
  and and_66 (and_66_out, phase2, or_17_out);
  and and_67 (and_67_out, phase3, or_18_out);
  and and_68 (and_68_out, phase1, or_19_out);
  and and_69 (and_69_out, phase2, or_20_out);
  and and_70 (and_70_out, phase2, or_21_out);
  and and_71 (and_71_out, phase3, or_22_out);
  and and_72 (and_72_out, phase1, or_23_out);
  and and_73 (and_73_out, phase2, or_24_out);
  and and_74 (and_74_out, call, or_25_out);
  and and_75 (and_75_out, push, or_26_out);
  and and_76 (and_76_out, call, or_27_out);
  or or_30 (or_30_out, and_50_out, and_19_out);
  or or_31 (or_31_out, and_53_out, and_28_out);
  or or_32 (or_32_out, and_54_out, and_29_out);
  or or_33 (or_33_out, and_32_out, and_33_out, and_57_out, and_34_out);
  or or_34 (or_34_out, and_37_out, and_58_out, and_38_out);
  or or_35 (or_35_out, and_59_out, and_39_out);
  or or_36 (AddselSP, and_62_out, and_63_out, and_64_out, and_42_out);
  assign src = or_28_out ? {1'b0, inst[2:0]} : 4'bz;  // Controlled_Buffer controlled_buffer_1
  assign src = or_30_out ? 4'b0111 : 4'bz;  // Controlled_Buffer controlled_buffer_2
  assign src = and_20_out ? 4'b0101 : 4'bz;  // Controlled_Buffer controlled_buffer_3
  assign src = and_21_out ? 4'b0100 : 4'bz;  // Controlled_Buffer controlled_buffer_4
  assign src = and_22_out ? {1'b0, inst[5:4], RPH[0]} : 4'bz;  // Controlled_Buffer controlled_buffer_5
  assign src = and_23_out ? {RPL, 1'b1} : 4'bz;  // Controlled_Buffer controlled_buffer_6
  assign src = and_51_out ? 4'b1000 : 4'bz;  // Controlled_Buffer controlled_buffer_7
  assign src = and_24_out ? 4'b1111 : 4'bz;  // Controlled_Buffer controlled_buffer_8
  assign src = and_25_out ? 4'b1110 : 4'bz;  // Controlled_Buffer controlled_buffer_9
  assign src = and_26_out ? 4'b1010 : 4'bz;  // Controlled_Buffer controlled_buffer_10
  assign src = and_27_out ? 4'b1011 : 4'bz;  // Controlled_Buffer controlled_buffer_11
  assign src = nor_1_out ? 4'b0110 : 4'bz;  // Controlled_Buffer controlled_buffer_12
  assign dest = and_52_out ? {1'b0, inst[5:3]} : 4'bz;  // Controlled_Buffer controlled_buffer_13
  assign dest = or_31_out ? 4'b1000 : 4'bz;  // Controlled_Buffer controlled_buffer_14
  assign dest = or_32_out ? 4'b0111 : 4'bz;  // Controlled_Buffer controlled_buffer_15
  assign dest = and_30_out ? 4'b1100 : 4'bz;  // Controlled_Buffer controlled_buffer_16
  assign dest = and_31_out ? 4'b1101 : 4'bz;  // Controlled_Buffer controlled_buffer_17
  assign dest = and_55_out ? 4'b1010 : 4'bz;  // Controlled_Buffer controlled_buffer_18
  assign dest = and_56_out ? 4'b1011 : 4'bz;  // Controlled_Buffer controlled_buffer_19
  assign dest = or_33_out ? 4'b0110 : 4'bz;  // Controlled_Buffer controlled_buffer_20
  assign dest = and_35_out ? {RPL, 1'b1} : 4'bz;  // Controlled_Buffer controlled_buffer_21
  assign dest = and_36_out ? {1'b0, inst[5:4], RPH[0]} : 4'bz;  // Controlled_Buffer controlled_buffer_22
  assign dest = or_34_out ? 4'b1111 : 4'bz;  // Controlled_Buffer controlled_buffer_23
  assign dest = or_35_out ? 4'b1110 : 4'bz;  // Controlled_Buffer controlled_buffer_24
  Multiplexer #(.width(3), .disabled(0), .enable("false")) multiplexer_1 (
    .in0(3'b111), .in1(inst[5:3]), .out(mode), .sel(and_60_out));
  nor nor_2 (AddselPC, AddselSP, AddselADDR, AddselHL);
  nor nor_3 (Restart, and_65_out, and_66_out, and_67_out, and_44_out);
  or or_37 (PCenable, phase0, and_68_out, and_69_out);
  or or_38 (wr_pch, and_70_out, and_45_out, and_46_out);
  or or_39 (wr_pcl, and_71_out, and_47_out, and_48_out);
  nor nor_4 (SPenable, and_72_out, and_73_out, and_74_out);
  or or_40 (SP_dir, and_75_out, and_76_out);

  // Other names for the same wires on the sheet: srclo[2:0] = inst[2:0]; destlo[2:0] = inst[5:3];
  //   mmm[2:0] = inst[5:3]; RPH[2:1] = inst[5:4]

  // Notes on the sheet:
  //   sel src
  //   sel acc
  //   sel L
  //   sel H
  //   sel RPH
  //   sel RPL
  //   sel T
  //   sel PCH
  //   sel PCL
  //   sel ADDRL
  //   sel ADDRH
  //   sel Mem
  //   sel T
  //   sel acc
  //   sel SPL
  //   sel SPL
  //   sel ADDRL
  //   sel ADDRH
  //   sel Mem
  //   sel RPL
  //   sel RPH
  //   sel PCH
  //   sel PCL
endmodule

module stack_pointer (
  input  [7:0] B_BUS,
  input  nenable,
  input  clock,
  input  nup_down,
  input  rdspl,
  input  rdsph,
  input  wr_spl,
  input  wr_sph,
  output [15:0] stack_pointer,
  output [7:0] A_BUS
);

  wire hc191_1_nrc, hc191_2_nrc, hc191_3_nrc, not_1_out, not_2_out;

  not not_1 (not_1_out, wr_spl);
  hc191 hc191_1 (
    .D0(B_BUS[0]), .D1(B_BUS[1]), .D2(B_BUS[2]), .D3(B_BUS[3]), .nPL(not_1_out), .nU_D(nup_down),
    .nCE(nenable), .CLK(clock), .Q0(stack_pointer[0]), .Q1(stack_pointer[1]), .Q2(stack_pointer[2]),
    .Q3(stack_pointer[3]), .nRC(hc191_1_nrc));  // open: TC
  hc191 hc191_2 (
    .D0(B_BUS[4]), .D1(B_BUS[5]), .D2(B_BUS[6]), .D3(B_BUS[7]), .nPL(not_1_out), .nU_D(nup_down),
    .nCE(hc191_1_nrc), .CLK(clock), .Q0(stack_pointer[4]), .Q1(stack_pointer[5]), .Q2(stack_pointer[6]),
    .Q3(stack_pointer[7]), .nRC(hc191_2_nrc));  // open: TC
  not not_2 (not_2_out, wr_sph);
  hc191 hc191_3 (
    .D0(B_BUS[0]), .D1(B_BUS[1]), .D2(B_BUS[2]), .D3(B_BUS[3]), .nPL(not_2_out), .nU_D(nup_down),
    .nCE(hc191_2_nrc), .CLK(clock), .Q0(stack_pointer[8]), .Q1(stack_pointer[9]), .Q2(stack_pointer[10]),
    .Q3(stack_pointer[11]), .nRC(hc191_3_nrc));  // open: TC
  hc191 hc191_4 (
    .D0(B_BUS[4]), .D1(B_BUS[5]), .D2(B_BUS[6]), .D3(B_BUS[7]), .nPL(not_2_out), .nU_D(nup_down),
    .nCE(hc191_3_nrc), .CLK(clock), .Q0(stack_pointer[12]), .Q1(stack_pointer[13]), .Q2(stack_pointer[14]),
    .Q3(stack_pointer[15]));  // open: TC, nRC
  assign A_BUS = rdspl ? stack_pointer[7:0] : 8'bz;  // Controlled_Buffer controlled_buffer_1
  assign A_BUS = rdsph ? stack_pointer[15:8] : 8'bz;  // Controlled_Buffer controlled_buffer_2
endmodule
