// Logisim project cisc-8.circ as structural Verilog: 13 circuits, main circuit main
module main (
  input  nreset,
  input  interrupt
);

  wire AddselADDR, AddselHL, AddselSP, and_1_out, and_2_out, carry_flag, carry_out, Clock, dest_acc,
       dest_addrh, dest_addrl, dest_b, dest_c, dest_d, dest_e, dest_flag, dest_h, dest_l, dest_mem, dest_pch,
       dest_pcl, dest_sph, dest_spl, dest_t, instruction_decode_3_1_inst_latch, multiplexer_1_out,
       multiplexer_3_out, multiplexer_4_out, nor_1_out, not_1_out, not_2_out, not_3_out, not_4_out,
       not_5_out, not_6_out, not_7_out, or_1_out, or_2_out, passthru, PCenable, phase0, Restart, SPdir,
       SPenable, src_00, src_08, src_acc, src_addrh, src_addrl, src_b, src_c, src_d, src_e, src_flag, src_h,
       src_l, src_mem, src_pch, src_pcl, src_sph, src_spl, src_t, wr_pch, wr_pcl, writereg, xnor_1_out,
       xnor_2_out, zero, zero_flag;
  wire [1:0] sel_addr;
  wire [2:0] hc163_1_q0, mode;
  wire [7:0] A_BUS, ACC_q, B_BUS, instruction_reg_q, ram_1_data, REG_B_q, REG_C_q, REG_D_q, REG_E_q, temp_q;
  wire [15:0] address, addrl_q, pc, REG_L_q, sp;

  // Probe on B_BUS
  Clock clock_1 (.out(Clock));
  not not_1 (not_1_out, dest_mem);
  assign A_BUS = src_b ? REG_B_q : 8'bz;  // Controlled_Buffer controlled_buffer_1
  Register REG_B (.D(B_BUS), .Q(REG_B_q), .clk(dest_b));  // open: en, clr
  RAM #(.addrWidth(16)) ram_1 (.addr(address), .data(ram_1_data), .clk(not_1_out), .ld(src_mem));  // open: sel, clr
  and and_1 (and_1_out, nreset, Restart);
  not not_2 (not_2_out, Clock);
  assign A_BUS = src_c ? REG_C_q : 8'bz;  // Controlled_Buffer controlled_buffer_2
  Register REG_C (.D(B_BUS), .Q(REG_C_q), .clk(dest_c));  // open: en, clr
  assign A_BUS = src_mem ? ram_1_data : 8'bz;  // Controlled_Buffer controlled_buffer_3
  assign ram_1_data = nor_1_out ? B_BUS : 8'bz;  // Controlled_Buffer controlled_buffer_4
  nor nor_1 (nor_1_out, src_mem, Clock);
  hc163 hc163_1 (
    .CET(1'b1), .CEP(1'b1), .PE(1'b1), .nMR(and_1_out), .Clock(not_2_out), .Q0(hc163_1_q0[0]),
    .Q1(hc163_1_q0[1]), .Q2(hc163_1_q0[2]));  // open: D0, D1, D2, D3, Q3, TC
  assign A_BUS = src_d ? REG_D_q : 8'bz;  // Controlled_Buffer controlled_buffer_5
  Register REG_D (.D(B_BUS), .Q(REG_D_q), .clk(dest_d));  // open: en, clr
  // Probe on hc163_1_q0
  assign A_BUS = src_e ? REG_E_q : 8'bz;  // Controlled_Buffer controlled_buffer_6
  Register REG_E (.D(B_BUS), .Q(REG_E_q), .clk(dest_e));  // open: en, clr
  assign A_BUS = src_h ? REG_L_q[15:8] : 8'bz;  // Controlled_Buffer controlled_buffer_7
  Register REG_L (.D(B_BUS), .Q(REG_L_q[7:0]), .clk(dest_l));  // open: en, clr
  Register REG_H (.D(B_BUS), .Q(REG_L_q[15:8]), .clk(dest_h));  // open: en, clr
  Register instruction_reg (
    .D(A_BUS), .Q(instruction_reg_q), .clk(instruction_decode_3_1_inst_latch));  // open: en, clr
  assign A_BUS = src_l ? REG_L_q[7:0] : 8'bz;  // Controlled_Buffer controlled_buffer_8
  assign A_BUS = src_acc ? ACC_q : 8'bz;  // Controlled_Buffer controlled_buffer_9
  Register ACC (.D(B_BUS), .Q(ACC_q), .clk(dest_acc));  // open: en, clr
  assign A_BUS = src_addrl ? addrl_q[7:0] : 8'bz;  // Controlled_Buffer controlled_buffer_10
  Register addrl (.D(B_BUS), .Q(addrl_q[7:0]), .clk(dest_addrl));  // open: en, clr
  assign A_BUS = src_addrh ? addrl_q[15:8] : 8'bz;  // Controlled_Buffer controlled_buffer_11
  Register addrh (.D(B_BUS), .Q(addrl_q[15:8]), .clk(dest_addrh));  // open: en, clr
  assign A_BUS = src_t ? temp_q : 8'bz;  // Controlled_Buffer controlled_buffer_12
  Register temp (.D(B_BUS), .Q(temp_q), .clk(dest_t));  // open: en, clr
  xnor xnor_1 (xnor_1_out, zero_flag, instruction_reg_q[3]);
  Multiplexer #(.disabled(0), .enable("false")) multiplexer_1 (
    .in0(xnor_1_out), .in1(xnor_2_out), .out(multiplexer_1_out), .sel(instruction_reg_q[4]));
  xnor xnor_2 (xnor_2_out, instruction_reg_q[3], carry_flag);
  instruction_decode_3 instruction_decode_3_1 (
    .cond_true(multiplexer_1_out), .inst(instruction_reg_q), .phase(hc163_1_q0), .phase0(phase0),
    .inst_latch(instruction_decode_3_1_inst_latch), .interrupt(interrupt), .nreset(nreset),
    .writereg(writereg), .clock(Clock), .dest_b(dest_b), .src_b(src_b), .dest_c(dest_c), .src_c(src_c),
    .dest_d(dest_d), .src_d(src_d), .dest_e(dest_e), .src_e(src_e), .dest_h(dest_h), .src_h(src_h),
    .dest_l(dest_l), .src_l(src_l), .dest_mem(dest_mem), .src_mem(src_mem), .dest_acc(dest_acc),
    .src_acc(src_acc), .dest_T(dest_t), .src_sph(src_sph), .src_flag(src_flag), .dest_SPL(dest_spl),
    .src_spl(src_spl), .dest_SPH(dest_sph), .src_T(src_t), .dest_ADDRL(dest_addrl), .src_PCH(src_pch),
    .dest_ADDRH(dest_addrh), .src_PCL(src_pcl), .src_ADDRL(src_addrl), .src_ADDRH(src_addrh),
    .dest_flag(dest_flag), .src_00(src_00), .src_08(src_08), .dest__PCH(dest_pch), .mode(mode),
    .dest__PCL(dest_pcl), .AddselHL(AddselHL), .AddselADDR(AddselADDR), .AddselSP(AddselSP),
    .Restart(Restart), .PCenable(PCenable), .wr_pch(wr_pch), .SPenable(SPenable), .wr_pcl(wr_pcl),
    .SP_dir(SPdir));
  Multiplexer #(.select(2), .width(16), .enable("false")) multiplexer_2 (
    .in0(REG_L_q), .in1(addrl_q), .in2(sp), .in3(pc), .out(address), .sel(sel_addr));
  // Probe on A_BUS
  cisc_8_alu ALU (
    .mode(mode), .Cin(carry_flag), .A(temp_q), .B(A_BUS), .out(B_BUS), .Cout(carry_out), .zero(zero),
    .Passthru(passthru));
  // Probe on address
  not not_3 (not_3_out, passthru);
  and and_2 (and_2_out, not_3_out, writereg);
  or or_1 (or_1_out, phase0, PCenable);
  not not_4 (not_4_out, AddselSP);
  and and_3 (sel_addr[0], not_4_out, not_5_out);
  not not_5 (not_5_out, AddselHL);
  not not_6 (not_6_out, AddselADDR);
  and and_4 (sel_addr[1], not_6_out, not_7_out);
  not not_7 (not_7_out, AddselHL);
  Multiplexer #(.disabled(0), .enable("false")) multiplexer_3 (
    .in0(carry_out), .in1(B_BUS[0]), .out(multiplexer_3_out), .sel(passthru));
  Multiplexer #(.disabled(0), .enable("false")) multiplexer_4 (
    .in0(zero), .in1(B_BUS[6]), .out(multiplexer_4_out), .sel(passthru));
  or or_2 (or_2_out, and_2_out, dest_flag);
  D_Flip_Flop Carry (.clk(or_2_out), .D(multiplexer_3_out), .Q(carry_flag));  // open: Qn, preset, en, reset
  D_Flip_Flop u_Zero (.clk(or_2_out), .D(multiplexer_4_out), .Q(zero_flag));  // open: Qn, preset, en, reset
  prog_counter Program_counter (
    .enable(or_1_out), .reset(nreset), .clock(Clock), .b_bus(B_BUS), .wr_pcl(wr_pcl), .wr_pch(wr_pch),
    .rdpcl(src_pcl), .rdpch(src_pch), .prog_count(pc), .writereg(A_BUS));
  // Probe on sp
  stack_pointer stack_pointer (
    .B_BUS(B_BUS), .nenable(SPenable), .clock(Clock), .nup_down(SPdir), .wr_spl(dest_spl), .wr_sph(dest_sph),
    .rd_spl(src_spl), .rd_sph(src_sph), .stack_pointer(sp), .A_BUS(A_BUS));
  // Probe on pc
  assign A_BUS = src_flag ? {1'b0, zero_flag, {5{1'b0}}, carry_flag} : 8'bz;  // Controlled_Buffer controlled_buffer_13

  // Other names for the same wires on the sheet: reset = nreset
endmodule

module cisc_8_alu (
  input  [7:0] A,
  input  [7:0] B,
  input  [2:0] mode,
  input  Cin,
  output [7:0] out,
  output Cout,
  output zero,
  output Passthru
);

  wire \and , decoder_2_out2, decoder_2_out5, decoder_2_out7, nor_1_out, nor_2_out, not_1_out, \or ,
       or_2_out, \xor ;
  wire [7:0] adder_1_out, and_1_out, multiplexer_1_out, or_1_out, xor_1_out;

  Decoder #(.select(3), .enable("false")) decoder_1 (
    .out4(\and ), .out5(\xor ), .out6(\or ), .out7(Passthru), .sel(mode));  // open: out0, out1, out2, out3
  not not_1 (not_1_out, mode[2]);
  assign and_1_out = A & B;  // AND_Gate and_1, 8 bits wide
  assign or_1_out = A | B;  // OR_Gate or_1, 8 bits wide
  Decoder #(.select(3), .disabled(0), .enable("false")) decoder_2 (
    .out2(decoder_2_out2), .out5(decoder_2_out5), .out7(decoder_2_out7), .sel({Cin, mode[1:0]}));  // open: out0, out1, out3, out4, out6
  Multiplexer #(.width(8), .enable("false")) multiplexer_1 (
    .in0({8{mode[1]}}), .in1(A), .out(multiplexer_1_out), .sel(\xor ));
  assign xor_1_out = multiplexer_1_out ^ B;  // XOR_Gate xor_1, 8 bits wide
  or or_2 (or_2_out, decoder_2_out2, decoder_2_out5, decoder_2_out7);
  assign out = Passthru ? B : 8'bz;  // Controlled_Buffer controlled_buffer_1
  assign out = \or  ? or_1_out : 8'bz;  // Controlled_Buffer controlled_buffer_2
  Adder adder_1 (.a(A), .b(xor_1_out), .out(adder_1_out), .cin(or_2_out), .cout(Cout));
  assign out = not_1_out ? adder_1_out : 8'bz;  // Controlled_Buffer controlled_buffer_3
  assign out = \xor  ? xor_1_out : 8'bz;  // Controlled_Buffer controlled_buffer_4
  assign out = \and  ? and_1_out : 8'bz;  // Controlled_Buffer controlled_buffer_5
  nor nor_1 (nor_1_out, out[0], out[1], out[2], out[3]);
  nor nor_2 (nor_2_out, out[4], out[5], out[6], out[7]);
  and and_2 (zero, nor_1_out, nor_2_out);

  // Other names for the same wires on the sheet: pass_b = Passthru

  // Notes on the sheet:
  //   Add
  //   Adc
  //   Sub
  //   Sbb
  //   And
  //   Xor
  //   Or
  //   passb
  //   Mode
  //   0 0 0
  //   0 0 0
  //   0 0 1
  //   0 1 0
  //   0 1 1
  //   1 0 0
  //   1 0 1
  //   1 1 0
  //   1 1 1
endmodule

module hc191 (
  input  D0,
  input  D1,
  input  D2,
  input  D3,
  input  nPL,
  input  nU_D,
  input  nCE,
  input  CLK,
  output Q0,
  output Q1,
  output Q2,
  output Q3,
  output TC,
  output nRC
);

  wire and_1_out, and_2_out, and_3_out, and_4_out, and_5_out, and_6_out, and_7_out, and_8_out, and_9_out,
       and_10_out, and_11_out, and_12_out, and_13_out, and_14_out, j_k_ff_1_qn, j_k_ff_2_qn, j_k_ff_3_qn,
       j_k_ff_4_qn, nand_2_out, nand_3_out, nand_4_out, nand_5_out, not_1_out, not_2_out, not_3_out,
       not_4_out, not_5_out, not_6_out, not_7_out, not_8_out, or_2_out, or_3_out, or_4_out;

  not not_1 (not_1_out, nPL);
  not not_2 (not_2_out, nU_D);
  not not_3 (not_3_out, nCE);
  not not_4 (not_4_out, CLK);
  and and_1 (and_1_out, not_2_out, not_3_out);
  and and_2 (and_2_out, not_3_out, nU_D);
  and and_3 (and_3_out, not_2_out, Q1, Q0, Q2, Q3);
  nand nand_1 (nRC, not_4_out, not_3_out, TC);
  and and_4 (and_4_out, nU_D, j_k_ff_1_qn, j_k_ff_2_qn, j_k_ff_3_qn, j_k_ff_4_qn);
  or or_1 (TC, and_3_out, and_4_out);
  nand nand_2 (nand_2_out, D0, not_1_out);
  not not_5 (not_5_out, nand_2_out);
  J_K_Flip_Flop j_k_ff_1 (
    .J(not_3_out), .clk(not_4_out), .K(not_3_out), .Q(Q0), .Qn(j_k_ff_1_qn), .preset(not_5_out),
    .reset(and_5_out));  // open: en
  nand nand_3 (nand_3_out, D1, not_1_out);
  and and_5 (and_5_out, nand_2_out, not_1_out);
  and and_6 (and_6_out, and_2_out, j_k_ff_1_qn);
  or or_2 (or_2_out, and_6_out, and_7_out);
  not not_6 (not_6_out, nand_3_out);
  and and_7 (and_7_out, Q0, and_1_out);
  and and_8 (and_8_out, nand_3_out, not_1_out);
  J_K_Flip_Flop j_k_ff_2 (
    .J(or_2_out), .clk(not_4_out), .K(or_2_out), .Q(Q1), .Qn(j_k_ff_2_qn), .preset(not_6_out),
    .reset(and_8_out));  // open: en
  and and_9 (and_9_out, and_2_out, j_k_ff_1_qn, j_k_ff_2_qn);
  nand nand_4 (nand_4_out, D2, not_1_out);
  not not_7 (not_7_out, nand_4_out);
  and and_10 (and_10_out, Q0, Q1, and_1_out);
  or or_3 (or_3_out, and_9_out, and_10_out);
  and and_11 (and_11_out, nand_4_out, not_1_out);
  J_K_Flip_Flop j_k_ff_3 (
    .J(or_3_out), .clk(not_4_out), .K(or_3_out), .Q(Q2), .Qn(j_k_ff_3_qn), .preset(not_7_out),
    .reset(and_11_out));  // open: en
  nand nand_5 (nand_5_out, D3, not_1_out);
  and and_12 (and_12_out, Q0, Q1, Q2, and_1_out);
  and and_13 (and_13_out, and_2_out, j_k_ff_1_qn, j_k_ff_2_qn, j_k_ff_3_qn);
  or or_4 (or_4_out, and_13_out, and_12_out);
  J_K_Flip_Flop j_k_ff_4 (
    .J(or_4_out), .clk(not_4_out), .K(or_4_out), .Q(Q3), .Qn(j_k_ff_4_qn), .preset(not_8_out),
    .reset(and_14_out));  // open: en
  not not_8 (not_8_out, nand_5_out);
  and and_14 (and_14_out, nand_5_out, not_1_out);
endmodule

module hc163 (
  input  D0,
  input  D1,
  input  D2,
  input  D3,
  input  CET,
  input  CEP,
  input  PE,
  input  nMR,
  input  Clock,
  output Q0,
  output Q1,
  output Q2,
  output Q3,
  output TC
);

  wire and_1_out, and_2_out, and_3_out, and_4_out, and_5_out, and_6_out, and_7_out, and_8_out, and_9_out,
       d_ff_1_q, d_ff_1_qn, d_ff_2_q, d_ff_2_qn, d_ff_3_q, d_ff_3_qn, d_ff_4_q, d_ff_4_qn, nand_1_out,
       nand_2_out, nor_1_out, nor_2_out, nor_3_out, nor_4_out, nor_5_out, nor_6_out, not_1_out, not_2_out,
       or_1_out, or_2_out, or_3_out, or_4_out, or_5_out, xnor_1_out, xnor_2_out, xnor_3_out;

  nand nand_1 (nand_1_out, CET, CEP);
  nor nor_1 (nor_1_out, PE, not_1_out);
  not not_1 (not_1_out, nMR);
  nor nor_2 (nor_2_out, nor_1_out, not_1_out);
  not not_2 (not_2_out, nand_1_out);
  xnor xnor_1 (xnor_1_out, not_2_out, d_ff_1_qn);
  and and_1 (and_1_out, D0, nor_1_out);
  or or_1 (or_1_out, and_1_out, and_2_out);
  and and_2 (and_2_out, xnor_1_out, nor_2_out);
  D_Flip_Flop d_ff_1 (.clk(Clock), .D(or_1_out), .Q(d_ff_1_q), .Qn(d_ff_1_qn));  // open: preset, en, reset
  not not_3 (Q0, d_ff_1_qn);
  nor nor_3 (nor_3_out, nand_1_out, d_ff_1_qn);
  and and_3 (and_3_out, D1, nor_1_out);
  or or_2 (or_2_out, and_3_out, and_4_out);
  xnor xnor_2 (xnor_2_out, nor_3_out, d_ff_2_qn);
  and and_4 (and_4_out, xnor_2_out, nor_2_out);
  D_Flip_Flop d_ff_2 (.clk(Clock), .D(or_2_out), .Q(d_ff_2_q), .Qn(d_ff_2_qn));  // open: preset, en, reset
  not not_4 (Q1, d_ff_2_qn);
  nor nor_4 (nor_4_out, nand_1_out, d_ff_1_qn, d_ff_2_qn);
  xnor xnor_3 (xnor_3_out, nor_4_out, d_ff_3_qn);
  and and_5 (and_5_out, D2, nor_1_out);
  or or_3 (or_3_out, and_5_out, and_6_out);
  and and_6 (and_6_out, xnor_3_out, nor_2_out);
  D_Flip_Flop d_ff_3 (.clk(Clock), .D(or_3_out), .Q(d_ff_3_q), .Qn(d_ff_3_qn));  // open: preset, en, reset
  not not_5 (Q2, d_ff_3_qn);
  nor nor_5 (nor_5_out, nand_1_out, d_ff_1_qn, d_ff_2_qn, d_ff_3_qn);
  and and_7 (and_7_out, D3, nor_1_out);
  or or_4 (or_4_out, and_7_out, and_9_out);
  and and_8 (and_8_out, nor_5_out, d_ff_4_qn);
  nor nor_6 (nor_6_out, nor_5_out, d_ff_4_qn);
  or or_5 (or_5_out, and_8_out, nor_6_out);
  and and_9 (and_9_out, nor_2_out, or_5_out);
  D_Flip_Flop d_ff_4 (.clk(Clock), .D(or_4_out), .Q(d_ff_4_q), .Qn(d_ff_4_qn));  // open: preset, en, reset
  not not_6 (Q3, d_ff_4_qn);
  nand nand_2 (nand_2_out, d_ff_4_q, d_ff_3_q, d_ff_2_q, d_ff_1_q, CET);
  not not_7 (TC, nand_2_out);
endmodule

module _8_bit_up_count_w_preset (
  input  [7:0] D,
  input  CEP_T,
  input  nPE,
  input  nMR,
  input  CP,
  output [7:0] Q,
  output TC
);

  wire hc163_1_tc;

  hc163 hc163_1 (
    .D0(D[0]), .D1(D[1]), .D2(D[2]), .D3(D[3]), .CET(CEP_T), .CEP(CEP_T), .PE(nPE), .nMR(nMR), .Clock(CP),
    .Q0(Q[0]), .Q1(Q[1]), .Q2(Q[2]), .Q3(Q[3]), .TC(hc163_1_tc));
  hc163 hc163_2 (
    .D0(D[4]), .D1(D[5]), .D2(D[6]), .D3(D[7]), .CET(hc163_1_tc), .CEP(hc163_1_tc), .PE(nPE), .nMR(nMR),
    .Clock(CP), .Q0(Q[4]), .Q1(Q[5]), .Q2(Q[6]), .Q3(Q[7]), .TC(TC));
endmodule

module prog_counter (
  input  enable,
  input  reset,
  input  clock,
  input  [7:0] b_bus,
  input  wr_pcl,
  input  wr_pch,
  input  rdpcl,
  input  rdpch,
  output [15:0] prog_count,
  output [7:0] writereg
);

  wire hc163_1_tc, hc163_2_tc, hc163_3_tc, not_1_out, not_2_out;

  hc163 hc163_1 (
    .D0(b_bus[0]), .D1(b_bus[1]), .D2(b_bus[2]), .D3(b_bus[3]), .CET(enable), .CEP(enable), .PE(not_1_out),
    .nMR(reset), .Clock(clock), .Q0(prog_count[0]), .Q1(prog_count[1]), .Q2(prog_count[2]),
    .Q3(prog_count[3]), .TC(hc163_1_tc));
  not not_1 (not_1_out, wr_pcl);
  hc163 hc163_2 (
    .D0(b_bus[4]), .D1(b_bus[5]), .D2(b_bus[6]), .D3(b_bus[7]), .CET(hc163_1_tc), .CEP(hc163_1_tc),
    .PE(not_1_out), .nMR(reset), .Clock(clock), .Q0(prog_count[4]), .Q1(prog_count[5]), .Q2(prog_count[6]),
    .Q3(prog_count[7]), .TC(hc163_2_tc));
  hc163 hc163_3 (
    .D0(b_bus[0]), .D1(b_bus[1]), .D2(b_bus[2]), .D3(b_bus[3]), .CET(hc163_2_tc), .CEP(hc163_2_tc),
    .PE(not_2_out), .nMR(reset), .Clock(clock), .Q0(prog_count[8]), .Q1(prog_count[9]), .Q2(prog_count[10]),
    .Q3(prog_count[11]), .TC(hc163_3_tc));
  not not_2 (not_2_out, wr_pch);
  hc163 hc163_4 (
    .D0(b_bus[4]), .D1(b_bus[5]), .D2(b_bus[6]), .D3(b_bus[7]), .CET(hc163_3_tc), .CEP(hc163_3_tc),
    .PE(not_2_out), .nMR(reset), .Clock(clock), .Q0(prog_count[12]), .Q1(prog_count[13]),
    .Q2(prog_count[14]), .Q3(prog_count[15]));  // open: TC
  assign writereg = rdpch ? prog_count[15:8] : 8'bz;  // Controlled_Buffer controlled_buffer_1
  assign writereg = rdpcl ? prog_count[7:0] : 8'bz;  // Controlled_Buffer controlled_buffer_2
endmodule

module stack_pointer (
  input  [7:0] B_BUS,
  input  nenable,
  input  clock,
  input  nup_down,
  input  wr_spl,
  input  wr_sph,
  input  rd_spl,
  input  rd_sph,
  output [15:0] stack_pointer,
  output [7:0] A_BUS
);

  wire hc191_1_nrc, hc191_2_nrc, hc191_3_nrc, not_1_out, not_2_out;

  not not_1 (not_1_out, wr_spl);
  hc191 hc191_1 (
    .D0(B_BUS[0]), .D1(B_BUS[1]), .D2(B_BUS[2]), .D3(B_BUS[3]), .nPL(not_1_out), .nU_D(nup_down),
    .nCE(nenable), .CLK(clock), .Q0(stack_pointer[0]), .Q1(stack_pointer[1]), .Q2(stack_pointer[2]),
    .Q3(stack_pointer[3]), .nRC(hc191_1_nrc));  // open: TC
  hc191 hc191_2 (
    .D0(B_BUS[4]), .D1(B_BUS[5]), .D2(B_BUS[6]), .D3(B_BUS[7]), .nPL(not_1_out), .nU_D(nup_down),
    .nCE(hc191_1_nrc), .CLK(clock), .Q0(stack_pointer[4]), .Q1(stack_pointer[5]), .Q2(stack_pointer[6]),
    .Q3(stack_pointer[7]), .nRC(hc191_2_nrc));  // open: TC
  not not_2 (not_2_out, wr_sph);
  hc191 hc191_3 (
    .D0(B_BUS[0]), .D1(B_BUS[1]), .D2(B_BUS[2]), .D3(B_BUS[3]), .nPL(not_2_out), .nU_D(nup_down),
    .nCE(hc191_2_nrc), .CLK(clock), .Q0(stack_pointer[8]), .Q1(stack_pointer[9]), .Q2(stack_pointer[10]),
    .Q3(stack_pointer[11]), .nRC(hc191_3_nrc));  // open: TC
  hc191 hc191_4 (
    .D0(B_BUS[4]), .D1(B_BUS[5]), .D2(B_BUS[6]), .D3(B_BUS[7]), .nPL(not_2_out), .nU_D(nup_down),
    .nCE(hc191_3_nrc), .CLK(clock), .Q0(stack_pointer[12]), .Q1(stack_pointer[13]), .Q2(stack_pointer[14]),
    .Q3(stack_pointer[15]));  // open: TC, nRC
  assign A_BUS = rd_spl ? stack_pointer[7:0] : 8'bz;  // Controlled_Buffer controlled_buffer_1
  assign A_BUS = rd_sph ? stack_pointer[15:8] : 8'bz;  // Controlled_Buffer controlled_buffer_2
endmodule

module instruction_decode_3 (
  input  cond_true,
  input  [7:0] inst,
  input  [2:0] phase,
  input  interrupt,
  input  nreset,
  input  clock,
  output dest_b,
  output src_b,
  output dest_c,
  output src_c,
  output dest_d,
  output src_d,
  output dest_e,
  output src_e,
  output dest_h,
  output phase0,
  output src_h,
  output dest_l,
  output src_l,
  output dest_mem,
  output src_mem,
  output dest_acc,
  output src_acc,
  output dest_T,
  output src_sph,
  output inst_latch,
  output src_flag,
  output dest_SPL,
  output src_spl,
  output dest_SPH,
  output src_T,
  output dest_ADDRL,
  output src_PCH,
  output dest_ADDRH,
  output src_PCL,
  output src_ADDRL,
  output src_ADDRH,
  output dest_flag,
  output src_00,
  output src_08,
  output dest__PCH,
  output [2:0] mode,
  output dest__PCL,
  output AddselHL,
  output AddselADDR,
  output AddselSP,
  output writereg,
  output Restart,
  output PCenable,
  output wr_pch,
  output SPenable,
  output wr_pcl,
  output SP_dir
);

  wire and_2_out, and_3_out, and_4_out, and_5_out, and_6_out, and_7_out, and_8_out, and_9_out, and_10_out,
       and_11_out, and_12_out, and_13_out, and_14_out, and_15_out, and_16_out, and_17_out, and_18_out,
       and_19_out, and_20_out, and_23_out, and_24_out, and_25_out, and_26_out, and_27_out, and_28_out,
       and_29_out, and_31_out, and_33_out, and_35_out, and_36_out, and_37_out, and_39_out, and_40_out,
       and_41_out, and_42_out, and_43_out, and_44_out, and_47_out, and_60_out, and_61_out, and_62_out,
       and_63_out, and_64_out, and_65_out, and_66_out, and_67_out, and_68_out, and_69_out, and_70_out,
       and_71_out, and_72_out, and_73_out, and_74_out, and_75_out, and_76_out, and_77_out, and_78_out,
       and_80_out, and_81_out, and_82_out, and_83_out, and_84_out, and_85_out, and_86_out, and_87_out,
       and_88_out, and_90_out, and_91_out, and_92_out, and_93_out, and_94_out, and_95_out, and_96_out,
       and_97_out, and_98_out, and_99_out, and_100_out, and_101_out, and_102_out, and_103_out, call,
       d_ff_1_q, dad, decoder_1_out1, decoder_1_out2, decoder_1_out3, decoder_1_out5, decoder_1_out6,
       decoder_2_out1, decoder_2_out6, decoder_2_out7, decoder_3_out0, decoder_3_out3, decoder_5_out0,
       decoder_5_out1, decoder_5_out2, decoder_5_out3, decoder_5_out4, decoder_5_out5, decoder_5_out6,
       decoder_5_out7, decoder_6_out0, decoder_6_out1, decoder_6_out2, decoder_6_out3, decoder_7_out0,
       decoder_7_out1, decoder_7_out2, decoder_7_out3, decoder_8_out0, decoder_8_out1, decoder_8_out2,
       decoder_8_out3, decoder_9_out0, decoder_9_out1, decoder_9_out2, decoder_9_out3, decoder_9_out4,
       decoder_9_out5, decoder_9_out6, decoder_9_out7, decoder_10_out0, decoder_10_out1, decoder_10_out2,
       decoder_10_out3, \int , jc, jmp, jnc, lda, lri, lxi, maths, mlimm, mov, mov16, nor_1_out, not_1_out,
       not_2_out, not_3_out, not_4_out, or_1_out, or_2_out, or_3_out, or_4_out, or_5_out, or_6_out, or_7_out,
       or_8_out, or_9_out, or_10_out, or_11_out, or_12_out, or_13_out, or_14_out, or_15_out, or_16_out,
       or_21_out, or_23_out, or_24_out, or_37_out, or_38_out, or_39_out, or_40_out, or_41_out, or_42_out,
       or_43_out, or_44_out, or_45_out, or_46_out, or_47_out, or_48_out, or_49_out, or_50_out, or_51_out,
       or_52_out, or_53_out, or_54_out, or_55_out, or_56_out, or_57_out, or_58_out, or_59_out, or_60_out,
       or_61_out, or_62_out, or_64_out, or_65_out, or_66_out, or_67_out, or_68_out, or_69_out, or_70_out,
       or_71_out, or_72_out, or_73_out, phase1, phase2, phase3, phase4, phase5, phase6, pop, push, ret, sta;
  wire [2:0] multiplexer_1_out, multiplexer_2_out;

  Decoder #(.select(3), .disabled(0)) decoder_1 (
    .out1(decoder_1_out1), .out2(decoder_1_out2), .out3(decoder_1_out3), .out5(decoder_1_out5),
    .out6(decoder_1_out6), .sel(inst[2:0]), .en(d_ff_1_q));  // open: out0, out4, out7
  Decoder #(.select(3), .disabled(0)) decoder_2 (
    .out1(decoder_2_out1), .out6(decoder_2_out6), .out7(decoder_2_out7), .sel(inst[5:3]), .en(d_ff_1_q));  // open: out0, out2, out3, out4, out5
  D_Flip_Flop d_ff_1 (.clk(phase0), .D(interrupt), .Q(d_ff_1_q), .Qn(\int ), .preset(not_1_out));  // open: en, reset
  not not_1 (not_1_out, nreset);
  not not_2 (not_2_out, inst[3]);
  and and_1 (inst_latch, phase0, clock);
  Decoder #(.select(2), .disabled(0)) decoder_3 (
    .out0(decoder_3_out0), .out1(mov), .out2(maths), .out3(decoder_3_out3), .sel(inst[7:6]), .en(d_ff_1_q));
  not not_3 (not_3_out, cond_true);
  Decoder #(.select(3), .disabled(0), .enable("false")) decoder_4 (
    .out0(phase0), .out1(phase1), .out2(phase2), .out3(phase3), .out4(phase4), .out5(phase5), .out6(phase6),
    .sel(phase));  // open: out7
  and and_2 (and_2_out, phase1, mov);
  and and_3 (and_3_out, phase2, maths);
  or or_1 (or_1_out, maths, mlimm);
  and and_4 (and_4_out, phase3, sta);
  and and_5 (and_5_out, phase1, dad);
  and and_6 (and_6_out, phase1, mov16);
  and and_7 (and_7_out, phase3, dad);
  and and_8 (and_8_out, phase2, mov16);
  and and_9 (and_9_out, phase1, push);
  and and_10 (and_10_out, phase4, dad);
  and and_11 (and_11_out, phase2, push);
  and and_12 (and_12_out, phase2, dad);
  or or_2 (or_2_out, jmp, jc);
  and and_13 (and_13_out, phase3, call);
  and and_14 (and_14_out, phase0, \int );
  and and_15 (and_15_out, phase4, call);
  and and_16 (and_16_out, phase1, \int );
  and and_17 (and_17_out, phase3, lxi);
  and and_18 (and_18_out, phase5, call);
  and and_19 (and_19_out, phase6, call);
  and and_20 (and_20_out, phase4, lxi);
  and and_21 (src_00, phase2, \int );
  and and_22 (src_08, phase3, \int );
  and and_23 (and_23_out, phase2, dad);
  and and_24 (and_24_out, phase4, dad);
  or or_3 (or_3_out, maths, mlimm);
  and and_25 (and_25_out, phase1, mov);
  and and_26 (and_26_out, phase2, maths);
  or or_4 (or_4_out, lda, sta);
  or or_5 (or_5_out, push, pop, ret);
  or or_6 (or_6_out, pop, call, ret);
  and and_27 (and_27_out, phase4, call);
  or or_7 (or_7_out, mlimm, lxi, lda, sta, jnc, call);
  or or_8 (or_8_out, jmp, jc);
  and and_28 (and_28_out, phase6, call);
  or or_9 (or_9_out, ret, \int );
  or or_10 (or_10_out, jmp, jc);
  and and_29 (and_29_out, phase5, call);
  or or_11 (or_11_out, ret, \int );
  and and_30 (mlimm, decoder_3_out3, decoder_1_out6);
  or or_12 (or_12_out, and_2_out, and_3_out);
  and and_31 (and_31_out, phase1, or_1_out);
  or or_13 (or_13_out, and_5_out, and_6_out);
  or or_14 (or_14_out, and_7_out, and_8_out);
  or or_15 (or_15_out, and_9_out, and_10_out);
  or or_16 (or_16_out, and_11_out, and_12_out);
  and and_32 (src_T, phase3, or_2_out);
  or or_17 (src_PCH, and_13_out, and_14_out);
  or or_18 (src_PCL, and_15_out, and_16_out);
  or or_19 (src_ADDRL, and_17_out, and_18_out);
  or or_20 (src_ADDRH, and_19_out, and_20_out);
  Multiplexer #(.width(3), .disabled(0), .enable("false")) multiplexer_1 (
    .in0(3'b001), .in1(3'b000), .out(multiplexer_1_out), .sel(and_23_out));
  or or_21 (or_21_out, and_23_out, and_24_out);
  and and_33 (and_33_out, phase2, or_3_out);
  or or_22 (AddselHL, and_25_out, and_26_out);
  and and_34 (AddselADDR, phase2, or_4_out);
  and and_35 (and_35_out, phase1, or_5_out);
  and and_36 (and_36_out, or_5_out, phase2);
  and and_37 (and_37_out, phase3, or_6_out);
  or or_23 (or_23_out, lxi, lda, sta, lri, jmp, jc, jnc, call);
  and and_38 (mov16, decoder_3_out3, decoder_2_out7, decoder_1_out1);
  or or_24 (or_24_out, and_31_out, and_4_out);
  nor nor_1 (nor_1_out, src_00, src_ADDRH, src_ADDRL, src_PCL, src_PCH, src_T, or_16_out, or_15_out, or_14_out, or_13_out, or_24_out, or_12_out, src_08);
  Multiplexer #(.width(3), .disabled(0), .enable("false")) multiplexer_2 (
    .in0(3'b111), .in1(multiplexer_1_out), .out(multiplexer_2_out), .sel(or_21_out));
  and and_39 (and_39_out, phase1, or_23_out);
  and and_40 (and_40_out, phase2, or_7_out);
  and and_41 (and_41_out, phase2, or_8_out);
  and and_42 (and_42_out, phase3, or_9_out);
  and and_43 (and_43_out, phase3, or_10_out);
  and and_44 (and_44_out, phase2, or_11_out);
  and and_45 (dad, decoder_3_out0, inst[3], decoder_1_out1);
  Decoder #(.select(3), .disabled(0)) decoder_5 (
    .out0(decoder_5_out0), .out1(decoder_5_out1), .out2(decoder_5_out2), .out3(decoder_5_out3),
    .out4(decoder_5_out4), .out5(decoder_5_out5), .out6(decoder_5_out6), .out7(decoder_5_out7),
    .sel(inst[2:0]), .en(or_12_out));
  Decoder #(.select(2), .disabled(0)) decoder_6 (
    .out0(decoder_6_out0), .out1(decoder_6_out1), .out2(decoder_6_out2), .out3(decoder_6_out3),
    .sel(inst[5:4]), .en(or_15_out));
  Multiplexer #(.width(3), .disabled(0), .enable("false")) multiplexer_3 (
    .in0(multiplexer_2_out), .in1(inst[5:3]), .out(mode), .sel(and_33_out));
  or or_25 (AddselSP, and_35_out, and_36_out, and_37_out, and_27_out);
  or or_26 (PCenable, phase0, and_39_out, and_40_out);
  or or_27 (wr_pch, and_41_out, and_28_out, and_42_out);
  or or_28 (wr_pcl, and_43_out, and_29_out, and_44_out);
  and and_46 (lxi, decoder_3_out0, not_2_out, decoder_1_out1);
  and and_47 (and_47_out, decoder_6_out3, and_9_out);
  and and_48 (src_sph, decoder_6_out3, and_10_out);
  Decoder #(.select(2), .disabled(0)) decoder_7 (
    .out0(decoder_7_out0), .out1(decoder_7_out1), .out2(decoder_7_out2), .out3(decoder_7_out3),
    .sel(inst[5:4]), .en(or_16_out));
  and and_49 (lda, decoder_3_out0, decoder_2_out7, decoder_1_out2);
  and and_50 (src_flag, decoder_7_out3, and_11_out);
  and and_51 (src_spl, decoder_7_out3, or_16_out);
  and and_52 (sta, decoder_3_out0, decoder_2_out6, decoder_1_out2);
  or or_29 (src_b, decoder_5_out0, decoder_6_out0);
  or or_30 (src_c, decoder_5_out1, decoder_7_out0);
  or or_31 (src_d, decoder_5_out2, decoder_6_out1);
  or or_32 (src_e, decoder_5_out3, decoder_7_out1);
  or or_33 (src_h, decoder_5_out4, decoder_6_out2, or_14_out);
  or or_34 (src_l, decoder_5_out5, decoder_7_out2, or_13_out);
  or or_35 (src_mem, decoder_5_out6, nor_1_out);
  or or_36 (src_acc, decoder_5_out7, and_47_out, or_24_out);
  and and_53 (lri, decoder_3_out0, decoder_1_out6);
  and and_54 (push, decoder_3_out3, not_2_out, decoder_1_out5);
  and and_55 (pop, decoder_3_out3, not_2_out, decoder_1_out1);
  and and_56 (jmp, decoder_3_out3, not_2_out, decoder_1_out3);
  and and_57 (jnc, decoder_3_out3, decoder_1_out2, not_3_out);
  and and_58 (jc, decoder_3_out3, decoder_1_out2, cond_true);
  and and_59 (call, decoder_3_out3, decoder_2_out1, decoder_1_out5);
  or or_37 (or_37_out, lri, mov);
  or or_38 (or_38_out, maths, mlimm, dad, pop, jmp, jc, jnc);
  and and_60 (and_60_out, phase2, jnc);
  and and_61 (and_61_out, phase3, dad);
  or or_39 (or_39_out, maths, mlimm);
  and and_62 (and_62_out, phase3, lda);
  and and_63 (and_63_out, phase1, mov16);
  and and_64 (and_64_out, phase2, mov16);
  or or_40 (or_40_out, lda, sta, call, lxi);
  or or_41 (or_41_out, lda, sta, call, lxi);
  and and_65 (and_65_out, phase1, push);
  and and_66 (and_66_out, phase2, push);
  or or_42 (or_42_out, sta, call);
  and and_67 (and_67_out, phase4, call);
  or or_43 (or_43_out, phase0, phase1);
  and and_68 (and_68_out, phase3, lxi);
  and and_69 (and_69_out, phase2, pop);
  and and_70 (and_70_out, phase4, lxi);
  and and_71 (and_71_out, phase3, pop);
  and and_72 (and_72_out, phase1, ret);
  or or_44 (or_44_out, jmp, jc, ret, \int );
  and and_73 (and_73_out, phase6, call);
  or or_45 (or_45_out, jmp, jc, ret, \int );
  and and_74 (and_74_out, phase5, call);
  and and_75 (and_75_out, phase4, dad);
  and and_76 (and_76_out, phase2, dad);
  not not_4 (not_4_out, phase0);
  or or_46 (or_46_out, mov, lri);
  or or_47 (or_47_out, maths, mlimm, mov16, push, jnc);
  or or_48 (or_48_out, lda, sta, pop, jmp, jc, ret, \int );
  or or_49 (or_49_out, dad, lxi);
  and and_77 (and_77_out, phase6, call);
  and and_78 (and_78_out, phase0, \int );
  or or_50 (or_50_out, push, pop, ret, \int );
  or or_51 (or_51_out, push, pop, ret);
  or or_52 (or_52_out, phase3, phase4);
  or or_53 (or_53_out, phase1, phase2);
  or or_54 (or_54_out, phase3, phase4);
  or or_55 (or_55_out, phase0, phase1);
  and and_79 (ret, decoder_3_out3, decoder_2_out1, decoder_1_out1);
  and and_80 (and_80_out, phase1, or_37_out);
  and and_81 (and_81_out, phase1, or_38_out);
  and and_82 (and_82_out, phase2, or_39_out);
  and and_83 (and_83_out, phase1, or_40_out);
  and and_84 (and_84_out, phase2, or_41_out);
  and and_85 (and_85_out, phase3, or_42_out);
  and and_86 (and_86_out, or_43_out, \int );
  or or_56 (or_56_out, and_68_out, and_69_out);
  or or_57 (or_57_out, and_70_out, and_71_out);
  and and_87 (and_87_out, phase2, or_44_out);
  and and_88 (and_88_out, phase3, or_45_out);
  and and_89 (writereg, not_4_out, clock);
  and and_90 (and_90_out, phase1, or_46_out);
  and and_91 (and_91_out, phase2, or_47_out);
  and and_92 (and_92_out, phase3, or_48_out);
  and and_93 (and_93_out, phase4, or_49_out);
  and and_94 (and_94_out, phase1, or_50_out);
  and and_95 (and_95_out, phase2, or_51_out);
  and and_96 (and_96_out, call, or_52_out);
  and and_97 (and_97_out, push, or_53_out);
  and and_98 (and_98_out, call, or_54_out);
  and and_99 (and_99_out, \int , or_55_out);
  or or_58 (or_58_out, and_81_out, and_60_out, and_61_out);
  or or_59 (or_59_out, and_82_out, and_62_out);
  or or_60 (or_60_out, and_65_out, and_66_out, and_85_out, and_67_out, and_86_out);
  or or_61 (or_61_out, and_72_out, and_87_out, and_73_out);
  or or_62 (or_62_out, and_88_out, and_74_out);
  Decoder #(.select(2), .disabled(0)) decoder_8 (
    .out0(decoder_8_out0), .out1(decoder_8_out1), .out2(decoder_8_out2), .out3(decoder_8_out3),
    .sel(inst[5:4]), .en(or_57_out));
  nor nor_2 (Restart, and_90_out, and_91_out, and_92_out, and_93_out, and_77_out);
  nor nor_3 (SPenable, and_78_out, and_94_out, and_95_out, and_96_out);
  or or_63 (SP_dir, and_97_out, and_98_out, and_99_out);
  Decoder #(.select(3), .disabled(0)) decoder_9 (
    .out0(decoder_9_out0), .out1(decoder_9_out1), .out2(decoder_9_out2), .out3(decoder_9_out3),
    .out4(decoder_9_out4), .out5(decoder_9_out5), .out6(decoder_9_out6), .out7(decoder_9_out7),
    .sel(inst[5:3]), .en(and_80_out));
  Decoder #(.select(2), .disabled(0)) decoder_10 (
    .out0(decoder_10_out0), .out1(decoder_10_out1), .out2(decoder_10_out2), .out3(decoder_10_out3),
    .sel(inst[5:4]), .en(or_56_out));
  and and_100 (and_100_out, decoder_8_out3, and_71_out);
  and and_101 (and_101_out, decoder_8_out3, and_70_out);
  and and_102 (and_102_out, decoder_10_out3, and_69_out);
  and and_103 (and_103_out, decoder_10_out3, and_68_out);
  or or_64 (or_64_out, decoder_9_out0, decoder_8_out0);
  or or_65 (or_65_out, decoder_9_out1, decoder_10_out0);
  or or_66 (or_66_out, decoder_9_out2, decoder_8_out1);
  or or_67 (or_67_out, decoder_9_out3, decoder_10_out1);
  or or_68 (or_68_out, decoder_9_out4, and_75_out, decoder_8_out2);
  or or_69 (or_69_out, decoder_9_out5, and_76_out, decoder_10_out2);
  or or_70 (or_70_out, decoder_9_out6, or_60_out);
  or or_71 (or_71_out, decoder_9_out7, and_100_out, or_59_out);
  or or_72 (or_72_out, and_63_out, and_103_out);
  or or_73 (or_73_out, and_64_out, and_101_out);
  and and_104 (dest_b, or_64_out, writereg);
  and and_105 (dest_c, or_65_out, writereg);
  and and_106 (dest_d, or_66_out, writereg);
  and and_107 (dest_e, or_67_out, writereg);
  and and_108 (dest_h, or_68_out, writereg);
  and and_109 (dest_l, or_69_out, writereg);
  and and_110 (dest_mem, or_70_out, writereg);
  and and_111 (dest_acc, or_71_out, writereg);
  and and_112 (dest_T, or_58_out, writereg);
  and and_113 (dest_SPL, or_72_out, writereg);
  and and_114 (dest_SPH, or_73_out, writereg);
  and and_115 (dest_ADDRL, and_83_out, writereg);
  and and_116 (dest_ADDRH, and_84_out, writereg);
  and and_117 (dest_flag, and_102_out, writereg);
  and and_118 (dest__PCH, or_61_out, writereg);
  and and_119 (dest__PCL, or_62_out, writereg);

  // Other names for the same wires on the sheet: destlo[2:0] = inst[5:3]; mmm[2:0] = inst[5:3]; rp[1:0] = inst[5:4];
  //   srclo[2:0] = inst[2:0]
endmodule

module stack_pointer_2 (
  input  nu_d,
  input  wr_Spl,
  input  wr_sph
);

  wire or_1_out;
  wire [7:0] B_BUS, multiplexer_1_out, multiplexer_2_out, register_1_q, register_2_q;
  wire [15:0] adder_1_out, multiplexer_3_out;

  Multiplexer #(.width(8), .disabled(0), .enable("false")) multiplexer_1 (
    .in0(adder_1_out[7:0]), .in1(B_BUS), .out(multiplexer_1_out), .sel(or_1_out));
  Multiplexer #(.width(8), .disabled(0), .enable("false")) multiplexer_2 (
    .in0(adder_1_out[15:8]), .in1(B_BUS), .out(multiplexer_2_out), .sel(or_1_out));
  or or_1 (or_1_out, wr_Spl, wr_sph);
  Register register_1 (.D(multiplexer_1_out), .Q(register_1_q), .clk(wr_Spl));  // open: en, clr
  Register register_2 (.D(multiplexer_2_out), .Q(register_2_q), .clk(wr_sph));  // open: en, clr
  Multiplexer #(.width(16), .disabled(0), .enable("false")) multiplexer_3 (
    .in0(16'h1), .in1({16{1'b1}}), .out(multiplexer_3_out), .sel(nu_d));
  Adder #(.width(16)) adder_1 (
    .a(multiplexer_3_out), .b({register_2_q, register_1_q}), .out(adder_1_out));  // open: cin, cout
endmodule

module single_bus (
);

  wire [7:0] A_q, ALU_out, Temp_q;

  Register A (.D(A_q), .Q(A_q));  // open: en, clk, clr
  Register B (.D(A_q), .Q(A_q));  // open: en, clk, clr
  Register C (.D(A_q), .Q(A_q));  // open: en, clk, clr
  Register Temp (.D(A_q), .Q(Temp_q));  // open: en, clk, clr
  cisc_8_alu ALU (.A(Temp_q), .B(A_q), .out(ALU_out));  // open: mode, Cin, Cout, zero, Passthru
  Register Acc (.D(ALU_out), .Q(A_q));  // open: en, clk, clr

  // Notes on the sheet:
  //   Databus A
endmodule

module alu_2 (
  input  [7:0] A,
  input  [7:0] B,
  input  [2:0] mode,
  input  Cin,
  output [7:0] out,
  output Cout,
  output zero,
  output Passthru
);

  wire \and , decoder_2_out2, decoder_2_out5, decoder_2_out7, nor_1_out, nor_2_out, not_1_out, \or ,
       or_2_out, \xor ;
  wire [7:0] adder_1_out, and_1_out, multiplexer_1_out, or_1_out, xor_1_out;

  Decoder #(.select(3), .enable("false")) decoder_1 (
    .out4(\and ), .out5(\xor ), .out6(\or ), .out7(Passthru), .sel(mode));  // open: out0, out1, out2, out3
  not not_1 (not_1_out, mode[2]);
  assign and_1_out = A & B;  // AND_Gate and_1, 8 bits wide
  assign or_1_out = A | B;  // OR_Gate or_1, 8 bits wide
  Decoder #(.select(3), .disabled(0), .enable("false")) decoder_2 (
    .out2(decoder_2_out2), .out5(decoder_2_out5), .out7(decoder_2_out7), .sel({Cin, mode[1:0]}));  // open: out0, out1, out3, out4, out6
  Multiplexer #(.width(8), .enable("false")) multiplexer_1 (
    .in0({8{mode[1]}}), .in1(A), .out(multiplexer_1_out), .sel(\xor ));
  assign xor_1_out = multiplexer_1_out ^ B;  // XOR_Gate xor_1, 8 bits wide
  or or_2 (or_2_out, decoder_2_out2, decoder_2_out5, decoder_2_out7);
  assign out = Passthru ? B : 8'bz;  // Controlled_Buffer controlled_buffer_1
  assign out = \or  ? or_1_out : 8'bz;  // Controlled_Buffer controlled_buffer_2
  Adder adder_1 (.a(A), .b(xor_1_out), .out(adder_1_out), .cin(or_2_out), .cout(Cout));
  assign out = not_1_out ? adder_1_out : 8'bz;  // Controlled_Buffer controlled_buffer_3
  assign out = \xor  ? xor_1_out : 8'bz;  // Controlled_Buffer controlled_buffer_4
  assign out = \and  ? and_1_out : 8'bz;  // Controlled_Buffer controlled_buffer_5
  nor nor_1 (nor_1_out, out[0], out[1], out[2], out[3]);
  nor nor_2 (nor_2_out, out[4], out[5], out[6], out[7]);
  and and_2 (zero, nor_1_out, nor_2_out);

  // Other names for the same wires on the sheet: pass_b = Passthru

  // Notes on the sheet:
  //   Add
  //   Adc
  //   Sub
  //   Sbb
  //   And
  //   Xor
  //   Or
  //   passb
  //   Mode
  //   0 0 0
  //   0 0 0
  //   0 0 1
  //   0 1 0
  //   0 1 1
  //   1 0 0
  //   1 0 1
  //   1 1 0
  //   1 1 1
endmodule

module graphics (
);

  wire and_1_out, nand_1_out, nor_1_out, or_1_out, undriven, undriven_2, undriven_3, undriven_4, undriven_5,
       undriven_6, undriven_7, undriven_8, undriven_9, undriven_10, undriven_11, undriven_12, xnor_1_out,
       xor_1_out;

  and and_1 (and_1_out, undriven, undriven_2);
  nand nand_1 (nand_1_out, undriven_3, undriven_4);
  // NOT_Gate not_1 is placed but not wired
  Adder adder_1 ();  // open: a, b, out, cin, cout
  or or_1 (or_1_out, undriven_5, undriven_6);
  nor nor_1 (nor_1_out, undriven_7, undriven_8);
  Decoder #(.select(2), .disabled(0)) decoder_1 ();  // open: out0, out1, out2, out3, sel, en
  Controlled_Buffer #(.width(8)) controlled_buffer_1 ();  // open: in, out, en
  xor xor_1 (xor_1_out, undriven_9, undriven_10);
  xnor xnor_1 (xnor_1_out, undriven_11, undriven_12);
  Multiplexer #(.select(2), .disabled(0), .enable("false")) multiplexer_1 ();  // open: in0, in1, in2, in3, out, sel

  // Notes on the sheet:
  //   AND
  //   NAND
  //   inverter
  //   adder
  //   OR
  //   NOR
  //   decoder
  //   switched buffer
  //   XOR
  //   XNOR
  //   multiplexer
endmodule

module test (
  input  nup_down,
  input  [15:0] in_2,
  input  nload_count,
  input  clock,
  input  nup_down_2,
  input  [7:0] B_BUS,
  input  wr_spl,
  input  wr_sph,
  input  clock_2,
  input  rd_spl,
  input  rd_sph,
  output [15:0] out_12,
  output [15:0] out_13,
  output [7:0] A_BUS
);

  wire [7:0] multiplexer_1_out, multiplexer_2_out;
  wire [15:0] adder_1_out, adder_2_out, multiplexer_3_out;

  Multiplexer #(.width(8), .disabled(0), .enable("false")) multiplexer_1 (
    .in0(adder_2_out[7:0]), .in1(B_BUS), .out(multiplexer_1_out), .sel(wr_spl));
  Multiplexer #(.width(8), .disabled(0), .enable("false")) multiplexer_2 (
    .in0(adder_2_out[15:8]), .in1(B_BUS), .out(multiplexer_2_out), .sel(wr_sph));
  Multiplexer #(.width(16), .disabled(0), .enable("false")) multiplexer_3 (
    .in0(in_2), .in1(adder_1_out), .out(multiplexer_3_out), .sel(nload_count));
  Register #(.width(16)) register_1 (.D(multiplexer_3_out), .Q(out_12), .clk(clock));  // open: en, clr
  Register register_2 (.D(multiplexer_1_out), .Q(out_13[7:0]), .clk(clock_2));  // open: en, clr
  Register register_3 (.D(multiplexer_2_out), .Q(out_13[15:8]), .clk(clock_2));  // open: en, clr
  Adder #(.width(16)) adder_1 (.a({{15{nup_down}}, 1'b1}), .b(out_12), .out(adder_1_out));  // open: cin, cout
  assign A_BUS = rd_spl ? out_13[7:0] : 8'bz;  // Controlled_Buffer controlled_buffer_1
  Adder #(.width(16)) adder_2 (.a({{15{nup_down_2}}, 1'b1}), .b(out_13), .out(adder_2_out));  // open: cin, cout
  assign A_BUS = rd_sph ? out_13[15:8] : 8'bz;  // Controlled_Buffer controlled_buffer_2
endmodule
