// Logisim project proc.circ as structural Verilog: 9 circuits, main circuit main
module main (
  input  c_in,
  input  carry,
  input  zero,
  input  nreset,
  input  carry_2,
  input  zero_2,
  input  in_7,
  input  in_8,
  input  in_9,
  input  in_10,
  input  in_11,
  input  in_12
);

  wire adrrl_tc, alu, and_1_out, Clock, decoder_1_out0, decoder_1_out1, decoder_1_out2, decoder_1_out3,
       decoder_1_out4, decoder_1_out5, decoder_1_out6, decoder_2_out0, decoder_2_out1, decoder_2_out2,
       decoder_2_out3, decoder_2_out4, decoder_2_out5, decoder_2_out6, incaddr, inst, link, not_1_out,
       not_2_out, or_1_out, or_2_out, reada, readmem, regdest, regsrc, sequencer_1_alu, sequencer_1_incaddr,
       sequencer_1_inst, sequencer_1_link, sequencer_1_reada, sequencer_1_readmem, sequencer_1_regdest,
       sequencer_1_regsrc, sequencer_1_rwitea, sequencer_1_swapdest, sequencer_1_temp, sequencer_1_writemem,
       swapdest, temp, undriven, writea, writemem;
  wire [2:0] dest, hc163_1_q0, multiplexer_1_out;
  wire [3:0] sequencer_1_count;
  wire [7:0] A_q, addrh_q, adrrl_q, B_q, C_q, controlled_buffer_1_out, controlled_buffer_2_out,
       controlled_buffer_15_out, D_q, E_q, H_q, L_q, marh_q, marl_q, n8_bit_alu_1_out, sph_q, spl_q, Temp_q;
  wire [7:3] instruction;
  wire [15:0] multiplexer_2_out;
  wire [15:11] rom_1_data;

  // Probe on sequencer_1_count
  Sequencer sequencer_1 (
    .nreset(nreset), .clk(Clock), .instruction({instruction, dest}), .carry(carry), .zero(zero),
    .count(sequencer_1_count), .alu(sequencer_1_alu), .regsrc(sequencer_1_regsrc),
    .regdest(sequencer_1_regdest), .writemem(sequencer_1_writemem), .readmem(sequencer_1_readmem),
    .inst(sequencer_1_inst), .temp(sequencer_1_temp), .link(sequencer_1_link), .incaddr(sequencer_1_incaddr),
    .reada(sequencer_1_reada), .rwitea(sequencer_1_rwitea), .swapdest(sequencer_1_swapdest));
  and and_1 (and_1_out, nreset, not_1_out);
  not not_1 (not_1_out, rom_1_data[11]);
  not not_2 (not_2_out, Clock);
  hc163 hc163_1 (
    .CET(1'b1), .CEP(1'b1), .PE(1'b1), .nMR(and_1_out), .Clock(not_2_out), .Q0(hc163_1_q0[0]),
    .Q1(hc163_1_q0[1]), .Q2(hc163_1_q0[2]));  // open: D0, D1, D2, D3, Q3, TC
  Clock clock_1 (.out(Clock));
  Register instruction_reg (.D(controlled_buffer_2_out), .Q({instruction, dest}), .clk(inst));  // open: en, clr
  ROM #(.addrWidth(14), .dataWidth(16)) rom_1 (
    .addr({zero_2, carry_2, instruction, dest, hc163_1_q0, Clock}),
    .data({rom_1_data[15:13], swapdest, rom_1_data[11], reada, writea, incaddr, link, temp, inst, readmem, writemem, regdest, regsrc, alu}));  // open: sel
  Multiplexer #(.width(3), .enable("false")) multiplexer_1 (
    .in0(dest), .in1(instruction[5:3]), .out(multiplexer_1_out), .sel(swapdest));
  Register u_Temp (.D(controlled_buffer_2_out), .Q(Temp_q), .clk(temp));  // open: en, clr
  // Probe on controlled_buffer_1_out
  Decoder #(.select(3), .disabled(0)) decoder_1 (
    .out0(decoder_1_out0), .out1(decoder_1_out1), .out2(decoder_1_out2), .out3(decoder_1_out3),
    .out4(decoder_1_out4), .out5(decoder_1_out5), .out6(decoder_1_out6), .sel(multiplexer_1_out), .en(regdest));  // open: out7
  Decoder #(.select(3), .disabled(0)) decoder_2 (
    .out0(decoder_2_out0), .out1(decoder_2_out1), .out2(decoder_2_out2), .out3(decoder_2_out3),
    .out4(decoder_2_out4), .out5(decoder_2_out5), .out6(decoder_2_out6), .sel(instruction[5:3]), .en(regsrc));  // open: out7
  // Probe on controlled_buffer_2_out
  // Probe on Temp_q
  _8_bit_ALU u_8_bit_alu_1 (
    .mode(dest), .Cin(c_in), .A(controlled_buffer_2_out), .B(Temp_q), .out(n8_bit_alu_1_out));  // open: Cout, zero
  assign controlled_buffer_1_out = alu ? n8_bit_alu_1_out : 8'bz;  // Controlled_Buffer controlled_buffer_1
  assign controlled_buffer_2_out = or_1_out ? A_q : 8'bz;  // Controlled_Buffer controlled_buffer_2
  Register A (.D(controlled_buffer_1_out), .Q(A_q), .clk(or_2_out));  // open: en, clr
  or or_1 (or_1_out, reada, decoder_2_out0);
  or or_2 (or_2_out, writea, decoder_1_out0);
  assign controlled_buffer_2_out = decoder_2_out1 ? B_q : 8'bz;  // Controlled_Buffer controlled_buffer_3
  Register B (.D(controlled_buffer_1_out), .Q(B_q), .clk(decoder_1_out1));  // open: en, clr
  assign controlled_buffer_2_out = decoder_2_out2 ? C_q : 8'bz;  // Controlled_Buffer controlled_buffer_4
  Register C (.D(controlled_buffer_1_out), .Q(C_q), .clk(decoder_1_out2));  // open: en, clr
  assign controlled_buffer_2_out = decoder_2_out3 ? D_q : 8'bz;  // Controlled_Buffer controlled_buffer_5
  Register D (.D(controlled_buffer_1_out), .Q(D_q), .clk(decoder_1_out3));  // open: en, clr
  assign controlled_buffer_2_out = decoder_2_out4 ? E_q : 8'bz;  // Controlled_Buffer controlled_buffer_6
  Register E (.D(controlled_buffer_1_out), .Q(E_q), .clk(decoder_1_out4));  // open: en, clr
  assign controlled_buffer_2_out = decoder_2_out5 ? H_q : 8'bz;  // Controlled_Buffer controlled_buffer_7
  Register H (.D(controlled_buffer_1_out), .Q(H_q), .clk(decoder_1_out5));  // open: en, clr
  assign controlled_buffer_2_out = decoder_2_out6 ? L_q : 8'bz;  // Controlled_Buffer controlled_buffer_8
  Register L (.D(controlled_buffer_1_out), .Q(L_q), .clk(decoder_1_out6));  // open: en, clr
  assign controlled_buffer_2_out = in_7 ? marh_q : 8'bz;  // Controlled_Buffer controlled_buffer_9
  Register marh (.D(controlled_buffer_1_out), .Q(marh_q), .clk(undriven), .clr(undriven));  // open: en
  assign controlled_buffer_2_out = in_8 ? marl_q : 8'bz;  // Controlled_Buffer controlled_buffer_10
  Register marl (.D(controlled_buffer_1_out), .Q(marl_q));  // open: en, clk, clr
  assign controlled_buffer_2_out = in_9 ? sph_q : 8'bz;  // Controlled_Buffer controlled_buffer_11
  Register sph (.D(controlled_buffer_1_out), .Q(sph_q));  // open: en, clk, clr
  assign controlled_buffer_2_out = in_10 ? spl_q : 8'bz;  // Controlled_Buffer controlled_buffer_12
  Register spl (.D(controlled_buffer_1_out), .Q(spl_q));  // open: en, clk, clr
  _8_bit_up_count_pre adrrl (
    .CEP_T(incaddr), .nPE(1'b1), .nMR(nreset), .CP(Clock), .Q(adrrl_q), .TC(adrrl_tc));  // open: D
  _8_bit_up_count_pre addrh (.CEP_T(adrrl_tc), .nPE(1'b1), .nMR(nreset), .CP(Clock), .Q(addrh_q));  // open: D, TC
  assign controlled_buffer_1_out = link ? controlled_buffer_2_out : 8'bz;  // Controlled_Buffer controlled_buffer_13
  Multiplexer #(.select(2), .width(16), .enable("false")) multiplexer_2 (
    .in0({addrh_q, adrrl_q}), .in1({H_q, L_q}), .in2({marh_q, marl_q}), .in3({sph_q, spl_q}),
    .out(multiplexer_2_out), .sel({in_12, in_11}));
  // Probe on {in_12, in_11}
  // Probe on {addrh_q, adrrl_q}
  assign controlled_buffer_2_out = readmem ? controlled_buffer_15_out : 8'bz;  // Controlled_Buffer controlled_buffer_14
  assign controlled_buffer_15_out = writemem ? controlled_buffer_1_out : 8'bz;  // Controlled_Buffer controlled_buffer_15
  // Probe on multiplexer_2_out
  RAM #(.addrWidth(16), .bus("asynch")) ram_1 (
    .addr(multiplexer_2_out), .data(controlled_buffer_15_out));  // open: sel, ld, clr

  // Other names for the same wires on the sheet: instruction[2:0] = dest; source[2:0] = instruction[5:3];
  //   seladdra = in_11; seladdrb = in_12; reset = nreset; selmarh = in_7; selmarl = in_8; selsph = in_9;
  //   selspl = in_10

  // Notes on the sheet:
  //   contents of rom_1 (hex, n*v repeats v):
  //   110 130 882 886 110 130 882 886 110 130 882 886 110 130 882 886 110 130 882 886 110 130 882 886 110
  //   130 882 886 4*0 110 130 882 886 110 130 882 886 110 130 882 886 110 130 882 886 110 130 882 886 110
  //   130 882 886 110 130 882 886 4*0 110 130 882 886 110 130 882 886 110 130 882 886 110 130 882 886 110
  //   130 882 886 110 130 882 886 110 130 882 886 4*0 110 130 882 886 110 130 882 886 110 130 882 886 110
  //   130 882 886 110 130 882 886 110 130 882 886 110 130 882 886 4*0 110 130 882 886 110 130 882 886 110
  //   130 882 886 110 130 882 886 110 130 882 886 110 130 882 886 110 130 882 886 4*0 110 130 882 886 110
  //   130 882 886 110 130 882 886 110 130 882 886 110 130 882 886 110 130 882 886 110 130 882 886 4*0 110
  //   130 882 886 110 130 882 886 110 130 882 886 110 130 882 886 110 130 882 886 110 130 882 886 110 130
  //   882 886
endmodule

module HC574 (
  input  [7:0] D,
  input  CLK,
  input  OE,
  output [7:0] mon,
  output [7:0] Q
);

  assign Q = OE ? mon : 8'bz;  // Controlled_Buffer controlled_buffer_1
  Register register_1 (.D(D), .Q(mon), .clk(CLK));  // open: en, clr
endmodule

// Bidirect
module hc245 (
  input  [7:0] A0,
  input  [7:0] B1,
  input  T_nR,
  input  nEN,
  output [7:0] B0,
  output [7:0] A1
);

  wire and_1_out, and_2_out, not_1_out, not_2_out, not_3_out;

  not not_1 (not_1_out, nEN);
  and and_1 (and_1_out, not_1_out, not_2_out);
  not not_2 (not_2_out, T_nR);
  and and_2 (and_2_out, T_nR, not_3_out);
  not not_3 (not_3_out, nEN);
  assign B0 = and_2_out ? A0 : 8'bz;  // Controlled_Buffer controlled_buffer_1
  assign A1 = and_1_out ? B1 : 8'bz;  // Controlled_Buffer controlled_buffer_2
endmodule

module hc191_up_down_preset (
  input  D0,
  input  D1,
  input  D2,
  input  D3,
  input  nPL,
  input  nU_D,
  input  nCE,
  input  CLK,
  output Q0,
  output Q1,
  output Q2,
  output Q3,
  output TC,
  output nRC
);

  wire and_1_out, and_2_out, and_3_out, and_4_out, and_5_out, and_6_out, and_7_out, and_8_out, and_9_out,
       and_10_out, and_11_out, and_12_out, and_13_out, and_14_out, j_k_ff_1_qn, j_k_ff_2_qn, j_k_ff_3_qn,
       j_k_ff_4_qn, nand_2_out, nand_3_out, nand_4_out, nand_5_out, not_1_out, not_2_out, not_3_out,
       not_4_out, not_5_out, not_6_out, not_7_out, not_8_out, or_2_out, or_3_out, or_4_out;

  not not_1 (not_1_out, nPL);
  not not_2 (not_2_out, nU_D);
  not not_3 (not_3_out, nCE);
  not not_4 (not_4_out, CLK);
  and and_1 (and_1_out, not_2_out, not_3_out);
  and and_2 (and_2_out, not_3_out, nU_D);
  and and_3 (and_3_out, not_2_out, Q1, Q0, Q2, Q3);
  nand nand_1 (nRC, not_4_out, not_3_out, TC);
  and and_4 (and_4_out, nU_D, j_k_ff_1_qn, j_k_ff_2_qn, j_k_ff_3_qn, j_k_ff_4_qn);
  or or_1 (TC, and_3_out, and_4_out);
  nand nand_2 (nand_2_out, D0, not_1_out);
  not not_5 (not_5_out, nand_2_out);
  J_K_Flip_Flop j_k_ff_1 (
    .J(not_3_out), .clk(not_4_out), .K(not_3_out), .Q(Q0), .Qn(j_k_ff_1_qn), .preset(not_5_out),
    .reset(and_5_out));  // open: en
  nand nand_3 (nand_3_out, D1, not_1_out);
  and and_5 (and_5_out, nand_2_out, not_1_out);
  and and_6 (and_6_out, and_2_out, j_k_ff_1_qn);
  or or_2 (or_2_out, and_6_out, and_7_out);
  not not_6 (not_6_out, nand_3_out);
  and and_7 (and_7_out, Q0, and_1_out);
  and and_8 (and_8_out, nand_3_out, not_1_out);
  J_K_Flip_Flop j_k_ff_2 (
    .J(or_2_out), .clk(not_4_out), .K(or_2_out), .Q(Q1), .Qn(j_k_ff_2_qn), .preset(not_6_out),
    .reset(and_8_out));  // open: en
  and and_9 (and_9_out, and_2_out, j_k_ff_1_qn, j_k_ff_2_qn);
  nand nand_4 (nand_4_out, D2, not_1_out);
  not not_7 (not_7_out, nand_4_out);
  and and_10 (and_10_out, Q0, Q1, and_1_out);
  or or_3 (or_3_out, and_9_out, and_10_out);
  and and_11 (and_11_out, nand_4_out, not_1_out);
  J_K_Flip_Flop j_k_ff_3 (
    .J(or_3_out), .clk(not_4_out), .K(or_3_out), .Q(Q2), .Qn(j_k_ff_3_qn), .preset(not_7_out),
    .reset(and_11_out));  // open: en
  nand nand_5 (nand_5_out, D3, not_1_out);
  and and_12 (and_12_out, and_2_out, j_k_ff_1_qn, j_k_ff_2_qn, j_k_ff_3_qn);
  and and_13 (and_13_out, Q0, Q1, Q2, and_1_out);
  or or_4 (or_4_out, and_12_out, and_13_out);
  J_K_Flip_Flop j_k_ff_4 (
    .J(or_4_out), .clk(not_4_out), .K(or_4_out), .Q(Q3), .Qn(j_k_ff_4_qn), .preset(not_8_out),
    .reset(and_14_out));  // open: en
  not not_8 (not_8_out, nand_5_out);
  and and_14 (and_14_out, nand_5_out, not_1_out);
endmodule

module hc163 (
  input  D0,
  input  D1,
  input  D2,
  input  D3,
  input  CET,
  input  CEP,
  input  PE,
  input  nMR,
  input  Clock,
  output Q0,
  output Q1,
  output Q2,
  output Q3,
  output TC
);

  wire and_1_out, and_2_out, and_3_out, and_4_out, and_5_out, and_6_out, and_7_out, and_8_out, and_9_out,
       d_ff_1_q, d_ff_1_qn, d_ff_2_q, d_ff_2_qn, d_ff_3_q, d_ff_3_qn, d_ff_4_q, d_ff_4_qn, nand_1_out,
       nand_2_out, nor_1_out, nor_2_out, nor_3_out, nor_4_out, nor_5_out, nor_6_out, not_1_out, not_2_out,
       or_1_out, or_2_out, or_3_out, or_4_out, or_5_out, xnor_1_out, xnor_2_out, xnor_3_out;

  nand nand_1 (nand_1_out, CET, CEP);
  nor nor_1 (nor_1_out, PE, not_1_out);
  not not_1 (not_1_out, nMR);
  nor nor_2 (nor_2_out, nor_1_out, not_1_out);
  not not_2 (not_2_out, nand_1_out);
  xnor xnor_1 (xnor_1_out, not_2_out, d_ff_1_qn);
  and and_1 (and_1_out, D0, nor_1_out);
  or or_1 (or_1_out, and_1_out, and_2_out);
  and and_2 (and_2_out, xnor_1_out, nor_2_out);
  D_Flip_Flop d_ff_1 (.clk(Clock), .D(or_1_out), .Q(d_ff_1_q), .Qn(d_ff_1_qn));  // open: preset, en, reset
  not not_3 (Q0, d_ff_1_qn);
  nor nor_3 (nor_3_out, nand_1_out, d_ff_1_qn);
  and and_3 (and_3_out, D1, nor_1_out);
  or or_2 (or_2_out, and_3_out, and_4_out);
  xnor xnor_2 (xnor_2_out, nor_3_out, d_ff_2_qn);
  and and_4 (and_4_out, xnor_2_out, nor_2_out);
  D_Flip_Flop d_ff_2 (.clk(Clock), .D(or_2_out), .Q(d_ff_2_q), .Qn(d_ff_2_qn));  // open: preset, en, reset
  not not_4 (Q1, d_ff_2_qn);
  nor nor_4 (nor_4_out, nand_1_out, d_ff_1_qn, d_ff_2_qn);
  xnor xnor_3 (xnor_3_out, nor_4_out, d_ff_3_qn);
  and and_5 (and_5_out, D2, nor_1_out);
  or or_3 (or_3_out, and_5_out, and_6_out);
  and and_6 (and_6_out, xnor_3_out, nor_2_out);
  D_Flip_Flop d_ff_3 (.clk(Clock), .D(or_3_out), .Q(d_ff_3_q), .Qn(d_ff_3_qn));  // open: preset, en, reset
  not not_5 (Q2, d_ff_3_qn);
  nor nor_5 (nor_5_out, nand_1_out, d_ff_1_qn, d_ff_2_qn, d_ff_3_qn);
  and and_7 (and_7_out, D3, nor_1_out);
  or or_4 (or_4_out, and_7_out, and_9_out);
  and and_8 (and_8_out, nor_5_out, d_ff_4_qn);
  nor nor_6 (nor_6_out, nor_5_out, d_ff_4_qn);
  or or_5 (or_5_out, and_8_out, nor_6_out);
  and and_9 (and_9_out, nor_2_out, or_5_out);
  D_Flip_Flop d_ff_4 (.clk(Clock), .D(or_4_out), .Q(d_ff_4_q), .Qn(d_ff_4_qn));  // open: preset, en, reset
  not not_6 (Q3, d_ff_4_qn);
  nand nand_2 (nand_2_out, d_ff_4_q, d_ff_3_q, d_ff_2_q, d_ff_1_q, CET);
  not not_7 (TC, nand_2_out);
endmodule

module _8_bit_up_count_pre (
  input  [7:0] D,
  input  CEP_T,
  input  nPE,
  input  nMR,
  input  CP,
  output [7:0] Q,
  output TC
);

  wire hc163_1_tc;

  hc163 hc163_1 (
    .D0(D[0]), .D1(D[1]), .D2(D[2]), .D3(D[3]), .CET(CEP_T), .CEP(CEP_T), .PE(nPE), .nMR(nMR), .Clock(CP),
    .Q0(Q[0]), .Q1(Q[1]), .Q2(Q[2]), .Q3(Q[3]), .TC(hc163_1_tc));
  hc163 hc163_2 (
    .D0(D[4]), .D1(D[5]), .D2(D[6]), .D3(D[7]), .CET(hc163_1_tc), .CEP(hc163_1_tc), .PE(nPE), .nMR(nMR),
    .Clock(CP), .Q0(Q[4]), .Q1(Q[5]), .Q2(Q[6]), .Q3(Q[7]), .TC(TC));
endmodule

module hc161 (
  input  D0,
  input  D1,
  input  D2,
  input  D3,
  input  CET,
  input  CEP,
  input  PE,
  input  nMR,
  input  Clock,
  output Q0,
  output Q1,
  output Q2,
  output Q3,
  output TC
);

  wire and_1_out, and_2_out, and_3_out, and_4_out, and_5_out, and_6_out, and_7_out, and_8_out, and_9_out,
       d_ff_1_q, d_ff_1_qn, d_ff_2_q, d_ff_2_qn, d_ff_3_q, d_ff_3_qn, d_ff_4_q, d_ff_4_qn, nand_1_out,
       nand_2_out, nor_1_out, nor_2_out, nor_3_out, nor_4_out, not_1_out, not_2_out, not_3_out, not_4_out,
       or_1_out, or_2_out, or_3_out, or_4_out, or_5_out, xnor_1_out, xnor_2_out, xnor_3_out;

  nand nand_1 (nand_1_out, CET, CEP);
  not not_1 (not_1_out, PE);
  not not_2 (not_2_out, nMR);
  not not_3 (not_3_out, not_1_out);
  not not_4 (not_4_out, nand_1_out);
  xnor xnor_1 (xnor_1_out, not_4_out, d_ff_1_qn);
  and and_1 (and_1_out, D0, not_1_out);
  and and_2 (and_2_out, xnor_1_out, not_3_out);
  or or_1 (or_1_out, and_1_out, and_2_out);
  D_Flip_Flop d_ff_1 (.clk(Clock), .D(or_1_out), .Q(d_ff_1_q), .Qn(d_ff_1_qn), .reset(not_2_out));  // open: preset, en
  not not_5 (Q0, d_ff_1_qn);
  nor nor_1 (nor_1_out, nand_1_out, d_ff_1_qn);
  xnor xnor_2 (xnor_2_out, nor_1_out, d_ff_2_qn);
  and and_3 (and_3_out, D1, not_1_out);
  and and_4 (and_4_out, xnor_2_out, not_3_out);
  or or_2 (or_2_out, and_3_out, and_4_out);
  D_Flip_Flop d_ff_2 (.clk(Clock), .D(or_2_out), .Q(d_ff_2_q), .Qn(d_ff_2_qn), .reset(not_2_out));  // open: preset, en
  not not_6 (Q1, d_ff_2_qn);
  nor nor_2 (nor_2_out, nand_1_out, d_ff_1_qn, d_ff_2_qn);
  xnor xnor_3 (xnor_3_out, nor_2_out, d_ff_3_qn);
  and and_5 (and_5_out, D2, not_1_out);
  and and_6 (and_6_out, xnor_3_out, not_3_out);
  or or_3 (or_3_out, and_5_out, and_6_out);
  D_Flip_Flop d_ff_3 (.clk(Clock), .D(or_3_out), .Q(d_ff_3_q), .Qn(d_ff_3_qn), .reset(not_2_out));  // open: preset, en
  not not_7 (Q2, d_ff_3_qn);
  nor nor_3 (nor_3_out, nand_1_out, d_ff_1_qn, d_ff_2_qn, d_ff_3_qn);
  and and_7 (and_7_out, nor_3_out, d_ff_4_qn);
  or or_4 (or_4_out, and_7_out, nor_4_out);
  and and_8 (and_8_out, not_3_out, or_4_out);
  and and_9 (and_9_out, D3, not_1_out);
  or or_5 (or_5_out, and_9_out, and_8_out);
  nor nor_4 (nor_4_out, nor_3_out, d_ff_4_qn);
  D_Flip_Flop d_ff_4 (.clk(Clock), .D(or_5_out), .Q(d_ff_4_q), .Qn(d_ff_4_qn), .reset(not_2_out));  // open: preset, en
  not not_8 (Q3, d_ff_4_qn);
  nand nand_2 (nand_2_out, d_ff_4_q, d_ff_3_q, d_ff_2_q, d_ff_1_q, CET);
  not not_9 (TC, nand_2_out);
endmodule

module register_block (
  input  [7:0] D_in,
  input  write,
  input  [2:0] destination,
  input  oe,
  input  [2:0] source,
  output [7:0] q_out,
  output [7:0] mon_a,
  output [7:0] mon_b,
  output [7:0] mon_c,
  output [7:0] mon_d,
  output [7:0] mon_e,
  output [7:0] mon_h,
  output [7:0] mon_h_2
);

  wire decoder_1_out0, decoder_1_out1, decoder_1_out2, decoder_1_out3, decoder_1_out4, decoder_1_out5,
       decoder_1_out6, decoder_2_out0, decoder_2_out1, decoder_2_out2, decoder_2_out3, decoder_2_out4,
       decoder_2_out5, decoder_2_out6, not_1_out, not_2_out;

  not not_1 (not_1_out, write);
  Decoder #(.select(3), .disabled(0)) decoder_1 (
    .out0(decoder_1_out0), .out1(decoder_1_out1), .out2(decoder_1_out2), .out3(decoder_1_out3),
    .out4(decoder_1_out4), .out5(decoder_1_out5), .out6(decoder_1_out6), .sel(destination), .en(not_1_out));  // open: out7
  Decoder #(.select(3), .disabled(0)) decoder_2 (
    .out0(decoder_2_out0), .out1(decoder_2_out1), .out2(decoder_2_out2), .out3(decoder_2_out3),
    .out4(decoder_2_out4), .out5(decoder_2_out5), .out6(decoder_2_out6), .sel(source), .en(not_2_out));  // open: out7
  not not_2 (not_2_out, oe);
  HC574 a (.D(D_in), .CLK(decoder_1_out0), .OE(decoder_2_out0), .mon(mon_a), .Q(q_out));
  HC574 b (.D(D_in), .CLK(decoder_1_out1), .OE(decoder_2_out1), .mon(mon_b), .Q(q_out));
  HC574 c (.D(D_in), .CLK(decoder_1_out2), .OE(decoder_2_out2), .mon(mon_c), .Q(q_out));
  HC574 d (.D(D_in), .CLK(decoder_1_out3), .OE(decoder_2_out3), .mon(mon_d), .Q(q_out));
  HC574 e (.D(D_in), .CLK(decoder_1_out4), .OE(decoder_2_out4), .mon(mon_e), .Q(q_out));
  HC574 h (.D(D_in), .CLK(decoder_1_out5), .OE(decoder_2_out5), .mon(mon_h), .Q(q_out));
  HC574 l (.D(D_in), .CLK(decoder_1_out6), .OE(decoder_2_out6), .mon(mon_h_2), .Q(q_out));
endmodule

module Sequencer (
  input  nreset,
  input  clk,
  input  [7:0] instruction,
  input  carry,
  input  zero,
  output alu,
  output regsrc,
  output regdest,
  output writemem,
  output readmem,
  output [3:0] count,
  output inst,
  output temp,
  output link,
  output incaddr,
  output reada,
  output rwitea,
  output swapdest
);

  wire and_1_out, and_2_out, and_3_out, and_4_out, and_5_out, and_6_out, and_7_out, decoder_1_out0,
       decoder_1_out1, decoder_2_out2, decoder_2_out3, decoder_2_out7, decoder_3_out0, decoder_3_out1,
       decoder_3_out2, nor_1_out, nor_2_out, not_1_out, not_2_out, or_1_out;

  and and_1 (and_1_out, nreset, nor_1_out);
  not not_1 (not_1_out, clk);
  nor nor_1 (nor_1_out, and_2_out, and_3_out, alu);
  Decoder #(.select(2), .disabled(0), .enable("false")) decoder_1 (
    .out0(decoder_1_out0), .out1(decoder_1_out1), .sel(instruction[7:6]));  // open: out2, out3
  Decoder #(.select(3), .disabled(0), .enable("false")) decoder_2 (
    .out2(decoder_2_out2), .out3(decoder_2_out3), .out7(decoder_2_out7), .sel(instruction[2:0]));  // open: out0, out1, out4, out5, out6
  hc163 hc163_1 (
    .CET(1'b1), .CEP(1'b1), .PE(1'b1), .nMR(and_1_out), .Clock(not_1_out), .Q0(count[0]), .Q1(count[1]),
    .Q2(count[2]), .Q3(count[3]));  // open: D0, D1, D2, D3, TC
  // Probe on count
  Decoder #(.select(4), .disabled(0), .enable("false")) decoder_3 (
    .out0(decoder_3_out0), .out1(decoder_3_out1), .out2(decoder_3_out2), .sel(count));  // open: out3, out4, out5, out6, out7, out8, out9, out10, out11, out12, out13, out14, out15
  nor nor_2 (nor_2_out, decoder_2_out2, decoder_2_out3, decoder_2_out7);
  and and_2 (and_2_out, decoder_1_out0, decoder_3_out1);
  and and_3 (and_3_out, and_4_out, decoder_3_out2);
  and and_4 (and_4_out, decoder_1_out1, nor_2_out);
  not not_2 (not_2_out, nor_2_out);
  and and_5 (and_5_out, decoder_1_out1, not_2_out);
  and and_6 (and_6_out, decoder_3_out1, decoder_1_out0);
  and and_7 (and_7_out, decoder_3_out1, and_4_out);
  or or_1 (or_1_out, and_6_out, and_5_out);
  // AND_Gate and_8 has open pins: in0=decoder_3_out0, in1=clk, out=open
  // AND_Gate and_9 has open pins: in0=and_7_out, in1=clk, out=open
  // AND_Gate and_10 has open pins: in0=clk, in1=and_3_out, out=open
  or or_2 (alu, and_5_out, and_3_out);
  or or_3 (regsrc, and_7_out, and_6_out);
  // AND_Gate and_11 has open pins: in0=or_1_out, in1=clk, out=open
endmodule
